// Logisim project wfy.circ as structural Verilog: 25 circuits, main circuit ◇单周期RISC-V
module \单周期RISC_V  (
  input  IR1,
  input  IR2,
  input  IR3,
  output RegWrite,
  output MemWrite,
  output [31:0] PC,
  output [31:0] IR,
  output [31:0] RDin,
  output [31:0] MDin,
  output [31:0] LedData
);

  wire ALU_Src, and_1_out, and_2_out, and_3_out, and_4_out, AUIPC, BEQ, BLTU, BNE, CLK, clock_1_out,
       comparator_1_eq, comparator_2_eq, comparator_2_lt, d_ff_2_q, ecall, Equal, Go, halt, IR1_t, IR2_t,
       IR3_t, IRA, IRB, IRC, JAL, JALR, LB, Less, MemToReg, nand_1_out, not_1_out, not_2_out, not_3_out,
       or_1_out, or_2_out, rst, S_type, SLTIU, URET, W1, W2, W3;
  wire [1:0] or_6_out, priority_encoder_1_out;
  wire [3:0] \单周期硬布线控制器_1_alu_op ;
  wire [4:0] multiplexer_2_out, multiplexer_3_out;
  wire [12:0] CNT_num;
  wire [15:0] multiplexer_6_out, \总周期数 ;
  wire [31:0] adder_2_out, adder_3_out, ALU_Result, AUIPC_Result, bit_extender_1_out, bit_extender_2_out,
       bit_extender_3_out, bit_extender_4_out, bit_extender_5_out, bit_extender_6_out, bit_extender_7_out,
       MemData, multiplexer_1_out, multiplexer_4_out, multiplexer_5_out, multiplexer_7_out,
       multiplexer_8_out, PC_4, regifile_1_r1, shifter_1_out, shifter_2_out, shifter_3_out;

  Button \u_继续运行  (.out(Go));
  Button _1 (.out(IRA));
  Button _2 (.out(IRB));
  Button _3 (.out(IRC));
  Button button_1 (.out(rst));
  LED #(.active("true")) led_1 (.in(W1));
  LED #(.active("true")) led_2 (.in(W2));
  LED #(.active("true")) led_3 (.in(W3));
  Hex_Digit_Display hex_digit_display_1 (.value(LedData[31:28]));  // open: dp
  Priority_Encoder #(.select(2), .disabled("Z")) priority_encoder_1 (
    .in0(1'b1), .in1(JALR), .in2(JAL), .in3(or_1_out), .out(priority_encoder_1_out));  // open: gs, en_out, en_in
  Multiplexer #(.select(2), .width(32), .disabled("Z"), .enable("false")) multiplexer_1 (
    .in0(PC_4), .in1(ALU_Result), .in2(adder_3_out), .in3(adder_2_out), .out(multiplexer_1_out),
    .sel(priority_encoder_1_out));
  Hex_Digit_Display hex_digit_display_2 (.value(LedData[27:24]));  // open: dp
  Hex_Digit_Display hex_digit_display_3 (.value(LedData[23:20]));  // open: dp
  or or_1 (or_1_out, and_1_out, and_2_out, and_3_out);
  Register #(.width(32), .trigger("rising"), .Select("low")) u_PC (
    .D(multiplexer_1_out), .en(or_2_out), .Q(PC), .clk(CLK), .clr(rst));
  or or_2 (or_2_out, ~halt, Go);  // OR_Gate
  Hex_Digit_Display hex_digit_display_4 (.value(LedData[19:16]));  // open: dp
  Hex_Digit_Display hex_digit_display_5 (.value(LedData[15:12]));  // open: dp
  and and_1 (and_1_out, BLTU, Less);
  and and_2 (and_2_out, BEQ, Equal);
  and and_3 (and_3_out, ~Equal, BNE);  // AND_Gate
  // RiscV_Probe riscv_probe_1: pin names not known; wires that end beside it: IR
  Adder #(.width(32)) adder_1 (.a(PC), .b(32'h4), .out(PC_4));  // open: cin, cout
  Hex_Digit_Display hex_digit_display_6 (.value(LedData[7:4]));  // open: dp
  Hex_Digit_Display hex_digit_display_7 (.value(LedData[11:8]));  // open: dp
  // Probe on \总周期数 
  ROM #(.addrWidth(10), .dataWidth(32), .Select("high")) rom_1 (.addr(PC[11:2]), .data(IR));
  not not_1 (not_1_out, halt);
  Counter #(.width(16), .max('hffff), .ongoal("wrap"), .trigger("rising"), .behavior("new")) counter_1 (
    .count(not_1_out), .Q(\总周期数 ), .clk(CLK));  // open: load, D, carry, clr, preset, down
  Hex_Digit_Display hex_digit_display_8 (.value(LedData[3:0]));  // open: dp
  \单周期硬布线控制器  \u_单周期硬布线控制器_1  (
    .Funct({IR[30], IR[25], IR[14:12]}), .OP(IR[6:2]), .ALU_OP(\单周期硬布线控制器_1_alu_op ), .MemToReg(MemToReg),
    .MemWrite(MemWrite), .ALU_SRC(ALU_Src), .RegWrite(RegWrite), .ecall(ecall), .S_type(S_type), .JALR(JALR),
    .BEQ(BEQ), .JAL(JAL), .BNE(BNE), .in_3(IR[21]), .uret(URET), .BLTU(BLTU), .LB(LB), .U_Type(AUIPC),
    .SLTIU(SLTIU));  // open: rs1_used, rs2_used, CSR
  Multiplexer #(.select(1), .width(5), .disabled("Z"), .enable("false")) multiplexer_2 (
    .in0(IR[19:15]), .in1(5'b10001), .out(multiplexer_2_out), .sel(ecall));
  Multiplexer #(.select(1), .width(5), .disabled("Z"), .enable("false")) multiplexer_3 (
    .in0(IR[24:20]), .in1(5'b01010), .out(multiplexer_3_out), .sel(ecall));
  or or_3 (IR1_t, IR1, IRA);
  assign bit_extender_1_out = {{20{IR[31]}}, IR[31:20]};  // Bit_Extender bit_extender_1
  Multiplexer #(.select(1), .width(32), .disabled("Z"), .enable("false")) multiplexer_4 (
    .in0(bit_extender_1_out), .in1(bit_extender_2_out), .out(multiplexer_4_out), .sel(S_type));
  assign bit_extender_2_out = {{20{IR[31]}}, {IR[31:25], IR[11:7]}};  // Bit_Extender bit_extender_2
  assign bit_extender_3_out = {{20{IR[31]}}, {IR[31], IR[7], IR[30:25], IR[11:8]}};  // Bit_Extender bit_extender_3
  assign bit_extender_4_out = {{12{IR[31]}}, {IR[31], IR[19:12], IR[20], IR[30:21]}};  // Bit_Extender bit_extender_4
  assign bit_extender_5_out = {{12{IR[31]}}, IR[31:12]};  // Bit_Extender bit_extender_5
  or or_4 (IR2_t, IR2, IRB);
  Regifile regifile_1 (
    .Din(RDin), .Clk(CLK), .R1(regifile_1_r1), .R2(MDin), .WE(RegWrite), .W_num(IR[11:7]),
    .R1_num(multiplexer_2_out), .R2_num(multiplexer_3_out));
  Shifter #(.width(32), .shift("ll")) shifter_1 (.in(bit_extender_3_out), .\dist (5'b00001), .out(shifter_1_out));
  Shifter #(.width(32), .shift("ll")) shifter_2 (.in(bit_extender_4_out), .\dist (5'b00001), .out(shifter_2_out));
  Shifter #(.width(32), .shift("ll")) shifter_3 (.in(bit_extender_5_out), .\dist (5'b01100), .out(shifter_3_out));
  Multiplexer #(.select(1), .width(32), .disabled("Z"), .enable("false")) multiplexer_5 (
    .in0(MDin), .in1(multiplexer_4_out), .out(multiplexer_5_out), .sel(ALU_Src));
  Adder #(.width(32)) adder_2 (.a(shifter_1_out), .b(PC), .out(adder_2_out));  // open: cin, cout
  Adder #(.width(32)) adder_3 (.a(PC), .b(shifter_2_out), .out(adder_3_out));  // open: cin, cout
  Adder #(.width(32)) adder_4 (.a(shifter_3_out), .b(PC), .out(AUIPC_Result));  // open: cin, cout
  or or_5 (IR3_t, IR3, IRC);
  ALU alu_1 (
    .X(regifile_1_r1), .Y(multiplexer_5_out), .AluOP(\单周期硬布线控制器_1_alu_op ), .Equal(Equal),
    .Result(ALU_Result), .out_6(Less));  // open: Result_2, out_4
  Comparator #(.width(32), .mode("twosComplement")) comparator_1 (
    .a(regifile_1_r1), .b(32'h22), .eq(comparator_1_eq));  // open: gt, lt
  and and_4 (and_4_out, comparator_1_eq, ecall);
  not not_2 (not_2_out, CLK);
  not not_3 (not_3_out, comparator_1_eq);
  Register #(.width(32), .trigger("rising"), .Select("low")) register_1 (
    .D(MDin), .en(and_4_out), .Q(LedData), .clk(CLK), .clr(rst));
  D_Flip_Flop #(.trigger("rising"), .Pre_Clr_Positions("ABOVE_BELOW"), .NegatePresetClear("false"), .enable("true"), .NewFFLayout("true")) d_ff_1 (
    .clk(not_2_out), .D(not_3_out), .Q(halt), .en(ecall), .reset(Go));  // open: Qn, preset
  RAM #(.addrWidth(10), .dataWidth(32), .bus("separate"), .Select("high")) ram_1 (
    .addr(ALU_Result[11:2]), .din(MDin), .data(MemData), .str(MemWrite), .sel(1'b1), .clk(CLK), .ld(1'b1),
    .clr(rst));
  Multiplexer #(.select(1), .width(16), .disabled("Z"), .enable("false")) multiplexer_6 (
    .in0(MemData[15:0]), .in1(MemData[31:16]), .out(multiplexer_6_out), .sel(ALU_Result[1]));
  assign bit_extender_6_out = {{16{multiplexer_6_out[15]}}, multiplexer_6_out};  // Bit_Extender bit_extender_6
  D_Flip_Flop #(.trigger("high"), .Pre_Clr_Positions("LEGACY"), .NegatePresetClear("false"), .enable("true"), .NewFFLayout("false")) d_ff_2 (.Q(d_ff_2_q));  // open: clk, D, Qn, preset, en, reset
  // Probe on 13'hc
  Multiplexer #(.select(1), .width(32), .disabled("Z"), .enable("false")) multiplexer_7 (
    .in0(MemData), .in1(bit_extender_6_out), .out(multiplexer_7_out), .sel(LB));
  Comparator #(.width(13), .mode("twosComplement")) comparator_2 (
    .a(CNT_num), .b(13'hc), .eq(comparator_2_eq), .lt(comparator_2_lt));  // open: gt
  Clock #(.highDuration(1), .lowDuration(1)) clock_1 (.out(clock_1_out));
  Multiplexer #(.select(2), .width(32), .disabled("Z"), .enable("false")) multiplexer_8 (
    .in0(ALU_Result), .in1(multiplexer_7_out), .in2(PC_4), .in3(AUIPC_Result), .out(multiplexer_8_out),
    .sel(or_6_out));
  or or_6 (or_6_out[0], MemToReg, AUIPC);
  Counter #(.width(13), .max('h1fff), .ongoal("stay"), .trigger("rising"), .behavior("old")) counter_2 (
    .count(comparator_2_lt), .Q(CNT_num), .clk(clock_1_out));  // open: load, D, carry, clr, preset
  assign bit_extender_7_out = {{31{1'b0}}, Less};  // Bit_Extender bit_extender_7
  or or_7 (or_6_out[1], AUIPC, JAL, JALR);
  nand nand_1 (nand_1_out, d_ff_2_q, comparator_2_eq);
  Multiplexer #(.select(1), .width(32), .disabled("Z"), .enable("false")) multiplexer_9 (
    .in0(multiplexer_8_out), .in1(bit_extender_7_out), .out(RDin), .sel(SLTIU));
  assign CLK = nand_1_out ? clock_1_out : 1'bz;  // Controlled_Buffer controlled_buffer_1
  Pull_Resistor #(.pull(1)) pull_resistor_1 (.node(CLK));

  // Notes on the sheet:
  //   中断源
  //   中断等待指示
  //   数码管输出应该用寄存器锁存，否则显示数据只能一闪而过
  //   数码管输出
  //   指令探针
  //   指令存储器
  //   contents of rom_1 (hex, n*v repeats v):
  //   100493 100006f 100493 200913 300993 100006f 100493 200913 300993 100006f 100493 200913 300993
  //   100006f 100493 200913 300993 408000ef 100413 100493 1f49493 900533 2200893 73 24d493 48463 fedff06f
  //   900533 2200893 73 100493 249493 900533 2200893 73 48463 fedff06f 100493 1f49493 900533 2200893 73
  //   4034d493 900533 2200893 73 4044d493 900533 2200893 73 4044d493 900533 2200893 73 4044d493 900533
  //   2200893 73 4044d493 900533 2200893 73 4044d493 900533 2200893 73 4044d493 900533 2200893 73 4044d493
  //   900533 2200893 73 100413 1f41993 41f9d993 433 c00913 300b13 140413 f47413 800293 100313 499993
  //   89e9b3 1300533 2200893 73 406282b3 fe0294e3 140413 f00f93 1f47433 1c41413 800293 100313 49d993
  //   89e9b3 1300533 2200893 73 406282b3 fe0294e3 1c45413 406b0b33 b0463 f95ff06f 2b3 fff2c293 829293
  //   ff2e293 500533 2200893 73 fff00413 493 84a023 140413 448493 84a023 140413 448493 84a023 140413
  //   448493 84a023 140413 448493 84a023 140413 448493 84a023 140413 448493 84a023 140413 448493 84a023
  //   140413 448493 84a023 140413 448493 84a023 140413 448493 84a023 140413 448493 84a023 140413 448493
  //   84a023 140413 448493 84a023 140413 448493 84a023 140413 448493 84a023 140413 448493 140413 433
  //   3c00493 42983 4aa03 149a2b3 28663 134a023 1442023 ffc48493 fe9412e3 800533 2200893 73 440413 3c00493
  //   fc9416e3 a00893 73 13 430497 900533 2200893 73 430497 900533 2200893 73 430497 900533 2200893 73
  //   430497 900533 2200893 73 430497 900533 2200893 73 430497 900533 2200893 73 430497 900533 2200893 73
  //   430497 900533 2200893 73 a00893 73 fff00293 313 1900413 841413 9700493 940533 2200893 73 5484b3
  //   494b313 fe0306e3 a00893 73 313 1000e13 8400493 849493 8348493 400913 891913 490913 849493 8248493
  //   849493 8148493 891913 490913 891913 490913 932023 12484b3 430313 fffe0e13 fe0e18e3 2000e13 313 31483
  //   900533 2200893 73 230313 fffe0e13 fe0e14e3 a00893 73 ff100493 900533 2200893 73 148493 fe9068e3
  //   900533 2200893 73 a00893 73 413 140413 800533 2200893 73 240413 800533 2200893 73 340413 800533
  //   2200893 73 440413 800533 2200893 73 540413 800533 2200893 73 640413 800533 2200893 73 740413 800533
  //   2200893 73 840413 800533 2200893 2200893 73 8067
  //   指令字
  //   I
  //   B
  //   J
  //   U_Type
  //   S
  //   为方便自动评测，需要输出PC，IR，寄存器堆写如数据RDin
  //   RAM写使能MemWrite、RAM写入数据MDin等信号
  //   数据存储器
  //   控制位
  //   暂停节拍，不能为0
  //   戳工具置1进入计数暂停模式，ctrl+k时钟自动运行到对应节拍暂停
  //   ctrl+k关闭时钟连续运行，将控制位置零，进入单步调试模式调试
  //   用这个时钟源需要去掉电路中的其他时钟源
  //   可计数暂停的时钟源
endmodule

// 单周期硬布线控制器
module \单周期硬布线控制器  (
  input  [4:0] OP,
  input  [4:0] Funct,
  input  in_3,
  output [3:0] ALU_OP,
  output uret,
  output MemToReg,
  output ecall,
  output MemWrite,
  output ALU_SRC,
  output RegWrite,
  output S_type,
  output BEQ,
  output BNE,
  output JALR,
  output JAL,
  output BLTU,
  output LB,
  output U_Type,
  output rs1_used,
  output rs2_used,
  output CSR,
  output SLTIU
);

  wire \控制信号自动生成_1_ecall ;

  \运算控制器自动生成  \u_运算控制器自动生成_1  (
    .OP2(OP[0]), .OP3(OP[1]), .OP4(OP[2]), .OP5(OP[3]), .OP6(OP[4]), .F12(Funct[0]), .F13(Funct[1]),
    .F14(Funct[2]), .F25(Funct[3]), .F30(Funct[4]), .S0(ALU_OP[0]), .S1(ALU_OP[1]), .S2(ALU_OP[2]),
    .S3(ALU_OP[3]));
  \控制信号自动生成  \u_控制信号自动生成_1  (
    .OP2(OP[0]), .OP3(OP[1]), .OP4(OP[2]), .OP5(OP[3]), .MemToReg(MemToReg), .OP6(OP[4]), .F12(Funct[0]),
    .F13(Funct[1]), .F14(Funct[2]), .F25(Funct[3]), .F30(Funct[4]), .MemWrite(MemWrite), .ALU_SRC(ALU_SRC),
    .RegWrite(RegWrite), .ecall(\控制信号自动生成_1_ecall ), .S_Type(S_type), .BEQ(BEQ), .BNE(BNE), .JALR(JALR),
    .JAL(JAL), .BLTU(BLTU), .LB(LB), .U_Type(U_Type), .rs1_used(rs1_used), .rs2_used(rs2_used), .CSR(CSR),
    .SLTIU(SLTIU));
  and and_1 (uret, in_3, \控制信号自动生成_1_ecall );
  and and_2 (ecall, ~in_3, \控制信号自动生成_1_ecall );  // AND_Gate

  // Other names for the same wires on the sheet: IR21 = in_3; OP_CODE[4:0] = OP

  // Notes on the sheet:
  //   运算器控制器，根据指令生成运算器功能选择信号
endmodule

// 控制信号生成
module \控制信号自动生成  (
  input  OP2,
  input  OP3,
  input  OP4,
  input  OP5,
  input  OP6,
  input  F12,
  input  F13,
  input  F14,
  input  F25,
  input  F30,
  output MemToReg,
  output MemWrite,
  output ALU_SRC,
  output RegWrite,
  output ecall,
  output S_Type,
  output BEQ,
  output BNE,
  output JALR,
  output JAL,
  output BLTU,
  output LB,
  output U_Type,
  output rs1_used,
  output rs2_used,
  output CSR,
  output SLTIU
);

  wire and_1_out, and_2_out, and_4_out, and_5_out, and_6_out, and_7_out, and_8_out, and_9_out, and_10_out,
       and_11_out, and_12_out, and_13_out, and_14_out, and_15_out, and_16_out, and_17_out, and_18_out,
       and_19_out, and_20_out, and_21_out, and_22_out, and_23_out, and_24_out, and_25_out, and_26_out,
       and_27_out, and_28_out, and_29_out, and_30_out, and_31_out, and_32_out, and_33_out, and_34_out,
       and_35_out, and_36_out, and_37_out, and_38_out, and_39_out, and_40_out, and_49_out, and_50_out,
       and_51_out, and_52_out, and_53_out, and_54_out, and_55_out, and_56_out, and_57_out, and_58_out,
       and_59_out, and_60_out, and_61_out, and_62_out, and_63_out, and_64_out, and_65_out, and_66_out,
       and_67_out, and_68_out, and_69_out, and_70_out, and_71_out, and_72_out, and_73_out, and_74_out,
       and_75_out, and_76_out, and_77_out, and_78_out, and_79_out, and_80_out, and_81_out, and_82_out,
       not_1_out, not_2_out, not_3_out, not_4_out, not_5_out, not_6_out, not_7_out, not_8_out, not_9_out,
       not_10_out, not_11_out, not_12_out, not_13_out, not_14_out, not_15_out, not_16_out, not_17_out,
       not_18_out, not_19_out, not_20_out, not_21_out, not_22_out, not_23_out, not_24_out, not_25_out,
       not_26_out, not_27_out, not_28_out, not_29_out, not_30_out, not_31_out, not_32_out, not_33_out,
       not_34_out, not_35_out, not_36_out, not_37_out, not_38_out, not_39_out, not_40_out, not_41_out,
       not_42_out, not_43_out, not_44_out, not_45_out, not_46_out, not_47_out, not_48_out, not_49_out,
       not_50_out, not_51_out, not_52_out, not_53_out, not_54_out, not_55_out, not_56_out, not_57_out,
       not_58_out, not_59_out, not_60_out, not_61_out, not_62_out, not_63_out, not_64_out, not_65_out,
       not_66_out, not_67_out, not_68_out, not_69_out, not_70_out, not_71_out, not_72_out, not_73_out,
       not_74_out, not_75_out, not_76_out, not_77_out, not_78_out, not_79_out, not_80_out, not_81_out,
       not_82_out, not_83_out, not_84_out, not_85_out, not_86_out, not_87_out, not_88_out, not_89_out,
       not_90_out, not_91_out, not_92_out, not_93_out, not_94_out, not_95_out, not_96_out, not_97_out,
       not_98_out, not_99_out, not_100_out, not_101_out, not_102_out, not_103_out, not_104_out, not_105_out,
       not_106_out, not_107_out, not_108_out, not_109_out, not_110_out, not_111_out, not_112_out,
       not_113_out, not_114_out, not_115_out, not_116_out, not_117_out, not_118_out, not_119_out,
       not_120_out, not_121_out, not_122_out, not_123_out, not_124_out, not_125_out, not_126_out,
       not_127_out, not_128_out, not_129_out, not_130_out, not_131_out, not_132_out, not_133_out,
       not_134_out, not_135_out, not_136_out, not_137_out, not_138_out, not_139_out, not_140_out,
       not_141_out, not_142_out, not_143_out, not_144_out, not_145_out, not_146_out, not_147_out,
       not_148_out, not_149_out, not_150_out, not_151_out, not_152_out, not_153_out, not_154_out,
       not_155_out, not_156_out, not_157_out, not_158_out, not_159_out, not_160_out, not_161_out,
       not_162_out, not_163_out, not_164_out, not_165_out, not_166_out, not_167_out, not_168_out,
       not_169_out, not_170_out, not_171_out, not_172_out, not_173_out, not_174_out, not_175_out,
       not_176_out, not_177_out, not_178_out, not_179_out, not_180_out, not_181_out, not_182_out,
       not_183_out, not_184_out, not_185_out, not_186_out, not_187_out, not_188_out, not_189_out,
       not_190_out, not_191_out, not_192_out, not_193_out, not_194_out, not_195_out, not_196_out,
       not_197_out, not_198_out, not_199_out, not_200_out, not_201_out, not_202_out, not_203_out,
       not_204_out, not_205_out, not_206_out, not_207_out, not_208_out, not_209_out, not_210_out,
       not_211_out, not_212_out, not_213_out, not_214_out, not_215_out, not_216_out, not_217_out,
       not_218_out, not_219_out, not_220_out, not_221_out, not_222_out, not_223_out, not_224_out,
       not_225_out, not_226_out, not_227_out, not_228_out, not_229_out, not_230_out, not_231_out,
       not_232_out, not_233_out, not_234_out, not_235_out, not_236_out, not_237_out, not_238_out,
       not_239_out, not_240_out, not_241_out, not_242_out, not_243_out, not_244_out, not_245_out,
       not_246_out, not_247_out, not_248_out, not_249_out, not_250_out, not_251_out, not_252_out,
       not_253_out, not_254_out, not_255_out, not_256_out, not_257_out, not_258_out, not_259_out,
       not_260_out, not_261_out, not_262_out, not_263_out, not_264_out, not_265_out, not_266_out,
       not_267_out, not_268_out, not_269_out, not_270_out, not_271_out, not_272_out, not_273_out,
       not_274_out, not_275_out, not_276_out, not_277_out, not_278_out, not_279_out, not_280_out,
       not_281_out, not_282_out, not_283_out, not_284_out, not_285_out, not_286_out, not_287_out,
       not_288_out, not_289_out, not_290_out, not_291_out, not_292_out, not_293_out, not_294_out,
       not_295_out, not_296_out, not_297_out, not_298_out, not_299_out, not_300_out, not_301_out,
       not_302_out, not_303_out, not_304_out, not_305_out, not_306_out, not_307_out, not_308_out,
       not_309_out, not_310_out, not_311_out, not_312_out, not_313_out, not_314_out, not_315_out,
       not_316_out, not_317_out, not_318_out, not_319_out, not_320_out, not_321_out, not_322_out,
       not_323_out, not_324_out, not_325_out, not_326_out, not_327_out, not_328_out, not_329_out,
       not_330_out, not_331_out, not_332_out, not_333_out, not_334_out, not_335_out, not_336_out,
       not_337_out, not_338_out, not_339_out, not_340_out, not_341_out, not_342_out, not_343_out,
       not_344_out, not_345_out, not_346_out, not_347_out, not_348_out, not_349_out, not_350_out,
       not_351_out, not_352_out, not_353_out, not_354_out, not_355_out, not_356_out, not_357_out,
       not_358_out, not_359_out, not_360_out, not_361_out, not_362_out, not_363_out, not_364_out,
       not_365_out, not_366_out, not_367_out, not_368_out, not_369_out, not_370_out, not_371_out,
       not_372_out, not_373_out, not_374_out, not_375_out, not_376_out, not_377_out, not_378_out,
       not_379_out, not_380_out, not_381_out, not_382_out, not_383_out, not_384_out, not_385_out,
       not_386_out, not_387_out, not_388_out, not_389_out, not_390_out, not_391_out, not_392_out,
       not_393_out, not_394_out, not_395_out, not_396_out, not_397_out, not_398_out, not_399_out,
       not_400_out, not_401_out, not_402_out, not_403_out, not_404_out, not_405_out, not_406_out,
       not_407_out, not_408_out, not_409_out, not_410_out, not_411_out, not_412_out, not_413_out,
       not_414_out, not_415_out, not_416_out, not_417_out, not_418_out, not_419_out, not_420_out,
       not_421_out, not_422_out, not_423_out, not_424_out, not_425_out, not_426_out, not_427_out,
       not_428_out, not_429_out, not_430_out, not_431_out, not_432_out, not_433_out, not_434_out,
       not_435_out, not_436_out, not_437_out, not_438_out, not_439_out, not_440_out, not_441_out,
       not_442_out, not_443_out, not_444_out, not_445_out, not_446_out, not_447_out, not_448_out,
       not_449_out, not_450_out, not_451_out, not_452_out, not_453_out, not_454_out, not_455_out,
       not_456_out, not_457_out, not_458_out, not_459_out, not_460_out, not_461_out, not_462_out,
       not_463_out, not_464_out, not_465_out, not_466_out, not_467_out, not_468_out, not_469_out,
       not_470_out, not_471_out, not_472_out, not_473_out, not_474_out;

  not not_1 (not_1_out, F14);
  not not_2 (not_2_out, F12);
  not not_3 (not_3_out, OP6);
  not not_4 (not_4_out, OP5);
  not not_5 (not_5_out, OP4);
  not not_6 (not_6_out, OP3);
  not not_7 (not_7_out, OP2);
  not not_8 (not_8_out, F14);
  not not_9 (not_9_out, F13);
  not not_10 (not_10_out, OP6);
  not not_11 (not_11_out, OP5);
  not not_12 (not_12_out, OP4);
  not not_13 (not_13_out, OP3);
  not not_14 (not_14_out, OP2);
  not not_15 (not_15_out, F14);
  not not_16 (not_16_out, F12);
  not not_17 (not_17_out, OP6);
  not not_18 (not_18_out, OP4);
  not not_19 (not_19_out, OP3);
  not not_20 (not_20_out, OP2);
  not not_21 (not_21_out, F14);
  not not_22 (not_22_out, F13);
  not not_23 (not_23_out, F12);
  not not_24 (not_24_out, OP6);
  not not_25 (not_25_out, OP5);
  not not_26 (not_26_out, OP3);
  not not_27 (not_27_out, OP2);
  not not_28 (not_28_out, OP6);
  not not_29 (not_29_out, OP5);
  not not_30 (not_30_out, OP3);
  not not_31 (not_31_out, OP2);
  not not_32 (not_32_out, F12);
  not not_33 (not_33_out, OP6);
  not not_34 (not_34_out, OP5);
  not not_35 (not_35_out, OP3);
  not not_36 (not_36_out, OP2);
  not not_37 (not_37_out, F13);
  not not_38 (not_38_out, F12);
  not not_39 (not_39_out, OP6);
  not not_40 (not_40_out, OP5);
  not not_41 (not_41_out, OP3);
  not not_42 (not_42_out, OP2);
  not not_43 (not_43_out, F14);
  not not_44 (not_44_out, F12);
  not not_45 (not_45_out, OP6);
  not not_46 (not_46_out, OP5);
  not not_47 (not_47_out, OP3);
  not not_48 (not_48_out, OP2);
  not not_49 (not_49_out, F30);
  not not_50 (not_50_out, F25);
  not not_51 (not_51_out, F14);
  not not_52 (not_52_out, F13);
  not not_53 (not_53_out, OP6);
  not not_54 (not_54_out, OP5);
  not not_55 (not_55_out, OP3);
  not not_56 (not_56_out, OP2);
  not not_57 (not_57_out, F30);
  not not_58 (not_58_out, F25);
  not not_59 (not_59_out, F13);
  not not_60 (not_60_out, OP6);
  not not_61 (not_61_out, OP5);
  not not_62 (not_62_out, OP3);
  not not_63 (not_63_out, OP2);
  not not_64 (not_64_out, F25);
  not not_65 (not_65_out, F13);
  not not_66 (not_66_out, OP6);
  not not_67 (not_67_out, OP5);
  not not_68 (not_68_out, OP3);
  not not_69 (not_69_out, OP2);
  not not_70 (not_70_out, F14);
  not not_71 (not_71_out, F12);
  not not_72 (not_72_out, OP6);
  not not_73 (not_73_out, OP5);
  not not_74 (not_74_out, OP4);
  not not_75 (not_75_out, OP3);
  not not_76 (not_76_out, OP2);
  not not_77 (not_77_out, F14);
  not not_78 (not_78_out, F12);
  not not_79 (not_79_out, OP6);
  not not_80 (not_80_out, OP4);
  not not_81 (not_81_out, OP3);
  not not_82 (not_82_out, OP2);
  not not_83 (not_83_out, F14);
  not not_84 (not_84_out, F13);
  not not_85 (not_85_out, F12);
  not not_86 (not_86_out, OP4);
  not not_87 (not_87_out, OP3);
  not not_88 (not_88_out, F12);
  not not_89 (not_89_out, OP3);
  not not_90 (not_90_out, OP2);
  not not_91 (not_91_out, OP3);
  not not_92 (not_92_out, OP2);
  not not_93 (not_93_out, F14);
  not not_94 (not_94_out, OP6);
  not not_95 (not_95_out, OP5);
  not not_96 (not_96_out, OP3);
  not not_97 (not_97_out, OP2);
  not not_98 (not_98_out, F14);
  not not_99 (not_99_out, F13);
  not not_100 (not_100_out, OP6);
  not not_101 (not_101_out, OP5);
  not not_102 (not_102_out, OP4);
  not not_103 (not_103_out, OP3);
  not not_104 (not_104_out, OP2);
  not not_105 (not_105_out, F30);
  not not_106 (not_106_out, F25);
  not not_107 (not_107_out, F14);
  not not_108 (not_108_out, F13);
  not not_109 (not_109_out, F12);
  not not_110 (not_110_out, OP6);
  not not_111 (not_111_out, OP3);
  not not_112 (not_112_out, OP2);
  not not_113 (not_113_out, F25);
  not not_114 (not_114_out, F14);
  not not_115 (not_115_out, F13);
  not not_116 (not_116_out, F12);
  not not_117 (not_117_out, OP6);
  not not_118 (not_118_out, OP3);
  not not_119 (not_119_out, OP2);
  not not_120 (not_120_out, F30);
  not not_121 (not_121_out, F25);
  not not_122 (not_122_out, OP6);
  not not_123 (not_123_out, OP3);
  not not_124 (not_124_out, OP2);
  not not_125 (not_125_out, F30);
  not not_126 (not_126_out, F25);
  not not_127 (not_127_out, F12);
  not not_128 (not_128_out, OP6);
  not not_129 (not_129_out, OP3);
  not not_130 (not_130_out, OP2);
  not not_131 (not_131_out, F30);
  not not_132 (not_132_out, F25);
  not not_133 (not_133_out, F14);
  not not_134 (not_134_out, F12);
  not not_135 (not_135_out, OP6);
  not not_136 (not_136_out, OP3);
  not not_137 (not_137_out, OP2);
  not not_138 (not_138_out, F30);
  not not_139 (not_139_out, F25);
  not not_140 (not_140_out, F14);
  not not_141 (not_141_out, OP6);
  not not_142 (not_142_out, OP3);
  not not_143 (not_143_out, OP2);
  not not_144 (not_144_out, F14);
  not not_145 (not_145_out, F13);
  not not_146 (not_146_out, F12);
  not not_147 (not_147_out, OP6);
  not not_148 (not_148_out, OP5);
  not not_149 (not_149_out, OP3);
  not not_150 (not_150_out, OP2);
  not not_151 (not_151_out, OP6);
  not not_152 (not_152_out, OP5);
  not not_153 (not_153_out, OP3);
  not not_154 (not_154_out, OP2);
  not not_155 (not_155_out, F12);
  not not_156 (not_156_out, OP6);
  not not_157 (not_157_out, OP5);
  not not_158 (not_158_out, OP3);
  not not_159 (not_159_out, OP2);
  not not_160 (not_160_out, F13);
  not not_161 (not_161_out, F12);
  not not_162 (not_162_out, OP6);
  not not_163 (not_163_out, OP5);
  not not_164 (not_164_out, OP3);
  not not_165 (not_165_out, OP2);
  not not_166 (not_166_out, F14);
  not not_167 (not_167_out, F12);
  not not_168 (not_168_out, OP6);
  not not_169 (not_169_out, OP5);
  not not_170 (not_170_out, OP3);
  not not_171 (not_171_out, OP2);
  not not_172 (not_172_out, F30);
  not not_173 (not_173_out, F25);
  not not_174 (not_174_out, F14);
  not not_175 (not_175_out, F13);
  not not_176 (not_176_out, OP6);
  not not_177 (not_177_out, OP5);
  not not_178 (not_178_out, OP3);
  not not_179 (not_179_out, OP2);
  not not_180 (not_180_out, F30);
  not not_181 (not_181_out, F25);
  not not_182 (not_182_out, F13);
  not not_183 (not_183_out, OP6);
  not not_184 (not_184_out, OP5);
  not not_185 (not_185_out, OP3);
  not not_186 (not_186_out, OP2);
  not not_187 (not_187_out, F25);
  not not_188 (not_188_out, F13);
  not not_189 (not_189_out, OP6);
  not not_190 (not_190_out, OP5);
  not not_191 (not_191_out, OP3);
  not not_192 (not_192_out, OP2);
  not not_193 (not_193_out, F14);
  not not_194 (not_194_out, F12);
  not not_195 (not_195_out, OP6);
  not not_196 (not_196_out, OP5);
  not not_197 (not_197_out, OP4);
  not not_198 (not_198_out, OP3);
  not not_199 (not_199_out, OP2);
  not not_200 (not_200_out, OP4);
  not not_201 (not_201_out, F14);
  not not_202 (not_202_out, F13);
  not not_203 (not_203_out, F12);
  not not_204 (not_204_out, OP4);
  not not_205 (not_205_out, OP3);
  not not_206 (not_206_out, OP6);
  not not_207 (not_207_out, OP5);
  not not_208 (not_208_out, OP3);
  not not_209 (not_209_out, F14);
  not not_210 (not_210_out, OP6);
  not not_211 (not_211_out, OP5);
  not not_212 (not_212_out, OP3);
  not not_213 (not_213_out, OP2);
  not not_214 (not_214_out, F14);
  not not_215 (not_215_out, F13);
  not not_216 (not_216_out, OP6);
  not not_217 (not_217_out, OP5);
  not not_218 (not_218_out, OP4);
  not not_219 (not_219_out, OP3);
  not not_220 (not_220_out, OP2);
  not not_221 (not_221_out, F30);
  not not_222 (not_222_out, F25);
  not not_223 (not_223_out, F14);
  not not_224 (not_224_out, F13);
  not not_225 (not_225_out, F12);
  not not_226 (not_226_out, OP3);
  not not_227 (not_227_out, OP2);
  not not_228 (not_228_out, F30);
  not not_229 (not_229_out, F25);
  not not_230 (not_230_out, F14);
  not not_231 (not_231_out, F13);
  not not_232 (not_232_out, F12);
  not not_233 (not_233_out, OP3);
  not not_234 (not_234_out, OP2);
  not not_235 (not_235_out, F14);
  not not_236 (not_236_out, F12);
  not not_237 (not_237_out, OP6);
  not not_238 (not_238_out, OP4);
  not not_239 (not_239_out, OP3);
  not not_240 (not_240_out, OP2);
  not not_241 (not_241_out, F14);
  not not_242 (not_242_out, F13);
  not not_243 (not_243_out, F12);
  not not_244 (not_244_out, OP4);
  not not_245 (not_245_out, OP3);
  not not_246 (not_246_out, OP2);
  not not_247 (not_247_out, F14);
  not not_248 (not_248_out, F13);
  not not_249 (not_249_out, OP4);
  not not_250 (not_250_out, OP3);
  not not_251 (not_251_out, OP2);
  not not_252 (not_252_out, F14);
  not not_253 (not_253_out, F13);
  not not_254 (not_254_out, F12);
  not not_255 (not_255_out, OP4);
  not not_256 (not_256_out, OP3);
  not not_257 (not_257_out, OP4);
  not not_258 (not_258_out, F12);
  not not_259 (not_259_out, OP4);
  not not_260 (not_260_out, OP3);
  not not_261 (not_261_out, OP2);
  not not_262 (not_262_out, F14);
  not not_263 (not_263_out, F13);
  not not_264 (not_264_out, OP6);
  not not_265 (not_265_out, OP5);
  not not_266 (not_266_out, OP4);
  not not_267 (not_267_out, OP3);
  not not_268 (not_268_out, OP2);
  not not_269 (not_269_out, OP6);
  not not_270 (not_270_out, OP5);
  not not_271 (not_271_out, OP3);
  not not_272 (not_272_out, F30);
  not not_273 (not_273_out, F25);
  not not_274 (not_274_out, F14);
  not not_275 (not_275_out, F13);
  not not_276 (not_276_out, F12);
  not not_277 (not_277_out, OP6);
  not not_278 (not_278_out, OP3);
  not not_279 (not_279_out, OP2);
  not not_280 (not_280_out, F25);
  not not_281 (not_281_out, F14);
  not not_282 (not_282_out, F13);
  not not_283 (not_283_out, F12);
  not not_284 (not_284_out, OP6);
  not not_285 (not_285_out, OP3);
  not not_286 (not_286_out, OP2);
  not not_287 (not_287_out, F30);
  not not_288 (not_288_out, F25);
  not not_289 (not_289_out, OP6);
  not not_290 (not_290_out, OP3);
  not not_291 (not_291_out, OP2);
  not not_292 (not_292_out, F30);
  not not_293 (not_293_out, F25);
  not not_294 (not_294_out, F12);
  not not_295 (not_295_out, OP6);
  not not_296 (not_296_out, OP3);
  not not_297 (not_297_out, OP2);
  not not_298 (not_298_out, F30);
  not not_299 (not_299_out, F25);
  not not_300 (not_300_out, F14);
  not not_301 (not_301_out, F12);
  not not_302 (not_302_out, OP6);
  not not_303 (not_303_out, OP3);
  not not_304 (not_304_out, OP2);
  not not_305 (not_305_out, F30);
  not not_306 (not_306_out, F25);
  not not_307 (not_307_out, F14);
  not not_308 (not_308_out, OP6);
  not not_309 (not_309_out, OP3);
  not not_310 (not_310_out, OP2);
  not not_311 (not_311_out, F14);
  not not_312 (not_312_out, F13);
  not not_313 (not_313_out, F12);
  not not_314 (not_314_out, OP6);
  not not_315 (not_315_out, OP5);
  not not_316 (not_316_out, OP3);
  not not_317 (not_317_out, OP2);
  not not_318 (not_318_out, OP6);
  not not_319 (not_319_out, OP5);
  not not_320 (not_320_out, OP3);
  not not_321 (not_321_out, OP2);
  not not_322 (not_322_out, F12);
  not not_323 (not_323_out, OP6);
  not not_324 (not_324_out, OP5);
  not not_325 (not_325_out, OP3);
  not not_326 (not_326_out, OP2);
  not not_327 (not_327_out, F13);
  not not_328 (not_328_out, F12);
  not not_329 (not_329_out, OP6);
  not not_330 (not_330_out, OP5);
  not not_331 (not_331_out, OP3);
  not not_332 (not_332_out, OP2);
  not not_333 (not_333_out, F14);
  not not_334 (not_334_out, F12);
  not not_335 (not_335_out, OP6);
  not not_336 (not_336_out, OP5);
  not not_337 (not_337_out, OP3);
  not not_338 (not_338_out, OP2);
  not not_339 (not_339_out, F30);
  not not_340 (not_340_out, F25);
  not not_341 (not_341_out, F14);
  not not_342 (not_342_out, F13);
  not not_343 (not_343_out, OP6);
  not not_344 (not_344_out, OP5);
  not not_345 (not_345_out, OP3);
  not not_346 (not_346_out, OP2);
  not not_347 (not_347_out, F30);
  not not_348 (not_348_out, F25);
  not not_349 (not_349_out, F13);
  not not_350 (not_350_out, OP6);
  not not_351 (not_351_out, OP5);
  not not_352 (not_352_out, OP3);
  not not_353 (not_353_out, OP2);
  not not_354 (not_354_out, F25);
  not not_355 (not_355_out, F13);
  not not_356 (not_356_out, OP6);
  not not_357 (not_357_out, OP5);
  not not_358 (not_358_out, OP3);
  not not_359 (not_359_out, OP2);
  not not_360 (not_360_out, F14);
  not not_361 (not_361_out, F12);
  not not_362 (not_362_out, OP6);
  not not_363 (not_363_out, OP5);
  not not_364 (not_364_out, OP4);
  not not_365 (not_365_out, OP3);
  not not_366 (not_366_out, OP2);
  not not_367 (not_367_out, F14);
  not not_368 (not_368_out, F12);
  not not_369 (not_369_out, OP6);
  not not_370 (not_370_out, OP4);
  not not_371 (not_371_out, OP3);
  not not_372 (not_372_out, OP2);
  not not_373 (not_373_out, F14);
  not not_374 (not_374_out, F13);
  not not_375 (not_375_out, F12);
  not not_376 (not_376_out, OP4);
  not not_377 (not_377_out, OP3);
  not not_378 (not_378_out, OP2);
  not not_379 (not_379_out, F14);
  not not_380 (not_380_out, F13);
  not not_381 (not_381_out, OP4);
  not not_382 (not_382_out, OP3);
  not not_383 (not_383_out, OP2);
  not not_384 (not_384_out, F14);
  not not_385 (not_385_out, F13);
  not not_386 (not_386_out, F12);
  not not_387 (not_387_out, OP4);
  not not_388 (not_388_out, OP3);
  not not_389 (not_389_out, F14);
  not not_390 (not_390_out, OP6);
  not not_391 (not_391_out, OP5);
  not not_392 (not_392_out, OP3);
  not not_393 (not_393_out, OP2);
  not not_394 (not_394_out, F14);
  not not_395 (not_395_out, F13);
  not not_396 (not_396_out, OP6);
  not not_397 (not_397_out, OP5);
  not not_398 (not_398_out, OP4);
  not not_399 (not_399_out, OP3);
  not not_400 (not_400_out, OP2);
  not not_401 (not_401_out, F12);
  not not_402 (not_402_out, OP4);
  not not_403 (not_403_out, OP3);
  not not_404 (not_404_out, OP2);
  not not_405 (not_405_out, F30);
  not not_406 (not_406_out, F25);
  not not_407 (not_407_out, F14);
  not not_408 (not_408_out, F13);
  not not_409 (not_409_out, F12);
  not not_410 (not_410_out, OP6);
  not not_411 (not_411_out, OP3);
  not not_412 (not_412_out, OP2);
  not not_413 (not_413_out, F25);
  not not_414 (not_414_out, F14);
  not not_415 (not_415_out, F13);
  not not_416 (not_416_out, F12);
  not not_417 (not_417_out, OP6);
  not not_418 (not_418_out, OP3);
  not not_419 (not_419_out, OP2);
  not not_420 (not_420_out, F30);
  not not_421 (not_421_out, F25);
  not not_422 (not_422_out, OP6);
  not not_423 (not_423_out, OP3);
  not not_424 (not_424_out, OP2);
  not not_425 (not_425_out, F30);
  not not_426 (not_426_out, F25);
  not not_427 (not_427_out, F12);
  not not_428 (not_428_out, OP6);
  not not_429 (not_429_out, OP3);
  not not_430 (not_430_out, OP2);
  not not_431 (not_431_out, F30);
  not not_432 (not_432_out, F25);
  not not_433 (not_433_out, F14);
  not not_434 (not_434_out, F12);
  not not_435 (not_435_out, OP6);
  not not_436 (not_436_out, OP3);
  not not_437 (not_437_out, OP2);
  not not_438 (not_438_out, F30);
  not not_439 (not_439_out, F25);
  not not_440 (not_440_out, F14);
  not not_441 (not_441_out, OP6);
  not not_442 (not_442_out, OP3);
  not not_443 (not_443_out, OP2);
  not not_444 (not_444_out, F14);
  not not_445 (not_445_out, F12);
  not not_446 (not_446_out, OP6);
  not not_447 (not_447_out, OP4);
  not not_448 (not_448_out, OP3);
  not not_449 (not_449_out, OP2);
  not not_450 (not_450_out, F14);
  not not_451 (not_451_out, F13);
  not not_452 (not_452_out, F12);
  not not_453 (not_453_out, OP4);
  not not_454 (not_454_out, OP3);
  not not_455 (not_455_out, OP2);
  not not_456 (not_456_out, F14);
  not not_457 (not_457_out, F13);
  not not_458 (not_458_out, OP4);
  not not_459 (not_459_out, OP3);
  not not_460 (not_460_out, OP2);
  not not_461 (not_461_out, F12);
  not not_462 (not_462_out, OP4);
  not not_463 (not_463_out, OP3);
  not not_464 (not_464_out, OP2);
  not not_465 (not_465_out, F12);
  not not_466 (not_466_out, OP3);
  not not_467 (not_467_out, OP2);
  not not_468 (not_468_out, OP3);
  not not_469 (not_469_out, OP2);
  not not_470 (not_470_out, F14);
  not not_471 (not_471_out, OP6);
  not not_472 (not_472_out, OP5);
  not not_473 (not_473_out, OP3);
  not not_474 (not_474_out, OP2);
  and and_1 (and_1_out, not_1_out, F13, not_2_out, not_3_out, not_4_out, not_5_out, not_6_out, not_7_out);
  and and_2 (and_2_out, not_8_out, not_9_out, F12, not_10_out, not_11_out, not_12_out, not_13_out, not_14_out);
  and and_3 (MemWrite, not_15_out, F13, not_16_out, not_17_out, OP5, not_18_out, not_19_out, not_20_out);
  and and_4 (and_4_out, not_21_out, not_22_out, not_23_out, not_24_out, not_25_out, OP4, not_26_out, not_27_out);
  and and_5 (and_5_out, F14, F13, F12, not_28_out, not_29_out, OP4, not_30_out, not_31_out);
  and and_6 (and_6_out, F14, F13, not_32_out, not_33_out, not_34_out, OP4, not_35_out, not_36_out);
  and and_7 (and_7_out, F14, not_37_out, not_38_out, not_39_out, not_40_out, OP4, not_41_out, not_42_out);
  and and_8 (and_8_out, not_43_out, F13, not_44_out, not_45_out, not_46_out, OP4, not_47_out, not_48_out);
  and and_9 (and_9_out, not_49_out, not_50_out, not_51_out, not_52_out, F12, not_53_out, not_54_out, OP4, not_55_out, not_56_out);
  and and_10 (and_10_out, not_57_out, not_58_out, F14, not_59_out, F12, not_60_out, not_61_out, OP4, not_62_out, not_63_out);
  and and_11 (and_11_out, F30, not_64_out, F14, not_65_out, F12, not_66_out, not_67_out, OP4, not_68_out, not_69_out);
  and and_12 (and_12_out, not_70_out, F13, not_71_out, not_72_out, not_73_out, not_74_out, not_75_out, not_76_out);
  and and_13 (and_13_out, not_77_out, F13, not_78_out, not_79_out, OP5, not_80_out, not_81_out, not_82_out);
  and and_14 (and_14_out, not_83_out, not_84_out, not_85_out, OP6, OP5, not_86_out, not_87_out, OP2);
  and and_15 (and_15_out, F14, F13, not_88_out, OP6, OP5, OP4, not_89_out, not_90_out);
  and and_16 (and_16_out, F14, F13, F12, OP6, OP5, OP4, not_91_out, not_92_out);
  and and_17 (and_17_out, not_93_out, F13, F12, not_94_out, not_95_out, OP4, not_96_out, not_97_out);
  and and_18 (and_18_out, not_98_out, not_99_out, F12, not_100_out, not_101_out, not_102_out, not_103_out, not_104_out);
  and and_19 (and_19_out, not_105_out, not_106_out, not_107_out, not_108_out, not_109_out, not_110_out, OP5, OP4, not_111_out, not_112_out);
  and and_20 (and_20_out, F30, not_113_out, not_114_out, not_115_out, not_116_out, not_117_out, OP5, OP4, not_118_out, not_119_out);
  and and_21 (and_21_out, not_120_out, not_121_out, F14, F13, F12, not_122_out, OP5, OP4, not_123_out, not_124_out);
  and and_22 (and_22_out, not_125_out, not_126_out, F14, F13, not_127_out, not_128_out, OP5, OP4, not_129_out, not_130_out);
  and and_23 (and_23_out, not_131_out, not_132_out, not_133_out, F13, not_134_out, not_135_out, OP5, OP4, not_136_out, not_137_out);
  and and_24 (and_24_out, not_138_out, not_139_out, not_140_out, F13, F12, not_141_out, OP5, OP4, not_142_out, not_143_out);
  and and_25 (and_25_out, not_144_out, not_145_out, not_146_out, not_147_out, not_148_out, OP4, not_149_out, not_150_out);
  and and_26 (and_26_out, F14, F13, F12, not_151_out, not_152_out, OP4, not_153_out, not_154_out);
  and and_27 (and_27_out, F14, F13, not_155_out, not_156_out, not_157_out, OP4, not_158_out, not_159_out);
  and and_28 (and_28_out, F14, not_160_out, not_161_out, not_162_out, not_163_out, OP4, not_164_out, not_165_out);
  and and_29 (and_29_out, not_166_out, F13, not_167_out, not_168_out, not_169_out, OP4, not_170_out, not_171_out);
  and and_30 (and_30_out, not_172_out, not_173_out, not_174_out, not_175_out, F12, not_176_out, not_177_out, OP4, not_178_out, not_179_out);
  and and_31 (and_31_out, not_180_out, not_181_out, F14, not_182_out, F12, not_183_out, not_184_out, OP4, not_185_out, not_186_out);
  and and_32 (and_32_out, F30, not_187_out, F14, not_188_out, F12, not_189_out, not_190_out, OP4, not_191_out, not_192_out);
  and and_33 (and_33_out, not_193_out, F13, not_194_out, not_195_out, not_196_out, not_197_out, not_198_out, not_199_out);
  and and_34 (and_34_out, OP6, OP5, not_200_out, OP3, OP2);
  and and_35 (and_35_out, not_201_out, not_202_out, not_203_out, OP6, OP5, not_204_out, not_205_out, OP2);
  and and_36 (and_36_out, not_206_out, not_207_out, OP4, not_208_out, OP2);
  and and_37 (and_37_out, not_209_out, F13, F12, not_210_out, not_211_out, OP4, not_212_out, not_213_out);
  and and_38 (and_38_out, not_214_out, not_215_out, F12, not_216_out, not_217_out, not_218_out, not_219_out, not_220_out);
  and and_39 (and_39_out, not_221_out, not_222_out, not_223_out, not_224_out, not_225_out, OP6, OP5, OP4, not_226_out, not_227_out);
  and and_40 (and_40_out, not_228_out, not_229_out, not_230_out, not_231_out, not_232_out, OP6, OP5, OP4, not_233_out, not_234_out);
  and and_41 (S_Type, not_235_out, F13, not_236_out, not_237_out, OP5, not_238_out, not_239_out, not_240_out);
  and and_42 (BEQ, not_241_out, not_242_out, not_243_out, OP6, OP5, not_244_out, not_245_out, not_246_out);
  and and_43 (BNE, not_247_out, not_248_out, F12, OP6, OP5, not_249_out, not_250_out, not_251_out);
  and and_44 (JALR, not_252_out, not_253_out, not_254_out, OP6, OP5, not_255_out, not_256_out, OP2);
  and and_45 (JAL, OP6, OP5, not_257_out, OP3, OP2);
  and and_46 (BLTU, F14, F13, not_258_out, OP6, OP5, not_259_out, not_260_out, not_261_out);
  and and_47 (LB, not_262_out, not_263_out, F12, not_264_out, not_265_out, not_266_out, not_267_out, not_268_out);
  and and_48 (U_Type, not_269_out, not_270_out, OP4, not_271_out, OP2);
  and and_49 (and_49_out, not_272_out, not_273_out, not_274_out, not_275_out, not_276_out, not_277_out, OP5, OP4, not_278_out, not_279_out);
  and and_50 (and_50_out, F30, not_280_out, not_281_out, not_282_out, not_283_out, not_284_out, OP5, OP4, not_285_out, not_286_out);
  and and_51 (and_51_out, not_287_out, not_288_out, F14, F13, F12, not_289_out, OP5, OP4, not_290_out, not_291_out);
  and and_52 (and_52_out, not_292_out, not_293_out, F14, F13, not_294_out, not_295_out, OP5, OP4, not_296_out, not_297_out);
  and and_53 (and_53_out, not_298_out, not_299_out, not_300_out, F13, not_301_out, not_302_out, OP5, OP4, not_303_out, not_304_out);
  and and_54 (and_54_out, not_305_out, not_306_out, not_307_out, F13, F12, not_308_out, OP5, OP4, not_309_out, not_310_out);
  and and_55 (and_55_out, not_311_out, not_312_out, not_313_out, not_314_out, not_315_out, OP4, not_316_out, not_317_out);
  and and_56 (and_56_out, F14, F13, F12, not_318_out, not_319_out, OP4, not_320_out, not_321_out);
  and and_57 (and_57_out, F14, F13, not_322_out, not_323_out, not_324_out, OP4, not_325_out, not_326_out);
  and and_58 (and_58_out, F14, not_327_out, not_328_out, not_329_out, not_330_out, OP4, not_331_out, not_332_out);
  and and_59 (and_59_out, not_333_out, F13, not_334_out, not_335_out, not_336_out, OP4, not_337_out, not_338_out);
  and and_60 (and_60_out, not_339_out, not_340_out, not_341_out, not_342_out, F12, not_343_out, not_344_out, OP4, not_345_out, not_346_out);
  and and_61 (and_61_out, not_347_out, not_348_out, F14, not_349_out, F12, not_350_out, not_351_out, OP4, not_352_out, not_353_out);
  and and_62 (and_62_out, F30, not_354_out, F14, not_355_out, F12, not_356_out, not_357_out, OP4, not_358_out, not_359_out);
  and and_63 (and_63_out, not_360_out, F13, not_361_out, not_362_out, not_363_out, not_364_out, not_365_out, not_366_out);
  and and_64 (and_64_out, not_367_out, F13, not_368_out, not_369_out, OP5, not_370_out, not_371_out, not_372_out);
  and and_65 (and_65_out, not_373_out, not_374_out, not_375_out, OP6, OP5, not_376_out, not_377_out, not_378_out);
  and and_66 (and_66_out, not_379_out, not_380_out, F12, OP6, OP5, not_381_out, not_382_out, not_383_out);
  and and_67 (and_67_out, not_384_out, not_385_out, not_386_out, OP6, OP5, not_387_out, not_388_out, OP2);
  and and_68 (and_68_out, not_389_out, F13, F12, not_390_out, not_391_out, OP4, not_392_out, not_393_out);
  and and_69 (and_69_out, not_394_out, not_395_out, F12, not_396_out, not_397_out, not_398_out, not_399_out, not_400_out);
  and and_70 (and_70_out, F14, F13, not_401_out, OP6, OP5, not_402_out, not_403_out, not_404_out);
  and and_71 (and_71_out, not_405_out, not_406_out, not_407_out, not_408_out, not_409_out, not_410_out, OP5, OP4, not_411_out, not_412_out);
  and and_72 (and_72_out, F30, not_413_out, not_414_out, not_415_out, not_416_out, not_417_out, OP5, OP4, not_418_out, not_419_out);
  and and_73 (and_73_out, not_420_out, not_421_out, F14, F13, F12, not_422_out, OP5, OP4, not_423_out, not_424_out);
  and and_74 (and_74_out, not_425_out, not_426_out, F14, F13, not_427_out, not_428_out, OP5, OP4, not_429_out, not_430_out);
  and and_75 (and_75_out, not_431_out, not_432_out, not_433_out, F13, not_434_out, not_435_out, OP5, OP4, not_436_out, not_437_out);
  and and_76 (and_76_out, not_438_out, not_439_out, not_440_out, F13, F12, not_441_out, OP5, OP4, not_442_out, not_443_out);
  and and_77 (and_77_out, not_444_out, F13, not_445_out, not_446_out, OP5, not_447_out, not_448_out, not_449_out);
  and and_78 (and_78_out, not_450_out, not_451_out, not_452_out, OP6, OP5, not_453_out, not_454_out, not_455_out);
  and and_79 (and_79_out, not_456_out, not_457_out, F12, OP6, OP5, not_458_out, not_459_out, not_460_out);
  and and_80 (and_80_out, F14, F13, not_461_out, OP6, OP5, not_462_out, not_463_out, not_464_out);
  and and_81 (and_81_out, F14, F13, not_465_out, OP6, OP5, OP4, not_466_out, not_467_out);
  and and_82 (and_82_out, F14, F13, F12, OP6, OP5, OP4, not_468_out, not_469_out);
  and and_83 (SLTIU, not_470_out, F13, F12, not_471_out, not_472_out, OP4, not_473_out, not_474_out);
  or or_1 (MemToReg, and_1_out, and_2_out);
  or or_2 (ecall, and_39_out, and_40_out);
  or or_3 (CSR, and_81_out, and_82_out);
  or or_4 (ALU_SRC, and_4_out, and_5_out, and_6_out, and_7_out, and_8_out, and_9_out, and_10_out, and_11_out, and_12_out, and_13_out, and_14_out, and_15_out, and_16_out, and_17_out, and_18_out);
  or or_5 (RegWrite, and_19_out, and_20_out, and_21_out, and_22_out, and_23_out, and_24_out, and_25_out, and_26_out, and_27_out, and_28_out, and_29_out, and_30_out, and_31_out, and_32_out, and_33_out, and_34_out, and_35_out, and_36_out, and_37_out, and_38_out);
  or or_6 (rs2_used, and_71_out, and_72_out, and_73_out, and_74_out, and_75_out, and_76_out, and_77_out, and_78_out, and_79_out, and_80_out);
  or or_7 (rs1_used, and_49_out, and_50_out, and_51_out, and_52_out, and_53_out, and_54_out, and_55_out, and_56_out, and_57_out, and_58_out, and_59_out, and_60_out, and_61_out, and_62_out, and_63_out, and_64_out, and_65_out, and_66_out, and_67_out, and_68_out, and_69_out, and_70_out);
endmodule

// 运算器控制器
module \运算控制器自动生成  (
  input  OP2,
  input  OP3,
  input  OP4,
  input  OP5,
  input  OP6,
  input  F12,
  input  F13,
  input  F14,
  input  F25,
  input  F30,
  output S0,
  output S1,
  output S2,
  output S3
);

  wire and_1_out, and_2_out, and_3_out, and_4_out, and_5_out, and_6_out, and_7_out, and_8_out, and_9_out,
       and_10_out, and_11_out, and_12_out, and_13_out, and_14_out, and_15_out, and_16_out, and_17_out,
       and_18_out, and_19_out, and_20_out, and_21_out, and_22_out, and_23_out, and_24_out, and_25_out,
       and_26_out, and_27_out, and_28_out, and_29_out, and_30_out, and_31_out, and_32_out, and_33_out,
       and_34_out, and_35_out, and_36_out, and_37_out, and_38_out, and_39_out, and_40_out, and_41_out,
       and_42_out, and_43_out, and_44_out, and_45_out, and_46_out, and_47_out, and_48_out, not_1_out,
       not_2_out, not_3_out, not_4_out, not_5_out, not_6_out, not_7_out, not_8_out, not_9_out, not_10_out,
       not_11_out, not_12_out, not_13_out, not_14_out, not_15_out, not_16_out, not_17_out, not_18_out,
       not_19_out, not_20_out, not_21_out, not_22_out, not_23_out, not_24_out, not_25_out, not_26_out,
       not_27_out, not_28_out, not_29_out, not_30_out, not_31_out, not_32_out, not_33_out, not_34_out,
       not_35_out, not_36_out, not_37_out, not_38_out, not_39_out, not_40_out, not_41_out, not_42_out,
       not_43_out, not_44_out, not_45_out, not_46_out, not_47_out, not_48_out, not_49_out, not_50_out,
       not_51_out, not_52_out, not_53_out, not_54_out, not_55_out, not_56_out, not_57_out, not_58_out,
       not_59_out, not_60_out, not_61_out, not_62_out, not_63_out, not_64_out, not_65_out, not_66_out,
       not_67_out, not_68_out, not_69_out, not_70_out, not_71_out, not_72_out, not_73_out, not_74_out,
       not_75_out, not_76_out, not_77_out, not_78_out, not_79_out, not_80_out, not_81_out, not_82_out,
       not_83_out, not_84_out, not_85_out, not_86_out, not_87_out, not_88_out, not_89_out, not_90_out,
       not_91_out, not_92_out, not_93_out, not_94_out, not_95_out, not_96_out, not_97_out, not_98_out,
       not_99_out, not_100_out, not_101_out, not_102_out, not_103_out, not_104_out, not_105_out, not_106_out,
       not_107_out, not_108_out, not_109_out, not_110_out, not_111_out, not_112_out, not_113_out,
       not_114_out, not_115_out, not_116_out, not_117_out, not_118_out, not_119_out, not_120_out,
       not_121_out, not_122_out, not_123_out, not_124_out, not_125_out, not_126_out, not_127_out,
       not_128_out, not_129_out, not_130_out, not_131_out, not_132_out, not_133_out, not_134_out,
       not_135_out, not_136_out, not_137_out, not_138_out, not_139_out, not_140_out, not_141_out,
       not_142_out, not_143_out, not_144_out, not_145_out, not_146_out, not_147_out, not_148_out,
       not_149_out, not_150_out, not_151_out, not_152_out, not_153_out, not_154_out, not_155_out,
       not_156_out, not_157_out, not_158_out, not_159_out, not_160_out, not_161_out, not_162_out,
       not_163_out, not_164_out, not_165_out, not_166_out, not_167_out, not_168_out, not_169_out,
       not_170_out, not_171_out, not_172_out, not_173_out, not_174_out, not_175_out, not_176_out,
       not_177_out, not_178_out, not_179_out, not_180_out, not_181_out, not_182_out, not_183_out,
       not_184_out, not_185_out, not_186_out, not_187_out, not_188_out, not_189_out, not_190_out,
       not_191_out, not_192_out, not_193_out, not_194_out, not_195_out, not_196_out, not_197_out,
       not_198_out, not_199_out, not_200_out, not_201_out, not_202_out, not_203_out, not_204_out,
       not_205_out, not_206_out, not_207_out, not_208_out, not_209_out, not_210_out, not_211_out,
       not_212_out, not_213_out, not_214_out, not_215_out, not_216_out, not_217_out, not_218_out,
       not_219_out, not_220_out, not_221_out, not_222_out, not_223_out, not_224_out, not_225_out,
       not_226_out, not_227_out, not_228_out, not_229_out, not_230_out, not_231_out, not_232_out,
       not_233_out, not_234_out, not_235_out, not_236_out, not_237_out, not_238_out, not_239_out,
       not_240_out, not_241_out, not_242_out, not_243_out, not_244_out, not_245_out, not_246_out,
       not_247_out, not_248_out, not_249_out, not_250_out, not_251_out, not_252_out, not_253_out,
       not_254_out, not_255_out, not_256_out, not_257_out, not_258_out, not_259_out, not_260_out,
       not_261_out, not_262_out, not_263_out;

  not not_1 (not_1_out, F30);
  not not_2 (not_2_out, F25);
  not not_3 (not_3_out, F14);
  not not_4 (not_4_out, F13);
  not not_5 (not_5_out, F12);
  not not_6 (not_6_out, OP6);
  not not_7 (not_7_out, OP3);
  not not_8 (not_8_out, OP2);
  not not_9 (not_9_out, F30);
  not not_10 (not_10_out, F25);
  not not_11 (not_11_out, OP6);
  not not_12 (not_12_out, OP3);
  not not_13 (not_13_out, OP2);
  not not_14 (not_14_out, F30);
  not not_15 (not_15_out, F25);
  not not_16 (not_16_out, F14);
  not not_17 (not_17_out, F12);
  not not_18 (not_18_out, OP6);
  not not_19 (not_19_out, OP3);
  not not_20 (not_20_out, OP2);
  not not_21 (not_21_out, F14);
  not not_22 (not_22_out, F13);
  not not_23 (not_23_out, F12);
  not not_24 (not_24_out, OP6);
  not not_25 (not_25_out, OP5);
  not not_26 (not_26_out, OP3);
  not not_27 (not_27_out, OP2);
  not not_28 (not_28_out, OP6);
  not not_29 (not_29_out, OP5);
  not not_30 (not_30_out, OP3);
  not not_31 (not_31_out, OP2);
  not not_32 (not_32_out, F13);
  not not_33 (not_33_out, F12);
  not not_34 (not_34_out, OP6);
  not not_35 (not_35_out, OP5);
  not not_36 (not_36_out, OP3);
  not not_37 (not_37_out, OP2);
  not not_38 (not_38_out, F14);
  not not_39 (not_39_out, F12);
  not not_40 (not_40_out, OP6);
  not not_41 (not_41_out, OP5);
  not not_42 (not_42_out, OP3);
  not not_43 (not_43_out, OP2);
  not not_44 (not_44_out, F25);
  not not_45 (not_45_out, F13);
  not not_46 (not_46_out, OP6);
  not not_47 (not_47_out, OP5);
  not not_48 (not_48_out, OP3);
  not not_49 (not_49_out, OP2);
  not not_50 (not_50_out, F14);
  not not_51 (not_51_out, F12);
  not not_52 (not_52_out, OP6);
  not not_53 (not_53_out, OP5);
  not not_54 (not_54_out, OP4);
  not not_55 (not_55_out, OP3);
  not not_56 (not_56_out, OP2);
  not not_57 (not_57_out, F14);
  not not_58 (not_58_out, F12);
  not not_59 (not_59_out, OP6);
  not not_60 (not_60_out, OP4);
  not not_61 (not_61_out, OP3);
  not not_62 (not_62_out, OP2);
  not not_63 (not_63_out, OP3);
  not not_64 (not_64_out, OP2);
  not not_65 (not_65_out, OP6);
  not not_66 (not_66_out, OP5);
  not not_67 (not_67_out, OP3);
  not not_68 (not_68_out, F14);
  not not_69 (not_69_out, F13);
  not not_70 (not_70_out, OP6);
  not not_71 (not_71_out, OP5);
  not not_72 (not_72_out, OP4);
  not not_73 (not_73_out, OP3);
  not not_74 (not_74_out, OP2);
  not not_75 (not_75_out, F25);
  not not_76 (not_76_out, F14);
  not not_77 (not_77_out, F13);
  not not_78 (not_78_out, F12);
  not not_79 (not_79_out, OP6);
  not not_80 (not_80_out, OP3);
  not not_81 (not_81_out, OP2);
  not not_82 (not_82_out, F30);
  not not_83 (not_83_out, F25);
  not not_84 (not_84_out, OP6);
  not not_85 (not_85_out, OP3);
  not not_86 (not_86_out, OP2);
  not not_87 (not_87_out, F30);
  not not_88 (not_88_out, F25);
  not not_89 (not_89_out, F14);
  not not_90 (not_90_out, F12);
  not not_91 (not_91_out, OP6);
  not not_92 (not_92_out, OP3);
  not not_93 (not_93_out, OP2);
  not not_94 (not_94_out, OP6);
  not not_95 (not_95_out, OP5);
  not not_96 (not_96_out, OP3);
  not not_97 (not_97_out, OP2);
  not not_98 (not_98_out, F14);
  not not_99 (not_99_out, F12);
  not not_100 (not_100_out, OP6);
  not not_101 (not_101_out, OP5);
  not not_102 (not_102_out, OP3);
  not not_103 (not_103_out, OP2);
  not not_104 (not_104_out, F30);
  not not_105 (not_105_out, F25);
  not not_106 (not_106_out, F13);
  not not_107 (not_107_out, OP6);
  not not_108 (not_108_out, OP5);
  not not_109 (not_109_out, OP3);
  not not_110 (not_110_out, OP2);
  not not_111 (not_111_out, F14);
  not not_112 (not_112_out, F13);
  not not_113 (not_113_out, F12);
  not not_114 (not_114_out, OP4);
  not not_115 (not_115_out, OP3);
  not not_116 (not_116_out, OP2);
  not not_117 (not_117_out, F14);
  not not_118 (not_118_out, F13);
  not not_119 (not_119_out, OP4);
  not not_120 (not_120_out, OP3);
  not not_121 (not_121_out, OP2);
  not not_122 (not_122_out, F14);
  not not_123 (not_123_out, F13);
  not not_124 (not_124_out, F12);
  not not_125 (not_125_out, OP4);
  not not_126 (not_126_out, OP3);
  not not_127 (not_127_out, OP3);
  not not_128 (not_128_out, OP2);
  not not_129 (not_129_out, F30);
  not not_130 (not_130_out, F25);
  not not_131 (not_131_out, F14);
  not not_132 (not_132_out, F13);
  not not_133 (not_133_out, F12);
  not not_134 (not_134_out, OP6);
  not not_135 (not_135_out, OP3);
  not not_136 (not_136_out, OP2);
  not not_137 (not_137_out, F25);
  not not_138 (not_138_out, F14);
  not not_139 (not_139_out, F13);
  not not_140 (not_140_out, F12);
  not not_141 (not_141_out, OP6);
  not not_142 (not_142_out, OP3);
  not not_143 (not_143_out, OP2);
  not not_144 (not_144_out, F30);
  not not_145 (not_145_out, F25);
  not not_146 (not_146_out, OP6);
  not not_147 (not_147_out, OP3);
  not not_148 (not_148_out, OP2);
  not not_149 (not_149_out, F30);
  not not_150 (not_150_out, F25);
  not not_151 (not_151_out, F14);
  not not_152 (not_152_out, OP6);
  not not_153 (not_153_out, OP3);
  not not_154 (not_154_out, OP2);
  not not_155 (not_155_out, F14);
  not not_156 (not_156_out, F13);
  not not_157 (not_157_out, F12);
  not not_158 (not_158_out, OP6);
  not not_159 (not_159_out, OP5);
  not not_160 (not_160_out, OP3);
  not not_161 (not_161_out, OP2);
  not not_162 (not_162_out, OP6);
  not not_163 (not_163_out, OP5);
  not not_164 (not_164_out, OP3);
  not not_165 (not_165_out, OP2);
  not not_166 (not_166_out, F14);
  not not_167 (not_167_out, F12);
  not not_168 (not_168_out, OP6);
  not not_169 (not_169_out, OP5);
  not not_170 (not_170_out, OP4);
  not not_171 (not_171_out, OP3);
  not not_172 (not_172_out, OP2);
  not not_173 (not_173_out, F14);
  not not_174 (not_174_out, F12);
  not not_175 (not_175_out, OP6);
  not not_176 (not_176_out, OP4);
  not not_177 (not_177_out, OP3);
  not not_178 (not_178_out, OP2);
  not not_179 (not_179_out, F14);
  not not_180 (not_180_out, F13);
  not not_181 (not_181_out, F12);
  not not_182 (not_182_out, OP4);
  not not_183 (not_183_out, OP3);
  not not_184 (not_184_out, OP2);
  not not_185 (not_185_out, F14);
  not not_186 (not_186_out, F13);
  not not_187 (not_187_out, OP4);
  not not_188 (not_188_out, OP3);
  not not_189 (not_189_out, OP2);
  not not_190 (not_190_out, F14);
  not not_191 (not_191_out, F13);
  not not_192 (not_192_out, F12);
  not not_193 (not_193_out, OP4);
  not not_194 (not_194_out, OP3);
  not not_195 (not_195_out, OP3);
  not not_196 (not_196_out, OP2);
  not not_197 (not_197_out, OP6);
  not not_198 (not_198_out, OP5);
  not not_199 (not_199_out, OP3);
  not not_200 (not_200_out, F14);
  not not_201 (not_201_out, OP6);
  not not_202 (not_202_out, OP5);
  not not_203 (not_203_out, OP3);
  not not_204 (not_204_out, OP2);
  not not_205 (not_205_out, F14);
  not not_206 (not_206_out, F13);
  not not_207 (not_207_out, OP6);
  not not_208 (not_208_out, OP5);
  not not_209 (not_209_out, OP4);
  not not_210 (not_210_out, OP3);
  not not_211 (not_211_out, OP2);
  not not_212 (not_212_out, F12);
  not not_213 (not_213_out, OP4);
  not not_214 (not_214_out, OP3);
  not not_215 (not_215_out, OP2);
  not not_216 (not_216_out, F30);
  not not_217 (not_217_out, F25);
  not not_218 (not_218_out, F12);
  not not_219 (not_219_out, OP6);
  not not_220 (not_220_out, OP3);
  not not_221 (not_221_out, OP2);
  not not_222 (not_222_out, F30);
  not not_223 (not_223_out, F25);
  not not_224 (not_224_out, F14);
  not not_225 (not_225_out, F12);
  not not_226 (not_226_out, OP6);
  not not_227 (not_227_out, OP3);
  not not_228 (not_228_out, OP2);
  not not_229 (not_229_out, F30);
  not not_230 (not_230_out, F25);
  not not_231 (not_231_out, F14);
  not not_232 (not_232_out, OP6);
  not not_233 (not_233_out, OP3);
  not not_234 (not_234_out, OP2);
  not not_235 (not_235_out, F12);
  not not_236 (not_236_out, OP6);
  not not_237 (not_237_out, OP5);
  not not_238 (not_238_out, OP3);
  not not_239 (not_239_out, OP2);
  not not_240 (not_240_out, F13);
  not not_241 (not_241_out, F12);
  not not_242 (not_242_out, OP6);
  not not_243 (not_243_out, OP5);
  not not_244 (not_244_out, OP3);
  not not_245 (not_245_out, OP2);
  not not_246 (not_246_out, F14);
  not not_247 (not_247_out, F12);
  not not_248 (not_248_out, OP6);
  not not_249 (not_249_out, OP5);
  not not_250 (not_250_out, OP3);
  not not_251 (not_251_out, OP2);
  not not_252 (not_252_out, F12);
  not not_253 (not_253_out, OP3);
  not not_254 (not_254_out, OP2);
  not not_255 (not_255_out, F14);
  not not_256 (not_256_out, OP6);
  not not_257 (not_257_out, OP5);
  not not_258 (not_258_out, OP3);
  not not_259 (not_259_out, OP2);
  not not_260 (not_260_out, F12);
  not not_261 (not_261_out, OP4);
  not not_262 (not_262_out, OP3);
  not not_263 (not_263_out, OP2);
  and and_1 (and_1_out, not_1_out, not_2_out, not_3_out, not_4_out, not_5_out, not_6_out, OP5, OP4, not_7_out, not_8_out);
  and and_2 (and_2_out, not_9_out, not_10_out, F14, F13, F12, not_11_out, OP5, OP4, not_12_out, not_13_out);
  and and_3 (and_3_out, not_14_out, not_15_out, not_16_out, F13, not_17_out, not_18_out, OP5, OP4, not_19_out, not_20_out);
  and and_4 (and_4_out, not_21_out, not_22_out, not_23_out, not_24_out, not_25_out, OP4, not_26_out, not_27_out);
  and and_5 (and_5_out, F14, F13, F12, not_28_out, not_29_out, OP4, not_30_out, not_31_out);
  and and_6 (and_6_out, F14, not_32_out, not_33_out, not_34_out, not_35_out, OP4, not_36_out, not_37_out);
  and and_7 (and_7_out, not_38_out, F13, not_39_out, not_40_out, not_41_out, OP4, not_42_out, not_43_out);
  and and_8 (and_8_out, F30, not_44_out, F14, not_45_out, F12, not_46_out, not_47_out, OP4, not_48_out, not_49_out);
  and and_9 (and_9_out, not_50_out, F13, not_51_out, not_52_out, not_53_out, not_54_out, not_55_out, not_56_out);
  and and_10 (and_10_out, not_57_out, F13, not_58_out, not_59_out, OP5, not_60_out, not_61_out, not_62_out);
  and and_11 (and_11_out, F14, F13, F12, OP6, OP5, OP4, not_63_out, not_64_out);
  and and_12 (and_12_out, not_65_out, not_66_out, OP4, not_67_out, OP2);
  and and_13 (and_13_out, not_68_out, not_69_out, F12, not_70_out, not_71_out, not_72_out, not_73_out, not_74_out);
  and and_14 (and_14_out, F30, not_75_out, not_76_out, not_77_out, not_78_out, not_79_out, OP5, OP4, not_80_out, not_81_out);
  and and_15 (and_15_out, not_82_out, not_83_out, F14, F13, F12, not_84_out, OP5, OP4, not_85_out, not_86_out);
  and and_16 (and_16_out, not_87_out, not_88_out, not_89_out, F13, not_90_out, not_91_out, OP5, OP4, not_92_out, not_93_out);
  and and_17 (and_17_out, F14, F13, F12, not_94_out, not_95_out, OP4, not_96_out, not_97_out);
  and and_18 (and_18_out, not_98_out, F13, not_99_out, not_100_out, not_101_out, OP4, not_102_out, not_103_out);
  and and_19 (and_19_out, not_104_out, not_105_out, F14, not_106_out, F12, not_107_out, not_108_out, OP4, not_109_out, not_110_out);
  and and_20 (and_20_out, not_111_out, not_112_out, not_113_out, OP6, OP5, not_114_out, not_115_out, not_116_out);
  and and_21 (and_21_out, not_117_out, not_118_out, F12, OP6, OP5, not_119_out, not_120_out, not_121_out);
  and and_22 (and_22_out, not_122_out, not_123_out, not_124_out, OP6, OP5, not_125_out, not_126_out, OP2);
  and and_23 (and_23_out, F14, F13, F12, OP6, OP5, OP4, not_127_out, not_128_out);
  and and_24 (and_24_out, not_129_out, not_130_out, not_131_out, not_132_out, not_133_out, not_134_out, OP5, OP4, not_135_out, not_136_out);
  and and_25 (and_25_out, F30, not_137_out, not_138_out, not_139_out, not_140_out, not_141_out, OP5, OP4, not_142_out, not_143_out);
  and and_26 (and_26_out, not_144_out, not_145_out, F14, F13, F12, not_146_out, OP5, OP4, not_147_out, not_148_out);
  and and_27 (and_27_out, not_149_out, not_150_out, not_151_out, F13, F12, not_152_out, OP5, OP4, not_153_out, not_154_out);
  and and_28 (and_28_out, not_155_out, not_156_out, not_157_out, not_158_out, not_159_out, OP4, not_160_out, not_161_out);
  and and_29 (and_29_out, F14, F13, F12, not_162_out, not_163_out, OP4, not_164_out, not_165_out);
  and and_30 (and_30_out, not_166_out, F13, not_167_out, not_168_out, not_169_out, not_170_out, not_171_out, not_172_out);
  and and_31 (and_31_out, not_173_out, F13, not_174_out, not_175_out, OP5, not_176_out, not_177_out, not_178_out);
  and and_32 (and_32_out, not_179_out, not_180_out, not_181_out, OP6, OP5, not_182_out, not_183_out, not_184_out);
  and and_33 (and_33_out, not_185_out, not_186_out, F12, OP6, OP5, not_187_out, not_188_out, not_189_out);
  and and_34 (and_34_out, not_190_out, not_191_out, not_192_out, OP6, OP5, not_193_out, not_194_out, OP2);
  and and_35 (and_35_out, F14, F13, F12, OP6, OP5, OP4, not_195_out, not_196_out);
  and and_36 (and_36_out, not_197_out, not_198_out, OP4, not_199_out, OP2);
  and and_37 (and_37_out, not_200_out, F13, F12, not_201_out, not_202_out, OP4, not_203_out, not_204_out);
  and and_38 (and_38_out, not_205_out, not_206_out, F12, not_207_out, not_208_out, not_209_out, not_210_out, not_211_out);
  and and_39 (and_39_out, F14, F13, not_212_out, OP6, OP5, not_213_out, not_214_out, not_215_out);
  and and_40 (and_40_out, not_216_out, not_217_out, F14, F13, not_218_out, not_219_out, OP5, OP4, not_220_out, not_221_out);
  and and_41 (and_41_out, not_222_out, not_223_out, not_224_out, F13, not_225_out, not_226_out, OP5, OP4, not_227_out, not_228_out);
  and and_42 (and_42_out, not_229_out, not_230_out, not_231_out, F13, F12, not_232_out, OP5, OP4, not_233_out, not_234_out);
  and and_43 (and_43_out, F14, F13, not_235_out, not_236_out, not_237_out, OP4, not_238_out, not_239_out);
  and and_44 (and_44_out, F14, not_240_out, not_241_out, not_242_out, not_243_out, OP4, not_244_out, not_245_out);
  and and_45 (and_45_out, not_246_out, F13, not_247_out, not_248_out, not_249_out, OP4, not_250_out, not_251_out);
  and and_46 (and_46_out, F14, F13, not_252_out, OP6, OP5, OP4, not_253_out, not_254_out);
  and and_47 (and_47_out, not_255_out, F13, F12, not_256_out, not_257_out, OP4, not_258_out, not_259_out);
  and and_48 (and_48_out, F14, F13, not_260_out, OP6, OP5, not_261_out, not_262_out, not_263_out);
  or or_1 (S0, and_1_out, and_2_out, and_3_out, and_4_out, and_5_out, and_6_out, and_7_out, and_8_out, and_9_out, and_10_out, and_11_out, and_12_out, and_13_out);
  or or_2 (S1, and_14_out, and_15_out, and_16_out, and_17_out, and_18_out, and_19_out, and_20_out, and_21_out, and_22_out, and_23_out);
  or or_3 (S2, and_24_out, and_25_out, and_26_out, and_27_out, and_28_out, and_29_out, and_30_out, and_31_out, and_32_out, and_33_out, and_34_out, and_35_out, and_36_out, and_37_out, and_38_out, and_39_out);
  or or_4 (S3, and_40_out, and_41_out, and_42_out, and_43_out, and_44_out, and_45_out, and_46_out, and_47_out, and_48_out);
endmodule

// ALU
module ALU (
  input  [31:0] X,
  input  [31:0] Y,
  input  [3:0] AluOP,
  output out_4,
  output Equal,
  output out_6,
  output [31:0] Result,
  output [31:0] Result_2
);

  wire [0:0] comparator_1_lt, comparator_2_lt;
  wire [31:0] adder_1_out, AND_out, divider_1_out, divider_1_rem, multiplier_1_cout, multiplier_1_out,
       NOR_out, OR_out, shifter_1_out, shifter_2_out, shifter_3_out, subtractor_1_out, XOR_out;

  assign AND_out = X & Y;  // AND_Gate AND, 32 bits wide
  assign OR_out = X | Y;  // OR_Gate OR, 32 bits wide
  Shifter #(.width(32), .shift("ll")) shifter_1 (.in(X), .\dist (Y[4:0]), .out(shifter_1_out));
  Shifter #(.width(32), .shift("ar")) shifter_2 (.in(X), .\dist (Y[4:0]), .out(shifter_2_out));
  Shifter #(.width(32), .shift("lr")) shifter_3 (.in(X), .\dist (Y[4:0]), .out(shifter_3_out));
  Multiplier #(.width(32)) multiplier_1 (.a(X), .b(Y), .out(multiplier_1_out), .cout(multiplier_1_cout));  // open: cin
  Divider #(.width(32)) divider_1 (.a(X), .b(Y), .out(divider_1_out), .rem(divider_1_rem));  // open: upper
  Adder #(.width(32)) adder_1 (.a(X), .b(Y), .out(adder_1_out));  // open: cin, cout
  Subtractor #(.width(32)) subtractor_1 (.a(X), .b(Y), .out(subtractor_1_out));  // open: bin, bout
  assign XOR_out = X ^ Y;  // XOR_Gate XOR, 32 bits wide
  assign NOR_out = ~(X | Y);  // NOR_Gate NOR, 32 bits wide
  Comparator #(.width(32), .mode("twosComplement")) comparator_1 (
    .a(X), .b(Y), .eq(Equal), .lt(comparator_1_lt[0]));  // open: gt
  Comparator #(.width(32), .mode("unsigned")) comparator_2 (.a(X), .b(Y), .lt(comparator_2_lt[0]));  // open: gt, eq
  Multiplexer #(.select(4), .width(32), .disabled("Z"), .enable("false")) multiplexer_1 (
    .in0(shifter_1_out), .in1(shifter_2_out), .in2(shifter_3_out), .in3(multiplier_1_out),
    .in4(divider_1_out), .in5(adder_1_out), .in6(subtractor_1_out), .in7(AND_out), .in8(OR_out),
    .in9(XOR_out), .in10(NOR_out), .in11({{31{1'b0}}, comparator_1_lt[0]}),
    .in12({{31{1'b0}}, comparator_2_lt[0]}), .in13({32{1'b0}}), .in14({32{1'b0}}), .in15({32{1'b0}}),
    .out(Result), .sel(AluOP));
  Multiplexer #(.select(4), .width(32), .disabled("Z"), .enable("false")) multiplexer_2 (
    .in0({32{1'b0}}), .in1({32{1'b0}}), .in2({32{1'b0}}), .in3(multiplier_1_cout), .in4(divider_1_rem),
    .in5({32{1'b0}}), .in6({32{1'b0}}), .in7({32{1'b0}}), .in8({32{1'b0}}), .in9({32{1'b0}}),
    .in10({32{1'b0}}), .in11({32{1'b0}}), .in12({32{1'b0}}), .in13({32{1'b0}}), .in14({32{1'b0}}),
    .in15({32{1'b0}}), .out(Result_2), .sel(AluOP));
  Multiplexer #(.select(4), .width(1), .disabled("Z"), .enable("false")) multiplexer_3 (
    .in0(1'b0), .in1(1'b0), .in2(1'b0), .in3(1'b0), .in4(1'b0), .in5(1'b0), .in6(1'b0), .in7(1'b0),
    .in8(1'b0), .in9(1'b0), .in10(1'b0), .in11(comparator_1_lt[0]), .in12(comparator_2_lt[0]), .in13(1'b0),
    .in14(1'b0), .in15(1'b0), .out(out_6), .sel(AluOP));
  not not_1 (out_4, out_6);

  // Other names for the same wires on the sheet: Result2[31:0] = Result_2; S[3:0] = AluOP; tunnel = out_6;
  //   tunnel_t = out_4

  // Notes on the sheet:
  //   不要改变此引脚区域内容，也不要改变ALU封装形式
  //   输入引脚
  //   输出引脚
endmodule

module Regifile (
  input  [31:0] Din,
  input  Clk,
  input  WE,
  input  [4:0] R1_num,
  input  [4:0] W_num,
  input  [4:0] R2_num,
  output [31:0] R1,
  output [31:0] R2
);

  // RegisterFile registerfile_1: pin names not known; wires that end beside it: Din, Clk, WE, W_num, R1_num, R2_num, R1, R2
endmodule

module \理想流水线  (
  output RegWrite,
  output MemWrite,
  output [31:0] IF_PC,
  output [31:0] ID_PC,
  output [31:0] EX_PC,
  output [31:0] M_PC,
  output [31:0] WB_PC,
  output [31:0] RDin,
  output [31:0] MDin,
  output [31:0] LedData
);

  wire and_1_out, and_2_out, and_3_out, and_5_out, CLK, clock_1_out, clock_2_out, comparator_1_eq,
       comparator_1_lt, comparator_2_eq, d_ff_1_q, ecall, Equ, EX_ecall, EX_halt, ex_mem_1_halt_2,
       ex_mem_1_jal_2, ex_mem_1_jalr_2, ex_mem_1_memtoreg_2, ex_mem_1_regwrite_2, ex_mem_1_u_type_2, Go,
       halt, id_ex_1_alusrc_2, id_ex_1_beq_2, id_ex_1_bltu_2, id_ex_1_bne_2, id_ex_1_jal_2, id_ex_1_lb_2,
       id_ex_1_memtoreg_2, id_ex_1_memwrite_2, id_ex_1_regwrite_2, id_ex_1_u_type_2, IR1, IR2, IR3, JAL, LB,
       Less, mem_wb_1_halt_2, mem_wb_1_jal_2, mem_wb_1_jalr_2, mem_wb_1_memtoreg_2, mem_wb_1_u_type_2,
       nand_1_out, not_1_out, not_2_out, or_1_out, or_2_out, RST, S_type, W1, W2, W3, \单周期硬布线控制器_1_alu_src ,
       \单周期硬布线控制器_1_beq , \单周期硬布线控制器_1_bltu , \单周期硬布线控制器_1_bne , \单周期硬布线控制器_1_jalr , \单周期硬布线控制器_1_lb ,
       \单周期硬布线控制器_1_memtoreg , \单周期硬布线控制器_1_memwrite , \单周期硬布线控制器_1_regwrite , \单周期硬布线控制器_1_u_type ,
       \单周期硬布线控制器_1_uret ;
  wire [1:0] id_ex_1_jalr_2, id_ex_1_rs1_forward_2, id_ex_1_rs2_forward_2, or_5_out;
  wire [3:0] id_ex_1_aluop_2, \单周期硬布线控制器_1_alu_op ;
  wire [4:0] ex_mem_1_rd_2, id_ex_1_rd_2, multiplexer_2_out, multiplexer_3_out, WB_rd;
  wire [7:0] multiplexer_9_out;
  wire [12:0] CNT_num;
  wire [15:0] \LoadUse次数 , \总周期数 , \插入气泡数 , \无条件分支数 , \条件分支成功数 ;
  wire [31:0] adder_2_out, ALU_addr, ALUResult, bit_extender_1_out, bit_extender_2_out, bit_extender_3_out,
       bit_extender_4_out, bit_extender_5_out, bit_extender_6_out, EX_IR, ex_mem_1_auipc_result_2,
       ex_mem_1_pc_4_2, id_ex_1_auipc_result_2, id_ex_1_imm_1_2, id_ex_1_imm_2_2, id_ex_1_pc_4_2,
       id_ex_1_r1_2, id_ex_1_r2_2, ID_IR, if_id_1_pc_4_2, IF_IR, jumpAddr, MEM_ALURes, MEM_IR,
       mem_wb_1_aluresult_2, mem_wb_1_auipc_result_2, mem_wb_1_pc_4_2, mem_wb_1_readdata_2, MemData,
       multiplexer_1_out, multiplexer_4_out, multiplexer_5_out, multiplexer_6_out, multiplexer_7_out,
       multiplexer_8_out, multiplexer_10_out, PC, PC_4, regifile_1_r1, regifile_1_r2, shifter_1_out,
       shifter_2_out, WB_IR;

  Button \u_总复位  (.out(RST));
  Button _1 (.out(IR1));
  Button _2 (.out(IR2));
  Button _3 (.out(IR3));
  // Probe on \总周期数 
  // Probe on \总周期数 
  Button \u_继续运行  (.out(Go));
  LED #(.active("true")) led_1 (.in(W1));
  LED #(.active("true")) led_2 (.in(W2));
  LED #(.active("true")) led_3 (.in(W3));
  Hex_Digit_Display hex_digit_display_1 (.value(LedData[31:28]));  // open: dp
  // Probe on IF_PC[19:0]
  // RiscV_Probe riscv_probe_1: pin names not known; wires that end beside it: IF_IR
  Register #(.width(32), .trigger("rising"), .Select("low")) u_PC (
    .D(multiplexer_1_out), .en(or_1_out), .Q(IF_PC), .clk(CLK), .clr(RST));
  Multiplexer #(.select(2), .width(32), .disabled("Z"), .enable("false")) multiplexer_1 (
    .in0(PC_4), .in1(ALUResult), .in2(jumpAddr), .out(multiplexer_1_out), .sel(id_ex_1_jalr_2));  // open: in3
  or or_1 (or_1_out, ~halt, Go);  // OR_Gate
  Hex_Digit_Display hex_digit_display_2 (.value(LedData[23:20]));  // open: dp
  Hex_Digit_Display hex_digit_display_3 (.value(LedData[27:24]));  // open: dp
  // Probe on ID_PC[19:0]
  // RiscV_Probe riscv_probe_2: pin names not known; wires that end beside it: ID_IR
  Hex_Digit_Display hex_digit_display_4 (.value(LedData[15:12]));  // open: dp
  Hex_Digit_Display hex_digit_display_5 (.value(LedData[19:16]));  // open: dp
  not not_1 (not_1_out, halt);
  Counter #(.width(16), .max('hffff), .ongoal("wrap"), .trigger("rising"), .behavior("new")) counter_1 (
    .count(not_1_out), .Q(\总周期数 ), .clk(CLK), .clr(RST));  // open: load, D, carry, preset, down
  Adder #(.width(32)) adder_1 (.a(IF_PC), .b(32'h4), .out(PC_4));  // open: cin, cout
  // RiscV_Probe riscv_probe_3: pin names not known; wires that end beside it: IF_IR
  Hex_Digit_Display hex_digit_display_6 (.value(LedData[11:8]));  // open: dp
  Hex_Digit_Display hex_digit_display_7 (.value(LedData[7:4]));  // open: dp
  Clock #(.highDuration(1), .lowDuration(1)) clock_1 (.out(clock_1_out));
  // Probe on EX_PC[19:0]
  // RiscV_Probe riscv_probe_4: pin names not known; wires that end beside it: clock_1_out, EX_IR, CLK
  or or_2 (or_2_out, id_ex_1_jalr_2[1], id_ex_1_jalr_2[0]);
  ROM #(.addrWidth(10), .dataWidth(32), .Select("high")) rom_1 (.addr(IF_PC[11:2]), .data(IF_IR));
  Hex_Digit_Display hex_digit_display_8 (.value(LedData[3:0]));  // open: dp
  IF_ID if_id_1 (
    .IR(IF_IR), .PC(IF_PC), .PC_4(PC_4), .IR_2(ID_IR), .PC_2(ID_PC), .PC_4_2(if_id_1_pc_4_2),
    .branch(or_2_out), .reset(RST), .en(1'b1), .clk(CLK));  // open: ID_PredictJump, IF_PredictJump
  // Probe on \总周期数 
  // Probe on M_PC[19:0]
  // RiscV_Probe riscv_probe_5: pin names not known; wires that end beside it: MEM_IR
  \单周期硬布线控制器  \u_单周期硬布线控制器_1  (
    .Funct({ID_IR[30], ID_IR[25], ID_IR[14:12]}), .OP(ID_IR[6:2]), .ALU_OP(\单周期硬布线控制器_1_alu_op ),
    .MemToReg(\单周期硬布线控制器_1_memtoreg ), .MemWrite(\单周期硬布线控制器_1_memwrite ), .ALU_SRC(\单周期硬布线控制器_1_alu_src ),
    .RegWrite(\单周期硬布线控制器_1_regwrite ), .ecall(ecall), .S_type(S_type), .JALR(\单周期硬布线控制器_1_jalr ),
    .BEQ(\单周期硬布线控制器_1_beq ), .JAL(JAL), .BNE(\单周期硬布线控制器_1_bne ), .in_3(ID_IR[21]), .uret(\单周期硬布线控制器_1_uret ),
    .BLTU(\单周期硬布线控制器_1_bltu ), .LB(\单周期硬布线控制器_1_lb ), .U_Type(\单周期硬布线控制器_1_u_type ));  // open: rs1_used, rs2_used, CSR, SLTIU
  Multiplexer #(.select(1), .width(5), .disabled("Z"), .enable("false")) multiplexer_2 (
    .in0(ID_IR[19:15]), .in1(5'b10001), .out(multiplexer_2_out), .sel(ecall));
  Multiplexer #(.select(1), .width(5), .disabled("Z"), .enable("false")) multiplexer_3 (
    .in0(ID_IR[24:20]), .in1(5'b01010), .out(multiplexer_3_out), .sel(ecall));
  assign bit_extender_1_out = {{12{ID_IR[31]}}, ID_IR[31:12]};  // Bit_Extender bit_extender_1
  // Probe on \总周期数 
  // Probe on \无条件分支数 
  // Probe on \条件分支成功数 
  // Probe on \插入气泡数 
  // Probe on \LoadUse次数 
  // Probe on multiplexer_2_out
  // Probe on multiplexer_3_out
  assign bit_extender_2_out = {{20{ID_IR[31]}}, ID_IR[31:20]};  // Bit_Extender bit_extender_2
  assign bit_extender_3_out = {{20{ID_IR[31]}}, {ID_IR[31:25], ID_IR[11:7]}};  // Bit_Extender bit_extender_3
  assign bit_extender_4_out = {{20{ID_IR[31]}}, {ID_IR[31], ID_IR[7], ID_IR[30:25], ID_IR[11:8]}};  // Bit_Extender bit_extender_4
  assign bit_extender_5_out = {{12{ID_IR[31]}}, {ID_IR[31], ID_IR[19:12], ID_IR[20], ID_IR[30:21]}};  // Bit_Extender bit_extender_5
  Shifter #(.width(32), .shift("ll")) shifter_1 (.in(bit_extender_1_out), .\dist (5'b01100), .out(shifter_1_out));
  // Probe on IF_PC[11:0]
  // Probe on WB_PC[19:0]
  // RiscV_Probe riscv_probe_6: pin names not known; wires that end beside it: WB_IR
  Regifile regifile_1 (
    .Din(RDin), .Clk(CLK), .R1(regifile_1_r1), .R2(regifile_1_r2), .WE(RegWrite), .W_num(WB_rd),
    .R1_num(multiplexer_2_out), .R2_num(multiplexer_3_out));
  Multiplexer #(.select(1), .width(32), .disabled("Z"), .enable("false")) multiplexer_4 (
    .in0(bit_extender_2_out), .in1(bit_extender_3_out), .out(multiplexer_4_out), .sel(S_type));
  Multiplexer #(.select(1), .width(32), .disabled("Z"), .enable("false")) multiplexer_5 (
    .in0(bit_extender_4_out), .in1(bit_extender_5_out), .out(multiplexer_5_out), .sel(JAL));
  Adder #(.width(32)) adder_2 (.a(shifter_1_out), .b(PC), .out(adder_2_out));  // open: cin, cout
  // Probe on EX_PC[11:0]
  // Probe on ID_PC[11:0]
  // Probe on M_PC[11:0]
  D_Flip_Flop #(.trigger("high"), .Pre_Clr_Positions("LEGACY"), .NegatePresetClear("false"), .enable("true"), .NewFFLayout("false")) d_ff_1 (.Q(d_ff_1_q));  // open: clk, D, Qn, preset, en, reset
  // Probe on 13'h3
  ID_EX id_ex_1 (
    .BEQ(\单周期硬布线控制器_1_beq ), .BNE(\单周期硬布线控制器_1_bne ), .MemToReg(\单周期硬布线控制器_1_memtoreg ),
    .MemWrite(\单周期硬布线控制器_1_memwrite ), .AluSrc(\单周期硬布线控制器_1_alu_src ), .RegWrite(\单周期硬布线控制器_1_regwrite ),
    .S_type(S_type), .ecall(ecall), .Jal(JAL), .Jalr(\单周期硬布线控制器_1_jalr ), .LB(\单周期硬布线控制器_1_lb ),
    .BLTU(\单周期硬布线控制器_1_bltu ), .Uret(\单周期硬布线控制器_1_uret ), .AluOP(\单周期硬布线控制器_1_alu_op ), .rd(ID_IR[11:7]),
    .R1(regifile_1_r1), .R2(regifile_1_r2), .imm_1(multiplexer_4_out), .imm_2(multiplexer_5_out), .PC(ID_PC),
    .PC_4(if_id_1_pc_4_2), .IR(ID_IR), .BEQ_2(id_ex_1_beq_2), .BNE_2(id_ex_1_bne_2),
    .MemToReg_2(id_ex_1_memtoreg_2), .MemWrite_2(id_ex_1_memwrite_2), .AluSrc_2(id_ex_1_alusrc_2),
    .RegWrite_2(id_ex_1_regwrite_2), .ecall_2(EX_ecall), .Jal_2(id_ex_1_jal_2), .Jalr_2(id_ex_1_jalr_2[0]),
    .LB_2(id_ex_1_lb_2), .BLTU_2(id_ex_1_bltu_2), .AluOP_2(id_ex_1_aluop_2), .rd_2(id_ex_1_rd_2),
    .R1_2(id_ex_1_r1_2), .R2_2(id_ex_1_r2_2), .imm_1_2(id_ex_1_imm_1_2), .imm_2_2(id_ex_1_imm_2_2),
    .PC_2(EX_PC), .PC_4_2(id_ex_1_pc_4_2), .IR_2(EX_IR), .RS1_Forward_2(id_ex_1_rs1_forward_2),
    .RS2_Forward_2(id_ex_1_rs2_forward_2), .reset(RST), .flush(1'b0), .en(1'b1), .clk(CLK),
    .U_Type(\单周期硬布线控制器_1_u_type ), .U_Type_2(id_ex_1_u_type_2), .AUIPC_result(adder_2_out),
    .AUIPC_result_2(id_ex_1_auipc_result_2));  // open: RS1_Forward, RS2_Forward, S_type_2, Uret_2, ID_PredictJump, EX_PredictJump, SLTIU, SLTIU_2
  // Probe on WB_PC[11:0]
  Comparator #(.width(13), .mode("twosComplement")) comparator_1 (
    .a(CNT_num), .b(13'h3), .eq(comparator_1_eq), .lt(comparator_1_lt));  // open: gt
  Clock #(.highDuration(1), .lowDuration(1)) clock_2 (.out(clock_2_out));
  Multiplexer #(.select(2), .width(32), .disabled("Z"), .enable("false")) multiplexer_6 (
    .in0(id_ex_1_r1_2), .in1(RDin), .in2(MEM_ALURes), .out(multiplexer_6_out), .sel(id_ex_1_rs1_forward_2));  // open: in3
  nand nand_1 (nand_1_out, d_ff_1_q, comparator_1_eq);
  Counter #(.width(13), .max('h1fff), .ongoal("stay"), .trigger("rising"), .behavior("old")) counter_2 (
    .count(comparator_1_lt), .Q(CNT_num), .clk(clock_2_out));  // open: load, D, carry, clr, preset
  Multiplexer #(.select(2), .width(32), .disabled("Z"), .enable("false")) multiplexer_7 (
    .in0(id_ex_1_r2_2), .in1(RDin), .in2(MEM_ALURes), .out(multiplexer_7_out), .sel(id_ex_1_rs2_forward_2));  // open: in3
  assign CLK = nand_1_out ? clock_2_out : 1'bz;  // Controlled_Buffer controlled_buffer_1
  or or_3 (id_ex_1_jalr_2[1], id_ex_1_jal_2, and_1_out, and_2_out, and_3_out);
  and and_1 (and_1_out, id_ex_1_bne_2, ~Equ);  // AND_Gate
  and and_2 (and_2_out, Equ, id_ex_1_beq_2);
  Multiplexer #(.select(1), .width(32), .disabled("Z"), .enable("false")) multiplexer_8 (
    .in0(multiplexer_7_out), .in1(id_ex_1_imm_1_2), .out(multiplexer_8_out), .sel(id_ex_1_alusrc_2));
  Pull_Resistor #(.pull(1)) pull_resistor_1 (.node(CLK));
  and and_3 (and_3_out, id_ex_1_bltu_2, Less);
  Shifter #(.width(32), .shift("ll")) shifter_2 (.in(id_ex_1_imm_2_2), .\dist (5'b00001), .out(shifter_2_out));
  Comparator #(.width(32), .mode("twosComplement")) comparator_2 (
    .a(multiplexer_6_out), .b(32'h22), .eq(comparator_2_eq));  // open: gt, lt
  not not_2 (not_2_out, comparator_2_eq);
  ALU alu_1 (
    .X(multiplexer_6_out), .Y(multiplexer_8_out), .AluOP(id_ex_1_aluop_2), .Equal(Equ), .Result(ALU_addr),
    .out_6(Less));  // open: Result_2, out_4
  and and_4 (EX_halt, not_2_out, EX_ecall);
  and and_5 (and_5_out, comparator_2_eq, EX_ecall);
  Adder #(.width(32)) adder_3 (.a(shifter_2_out), .b(EX_PC), .out(jumpAddr));  // open: cin, cout
  Register #(.width(32), .trigger("rising"), .Select("low")) register_1 (
    .D(multiplexer_7_out), .en(and_5_out), .Q(LedData), .clk(CLK), .clr(RST));
  EX_MEM ex_mem_1 (
    .Jal(id_ex_1_jal_2), .Jalr(id_ex_1_jalr_2[0]), .MemToReg(id_ex_1_memtoreg_2),
    .MemWrite(id_ex_1_memwrite_2), .LB(id_ex_1_lb_2), .RegWrite(id_ex_1_regwrite_2), .halt(EX_halt),
    .rd(id_ex_1_rd_2), .Result(ALU_addr), .WriteData(multiplexer_7_out), .IR(EX_IR), .PC(EX_PC),
    .PC_4(id_ex_1_pc_4_2), .Jal_2(ex_mem_1_jal_2), .Jalr_2(ex_mem_1_jalr_2),
    .MemToReg_2(ex_mem_1_memtoreg_2), .MemWrite_2(MemWrite), .LB_2(LB), .RegWrite_2(ex_mem_1_regwrite_2),
    .halt_2(ex_mem_1_halt_2), .rd_2(ex_mem_1_rd_2), .Result_2(MEM_ALURes), .WriteData_2(MDin), .IR_2(MEM_IR),
    .PC_2(M_PC), .PC_4_2(ex_mem_1_pc_4_2), .reset(RST), .en(1'b1), .clk(CLK), .U_Type(id_ex_1_u_type_2),
    .U_Type_2(ex_mem_1_u_type_2), .AUIPC_result(id_ex_1_auipc_result_2),
    .AUIPC_result_2(ex_mem_1_auipc_result_2));  // open: SLTIU, SLTIU_2, LESS, LESS_2
  RAM #(.addrWidth(10), .dataWidth(32), .bus("separate"), .Select("high")) ram_1 (
    .addr(MEM_ALURes[11:2]), .din(MDin), .data(MemData), .str(MemWrite), .sel(1'b1), .clk(CLK), .ld(1'b1),
    .clr(RST));
  Multiplexer #(.select(2), .width(8), .disabled("Z"), .enable("false")) multiplexer_9 (
    .in0(MemData[7:0]), .in1(MemData[15:8]), .in2(MemData[23:16]), .in3(MemData[31:24]),
    .out(multiplexer_9_out), .sel(MEM_ALURes[1:0]));
  assign bit_extender_6_out = {{24{multiplexer_9_out[7]}}, multiplexer_9_out};  // Bit_Extender bit_extender_6
  Multiplexer #(.select(1), .width(32), .disabled("Z"), .enable("false")) multiplexer_10 (
    .in0(MemData), .in1(bit_extender_6_out), .out(multiplexer_10_out), .sel(LB));
  MEM_WB mem_wb_1 (
    .Jal(ex_mem_1_jal_2), .Jalr(ex_mem_1_jalr_2), .MemToReg(ex_mem_1_memtoreg_2),
    .RegWrite(ex_mem_1_regwrite_2), .halt(ex_mem_1_halt_2), .rd(ex_mem_1_rd_2), .ALUResult(MEM_ALURes),
    .ReadData(multiplexer_10_out), .IR(MEM_IR), .PC(M_PC), .PC_4(ex_mem_1_pc_4_2), .Jal_2(mem_wb_1_jal_2),
    .Jalr_2(mem_wb_1_jalr_2), .MemToReg_2(mem_wb_1_memtoreg_2), .RegWrite_2(RegWrite),
    .halt_2(mem_wb_1_halt_2), .rd_2(WB_rd), .ALUResult_2(mem_wb_1_aluresult_2),
    .ReadData_2(mem_wb_1_readdata_2), .IR_2(WB_IR), .PC_2(WB_PC), .PC_4_2(mem_wb_1_pc_4_2), .reset(RST),
    .en(1'b1), .clk(CLK), .U_Type(ex_mem_1_u_type_2), .U_Type_2(mem_wb_1_u_type_2),
    .AUIPC_result(ex_mem_1_auipc_result_2), .AUIPC_result_2(mem_wb_1_auipc_result_2));  // open: SLTIU, SLTIU_2, LESS, LESS_2
  or or_4 (or_5_out[1], mem_wb_1_jalr_2, mem_wb_1_jal_2, mem_wb_1_u_type_2);
  or or_5 (or_5_out[0], mem_wb_1_u_type_2, mem_wb_1_memtoreg_2);
  D_Flip_Flop #(.trigger("rising"), .Pre_Clr_Positions("ABOVE_BELOW"), .NegatePresetClear("false"), .enable("true"), .NewFFLayout("true")) d_ff_2 (
    .clk(mem_wb_1_halt_2), .D(1'b1), .Q(halt), .en(1'b1), .reset(Go));  // open: Qn, preset
  Multiplexer #(.select(2), .width(32), .disabled("Z"), .enable("false")) multiplexer_11 (
    .in0(mem_wb_1_aluresult_2), .in1(mem_wb_1_readdata_2), .in2(mem_wb_1_pc_4_2),
    .in3(mem_wb_1_auipc_result_2), .out(RDin), .sel(or_5_out));

  // Other names for the same wires on the sheet: IR[31:0] = ID_IR; MEM_PC[31:0] = M_PC; WB_RegWrite = RegWrite

  // Notes on the sheet:
  //   中断源
  //   时空图监测，可删除
  //   中断等待指示
  //   数码管输出
  //   指令存储器
  //   指令探针
  //   contents of rom_1 (hex, n*v repeats v):
  //   413 493 913 993 46413 14e493 296913 39e993 842023 942223 1242423 1342623 a00893 493 913 993 73
  //   指令字
  //   J
  //   U_Type
  //   Beq
  //   Bne
  //   I
  //   S
  //   B
  //   Uret
  //   LB
  //   JALR
  //   BLTU
  //   JAL
  //   MemToReg
  //   MemWrite
  //   AluOP
  //   AluSrc
  //   RegWrite
  //   U_Type
  //   S_type
  //   控制位
  //   ecall
  //   imm_1
  //   imm_2
  //   rd
  //   IR
  //   PC
  //   PC+4
  //   流水调试日志用
  //   暂停节拍，不能为0
  //   戳工具置1进入计数暂停模式，ctrl+k时钟自动运行到对应节拍暂停
  //   ctrl+k关闭时钟连续运行，将控制位置零，进入单步调试模式调试
  //   用这个时钟源需要去掉电路中的其他时钟源
  //   可计数暂停的时钟源
  //   U_type
  //   为方便自动评测，需要输出流水线各段保存的PC值，注意是PC不是PC+4，另外ID段寄存器写入信息，Mem段内存写入信息也要输出
  //   LB
  //   JALR
  //   JAL
  //   MemToReg
  //   MemWrite
  //   RegWrite
  //   rd
  //   IR
  //   PC
  //   PC+4
  //   数据存储器
  //   JALR
  //   JAL
  //   U_Type
  //   MemToReg
  //   RegWrite
  //   halt
  //   ALUResult
  //   ReadData
endmodule
module \气泡流水线  (
  output RegWrite,
  output MemWrite,
  output [31:0] IF_PC,
  output [31:0] ID_PC,
  output [31:0] EX_PC,
  output [31:0] M_PC,
  output [31:0] WB_PC,
  output [31:0] RDin,
  output [31:0] MDin,
  output [31:0] LedData
);

  wire and_1_out, and_2_out, and_3_out, and_4_out, and_5_out, and_7_out, and_8_out, and_9_out, and_10_out,
       and_11_out, and_12_out, BranchSuc, BranchTaken, CLK, clock_1_out, clock_2_out, comparator_1_eq,
       comparator_1_lt, comparator_2_eq, d_ff_1_q, ecall, Equ, EX_ecall, EX_halt, ex_mem_1_halt_2,
       ex_mem_1_jal_2, ex_mem_1_jalr_2, ex_mem_1_less_2, ex_mem_1_memtoreg_2, ex_mem_1_regwrite_2,
       ex_mem_1_sltiu_2, ex_mem_1_u_type_2, Flush, Go, halt, id_ex_1_alusrc_2, id_ex_1_beq_2, id_ex_1_bltu_2,
       id_ex_1_bne_2, id_ex_1_jal_2, id_ex_1_lb_2, id_ex_1_memtoreg_2, id_ex_1_memwrite_2,
       id_ex_1_regwrite_2, id_ex_1_sltiu_2, id_ex_1_u_type_2, IR1, IR2, IR3, JAL, LB, Less, mem_wb_1_halt_2,
       mem_wb_1_jal_2, mem_wb_1_jalr_2, mem_wb_1_less_2, mem_wb_1_memtoreg_2, mem_wb_1_sltiu_2,
       mem_wb_1_u_type_2, nand_1_out, not_1_out, not_2_out, or_1_out, or_2_out, or_3_out, or_4_out, or_9_out,
       or_10_out, RST, S_type, stall, W1, W2, W3, \单周期硬布线控制器_1_alu_src , \单周期硬布线控制器_1_beq ,
       \单周期硬布线控制器_1_bltu , \单周期硬布线控制器_1_bne , \单周期硬布线控制器_1_jalr , \单周期硬布线控制器_1_lb , \单周期硬布线控制器_1_memtoreg ,
       \单周期硬布线控制器_1_memwrite , \单周期硬布线控制器_1_regwrite , \单周期硬布线控制器_1_rs1_used , \单周期硬布线控制器_1_rs2_used ,
       \单周期硬布线控制器_1_sltiu , \单周期硬布线控制器_1_u_type , \单周期硬布线控制器_1_uret , \无条件跳转 ;
  wire [1:0] id_ex_1_jalr_2, or_11_out;
  wire [3:0] id_ex_1_aluop_2, \单周期硬布线控制器_1_alu_op ;
  wire [4:0] ex_mem_1_rd_2, id_ex_1_rd_2, multiplexer_2_out, multiplexer_3_out, WB_rd;
  wire [12:0] CNT_num;
  wire [15:0] \LoadUse次数 , multiplexer_7_out, \总周期数 , \插入气泡数 , \无条件分支数 , \条件分支成功数 ;
  wire [31:0] adder_2_out, ALU_addr, bit_extender_1_out, bit_extender_2_out, bit_extender_3_out,
       bit_extender_4_out, bit_extender_5_out, bit_extender_6_out, bit_extender_7_out, EX_IR,
       ex_mem_1_auipc_result_2, ex_mem_1_pc_4_2, id_ex_1_auipc_result_2, id_ex_1_imm_1_2, id_ex_1_imm_2_2,
       id_ex_1_pc_4_2, id_ex_1_r1_2, id_ex_1_r2_2, ID_IR, if_id_1_pc_4_2, IF_IR, jumpAddr, MEM_ALURes,
       MEM_IR, mem_wb_1_aluresult_2, mem_wb_1_auipc_result_2, mem_wb_1_pc_4_2, mem_wb_1_readdata_2, MemData,
       multiplexer_1_out, multiplexer_4_out, multiplexer_5_out, multiplexer_6_out, multiplexer_8_out,
       multiplexer_9_out, PC_4, regifile_1_r1, regifile_1_r2, shifter_1_out, shifter_2_out, WB_IR;

  Button \u_总复位  (.out(RST));
  Button _1 (.out(IR1));
  Button _2 (.out(IR2));
  Button _3 (.out(IR3));
  // Probe on \总周期数 
  // Probe on \总周期数 
  \气泡处理逻辑  \u_气泡处理逻辑_1  (
    .IR(ID_IR), .BranchTaken(BranchTaken), .Ecall(ecall), .RS1_used(\单周期硬布线控制器_1_rs1_used ),
    .RS2_used(\单周期硬布线控制器_1_rs2_used ), .EX_RegWrite(id_ex_1_regwrite_2), .MEM_RegWrite(ex_mem_1_regwrite_2),
    .EX_rd(id_ex_1_rd_2), .MEM_rd(ex_mem_1_rd_2), .stall(stall), .flush(Flush));
  or or_1 (or_1_out, ~halt, Go);  // OR_Gate
  and and_1 (and_1_out, or_1_out, ~stall);  // AND_Gate
  Button \u_继续运行  (.out(Go));
  LED #(.active("true")) led_1 (.in(W1));
  LED #(.active("true")) led_2 (.in(W2));
  LED #(.active("true")) led_3 (.in(W3));
  Hex_Digit_Display hex_digit_display_1 (.value(LedData[31:28]));  // open: dp
  // Probe on IF_PC[19:0]
  // RiscV_Probe riscv_probe_1: pin names not known; wires that end beside it: IF_IR
  Multiplexer #(.select(2), .width(32), .disabled("Z"), .enable("false")) multiplexer_1 (
    .in0(PC_4), .in1(ALU_addr), .in2(jumpAddr), .out(multiplexer_1_out), .sel(id_ex_1_jalr_2));  // open: in3
  Hex_Digit_Display hex_digit_display_2 (.value(LedData[27:24]));  // open: dp
  Hex_Digit_Display hex_digit_display_3 (.value(LedData[23:20]));  // open: dp
  // Probe on ID_PC[19:0]
  // RiscV_Probe riscv_probe_2: pin names not known; wires that end beside it: ID_IR
  Register #(.width(32), .trigger("rising"), .Select("low")) PC (
    .D(multiplexer_1_out), .en(and_1_out), .Q(IF_PC), .clk(CLK), .clr(RST));
  Hex_Digit_Display hex_digit_display_4 (.value(LedData[15:12]));  // open: dp
  Hex_Digit_Display hex_digit_display_5 (.value(LedData[19:16]));  // open: dp
  Adder #(.width(32)) adder_1 (.a(IF_PC), .b(32'h4), .out(PC_4));  // open: cin, cout
  // RiscV_Probe riscv_probe_3: pin names not known; wires that end beside it: IF_IR
  Hex_Digit_Display hex_digit_display_6 (.value(LedData[7:4]));  // open: dp
  Hex_Digit_Display hex_digit_display_7 (.value(LedData[11:8]));  // open: dp
  Clock #(.highDuration(1), .lowDuration(1)) clock_1 (.out(clock_1_out));
  // Probe on EX_PC[19:0]
  // RiscV_Probe riscv_probe_4: pin names not known; wires that end beside it: clock_1_out, EX_IR, CLK
  ROM #(.addrWidth(10), .dataWidth(32), .Select("high")) rom_1 (.addr(IF_PC[11:2]), .data(IF_IR));
  and and_2 (and_2_out, ~stall, or_2_out);  // AND_Gate
  or or_2 (or_2_out, ~halt, Go);  // OR_Gate
  Hex_Digit_Display hex_digit_display_8 (.value(LedData[3:0]));  // open: dp
  or or_3 (or_3_out, id_ex_1_jalr_2[1], id_ex_1_jalr_2[0]);
  IF_ID if_id_1 (
    .IR(IF_IR), .PC(IF_PC), .PC_4(PC_4), .IR_2(ID_IR), .PC_2(ID_PC), .PC_4_2(if_id_1_pc_4_2),
    .branch(or_3_out), .reset(RST), .en(and_2_out), .clk(CLK));  // open: ID_PredictJump, IF_PredictJump
  // Probe on \总周期数 
  // Probe on M_PC[19:0]
  // RiscV_Probe riscv_probe_5: pin names not known; wires that end beside it: MEM_IR
  \单周期硬布线控制器  \u_单周期硬布线控制器_1  (
    .Funct({ID_IR[30], ID_IR[25], ID_IR[14:12]}), .OP(ID_IR[6:2]), .ALU_OP(\单周期硬布线控制器_1_alu_op ),
    .MemToReg(\单周期硬布线控制器_1_memtoreg ), .MemWrite(\单周期硬布线控制器_1_memwrite ), .ALU_SRC(\单周期硬布线控制器_1_alu_src ),
    .RegWrite(\单周期硬布线控制器_1_regwrite ), .ecall(ecall), .S_type(S_type), .JALR(\单周期硬布线控制器_1_jalr ),
    .BEQ(\单周期硬布线控制器_1_beq ), .JAL(JAL), .BNE(\单周期硬布线控制器_1_bne ), .in_3(ID_IR[21]), .uret(\单周期硬布线控制器_1_uret ),
    .BLTU(\单周期硬布线控制器_1_bltu ), .LB(\单周期硬布线控制器_1_lb ), .U_Type(\单周期硬布线控制器_1_u_type ),
    .rs1_used(\单周期硬布线控制器_1_rs1_used ), .rs2_used(\单周期硬布线控制器_1_rs2_used ), .SLTIU(\单周期硬布线控制器_1_sltiu ));  // open: CSR
  Multiplexer #(.select(1), .width(5), .disabled("Z"), .enable("false")) multiplexer_2 (
    .in0(ID_IR[19:15]), .in1(5'b10001), .out(multiplexer_2_out), .sel(ecall));
  Multiplexer #(.select(1), .width(5), .disabled("Z"), .enable("false")) multiplexer_3 (
    .in0(ID_IR[24:20]), .in1(5'b01010), .out(multiplexer_3_out), .sel(ecall));
  assign bit_extender_1_out = {{12{ID_IR[31]}}, ID_IR[31:12]};  // Bit_Extender bit_extender_1
  // Probe on \总周期数 
  // Probe on \无条件分支数 
  // Probe on \条件分支成功数 
  // Probe on \插入气泡数 
  // Probe on \LoadUse次数 
  // Probe on multiplexer_2_out
  // Probe on multiplexer_3_out
  assign bit_extender_2_out = {{20{ID_IR[31]}}, ID_IR[31:20]};  // Bit_Extender bit_extender_2
  assign bit_extender_3_out = {{20{ID_IR[31]}}, {ID_IR[31:25], ID_IR[11:7]}};  // Bit_Extender bit_extender_3
  assign bit_extender_4_out = {{20{ID_IR[31]}}, {ID_IR[31], ID_IR[7], ID_IR[30:25], ID_IR[11:8]}};  // Bit_Extender bit_extender_4
  assign bit_extender_5_out = {{12{ID_IR[31]}}, {ID_IR[31], ID_IR[19:12], ID_IR[20], ID_IR[30:21]}};  // Bit_Extender bit_extender_5
  Shifter #(.width(32), .shift("ll")) shifter_1 (.in(bit_extender_1_out), .\dist (5'b01100), .out(shifter_1_out));
  // Probe on IF_PC[11:0]
  // Probe on WB_PC[19:0]
  // RiscV_Probe riscv_probe_6: pin names not known; wires that end beside it: WB_IR
  not not_1 (not_1_out, CLK);
  Multiplexer #(.select(1), .width(32), .disabled("Z"), .enable("false")) multiplexer_4 (
    .in0(bit_extender_2_out), .in1(bit_extender_3_out), .out(multiplexer_4_out), .sel(S_type));
  Multiplexer #(.select(1), .width(32), .disabled("Z"), .enable("false")) multiplexer_5 (
    .in0(bit_extender_4_out), .in1(bit_extender_5_out), .out(multiplexer_5_out), .sel(JAL));
  Adder #(.width(32)) adder_2 (.a(shifter_1_out), .b(ID_PC), .out(adder_2_out));  // open: cin, cout
  // Probe on ID_PC[11:0]
  // Probe on EX_PC[11:0]
  Regifile regifile_1 (
    .Din(RDin), .Clk(not_1_out), .R1(regifile_1_r1), .R2(regifile_1_r2), .WE(RegWrite), .W_num(WB_rd),
    .R1_num(multiplexer_2_out), .R2_num(multiplexer_3_out));
  or or_4 (or_4_out, ~halt, Go);  // OR_Gate
  // Probe on adder_2_out
  // Probe on M_PC[11:0]
  D_Flip_Flop #(.trigger("high"), .Pre_Clr_Positions("LEGACY"), .NegatePresetClear("false"), .enable("true"), .NewFFLayout("false")) d_ff_1 (.Q(d_ff_1_q));  // open: clk, D, Qn, preset, en, reset
  // Probe on 13'h21
  ID_EX id_ex_1 (
    .BEQ(\单周期硬布线控制器_1_beq ), .BNE(\单周期硬布线控制器_1_bne ), .MemToReg(\单周期硬布线控制器_1_memtoreg ),
    .MemWrite(\单周期硬布线控制器_1_memwrite ), .AluSrc(\单周期硬布线控制器_1_alu_src ), .RegWrite(\单周期硬布线控制器_1_regwrite ),
    .S_type(S_type), .ecall(ecall), .Jal(JAL), .Jalr(\单周期硬布线控制器_1_jalr ), .LB(\单周期硬布线控制器_1_lb ),
    .BLTU(\单周期硬布线控制器_1_bltu ), .Uret(\单周期硬布线控制器_1_uret ), .AluOP(\单周期硬布线控制器_1_alu_op ), .rd(ID_IR[11:7]),
    .R1(regifile_1_r1), .R2(regifile_1_r2), .imm_1(multiplexer_4_out), .imm_2(multiplexer_5_out), .PC(ID_PC),
    .PC_4(if_id_1_pc_4_2), .IR(ID_IR), .BEQ_2(id_ex_1_beq_2), .BNE_2(id_ex_1_bne_2),
    .MemToReg_2(id_ex_1_memtoreg_2), .MemWrite_2(id_ex_1_memwrite_2), .AluSrc_2(id_ex_1_alusrc_2),
    .RegWrite_2(id_ex_1_regwrite_2), .ecall_2(EX_ecall), .Jal_2(id_ex_1_jal_2), .Jalr_2(id_ex_1_jalr_2[0]),
    .LB_2(id_ex_1_lb_2), .BLTU_2(id_ex_1_bltu_2), .AluOP_2(id_ex_1_aluop_2), .rd_2(id_ex_1_rd_2),
    .R1_2(id_ex_1_r1_2), .R2_2(id_ex_1_r2_2), .imm_1_2(id_ex_1_imm_1_2), .imm_2_2(id_ex_1_imm_2_2),
    .PC_2(EX_PC), .PC_4_2(id_ex_1_pc_4_2), .IR_2(EX_IR), .reset(RST), .flush(Flush), .en(or_4_out),
    .clk(CLK), .U_Type(\单周期硬布线控制器_1_u_type ), .U_Type_2(id_ex_1_u_type_2), .AUIPC_result(adder_2_out),
    .AUIPC_result_2(id_ex_1_auipc_result_2), .SLTIU(\单周期硬布线控制器_1_sltiu ), .SLTIU_2(id_ex_1_sltiu_2));  // open: RS1_Forward, RS2_Forward, S_type_2, Uret_2, RS1_Forward_2, RS2_Forward_2, ID_PredictJump, EX_PredictJump
  // Probe on WB_PC[11:0]
  Comparator #(.width(13), .mode("twosComplement")) comparator_1 (
    .a(CNT_num), .b(13'h21), .eq(comparator_1_eq), .lt(comparator_1_lt));  // open: gt
  Clock #(.highDuration(1), .lowDuration(1)) clock_2 (.out(clock_2_out));
  // Probe on id_ex_1_auipc_result_2
  nand nand_1 (nand_1_out, d_ff_1_q, comparator_1_eq);
  Counter #(.width(13), .max('h1fff), .ongoal("stay"), .trigger("rising"), .behavior("old")) counter_1 (
    .count(comparator_1_lt), .Q(CNT_num), .clk(clock_2_out));  // open: load, D, carry, clr, preset
  Multiplexer #(.select(1), .width(32), .disabled("Z"), .enable("false")) multiplexer_6 (
    .in0(id_ex_1_r2_2), .in1(id_ex_1_imm_1_2), .out(multiplexer_6_out), .sel(id_ex_1_alusrc_2));
  assign CLK = nand_1_out ? clock_2_out : 1'bz;  // Controlled_Buffer controlled_buffer_1
  or or_5 (id_ex_1_jalr_2[1], id_ex_1_jal_2, BranchSuc);
  and and_3 (and_3_out, id_ex_1_bne_2, ~Equ);  // AND_Gate
  Pull_Resistor #(.pull(1)) pull_resistor_1 (.node(CLK));
  or or_6 (BranchSuc, and_3_out, and_4_out, and_5_out);
  and and_4 (and_4_out, Equ, id_ex_1_beq_2);
  and and_5 (and_5_out, id_ex_1_bltu_2, Less);
  ALU alu_1 (
    .X(id_ex_1_r1_2), .Y(multiplexer_6_out), .AluOP(id_ex_1_aluop_2), .Equal(Equ), .Result(ALU_addr),
    .out_6(Less));  // open: Result_2, out_4
  Shifter #(.width(32), .shift("ll")) shifter_2 (.in(id_ex_1_imm_2_2), .\dist (5'b00001), .out(shifter_2_out));
  Comparator #(.width(32), .mode("twosComplement")) comparator_2 (
    .a(id_ex_1_r1_2), .b(32'h22), .eq(comparator_2_eq));  // open: gt, lt
  or or_7 (BranchTaken, id_ex_1_jalr_2[1], id_ex_1_jalr_2[0]);
  not not_2 (not_2_out, comparator_2_eq);
  and and_6 (EX_halt, not_2_out, EX_ecall);
  and and_7 (and_7_out, comparator_2_eq, EX_ecall);
  or or_8 (\无条件跳转 , id_ex_1_jalr_2[0], id_ex_1_jal_2);
  Adder #(.width(32)) adder_3 (.a(shifter_2_out), .b(EX_PC), .out(jumpAddr));  // open: cin, cout
  Register #(.width(32), .trigger("rising"), .Select("low")) register_1 (
    .D(id_ex_1_r2_2), .en(and_7_out), .Q(LedData), .clk(CLK), .clr(RST));
  EX_MEM ex_mem_1 (
    .Jal(id_ex_1_jal_2), .Jalr(id_ex_1_jalr_2[0]), .MemToReg(id_ex_1_memtoreg_2),
    .MemWrite(id_ex_1_memwrite_2), .LB(id_ex_1_lb_2), .RegWrite(id_ex_1_regwrite_2), .halt(EX_halt),
    .rd(id_ex_1_rd_2), .Result(ALU_addr), .WriteData(id_ex_1_r2_2), .IR(EX_IR), .PC(EX_PC),
    .PC_4(id_ex_1_pc_4_2), .Jal_2(ex_mem_1_jal_2), .Jalr_2(ex_mem_1_jalr_2),
    .MemToReg_2(ex_mem_1_memtoreg_2), .MemWrite_2(MemWrite), .LB_2(LB), .RegWrite_2(ex_mem_1_regwrite_2),
    .halt_2(ex_mem_1_halt_2), .rd_2(ex_mem_1_rd_2), .Result_2(MEM_ALURes), .WriteData_2(MDin), .IR_2(MEM_IR),
    .PC_2(M_PC), .PC_4_2(ex_mem_1_pc_4_2), .reset(RST), .en(or_9_out), .clk(CLK), .U_Type(id_ex_1_u_type_2),
    .U_Type_2(ex_mem_1_u_type_2), .AUIPC_result(id_ex_1_auipc_result_2),
    .AUIPC_result_2(ex_mem_1_auipc_result_2), .SLTIU(id_ex_1_sltiu_2), .SLTIU_2(ex_mem_1_sltiu_2),
    .LESS(Less), .LESS_2(ex_mem_1_less_2));
  or or_9 (or_9_out, ~halt, Go);  // OR_Gate
  // Probe on ex_mem_1_auipc_result_2
  RAM #(.addrWidth(10), .dataWidth(32), .bus("separate"), .Select("high")) ram_1 (
    .addr(MEM_ALURes[11:2]), .din(MDin), .data(MemData), .str(MemWrite), .sel(1'b1), .clk(CLK), .ld(1'b1),
    .clr(RST));
  Multiplexer #(.select(1), .width(16), .disabled("Z"), .enable("false")) multiplexer_7 (
    .in0(MemData[15:0]), .in1(MemData[31:16]), .out(multiplexer_7_out), .sel(MEM_ALURes[1]));
  assign bit_extender_6_out = {{16{multiplexer_7_out[15]}}, multiplexer_7_out};  // Bit_Extender bit_extender_6
  Multiplexer #(.select(1), .width(32), .disabled("Z"), .enable("false")) multiplexer_8 (
    .in0(MemData), .in1(bit_extender_6_out), .out(multiplexer_8_out), .sel(LB));
  MEM_WB mem_wb_1 (
    .Jal(ex_mem_1_jal_2), .Jalr(ex_mem_1_jalr_2), .MemToReg(ex_mem_1_memtoreg_2),
    .RegWrite(ex_mem_1_regwrite_2), .halt(ex_mem_1_halt_2), .rd(ex_mem_1_rd_2), .ALUResult(MEM_ALURes),
    .ReadData(multiplexer_8_out), .IR(MEM_IR), .PC(M_PC), .PC_4(ex_mem_1_pc_4_2), .Jal_2(mem_wb_1_jal_2),
    .Jalr_2(mem_wb_1_jalr_2), .MemToReg_2(mem_wb_1_memtoreg_2), .RegWrite_2(RegWrite),
    .halt_2(mem_wb_1_halt_2), .rd_2(WB_rd), .ALUResult_2(mem_wb_1_aluresult_2),
    .ReadData_2(mem_wb_1_readdata_2), .IR_2(WB_IR), .PC_2(WB_PC), .PC_4_2(mem_wb_1_pc_4_2), .reset(RST),
    .en(or_10_out), .clk(CLK), .U_Type(ex_mem_1_u_type_2), .U_Type_2(mem_wb_1_u_type_2),
    .AUIPC_result(ex_mem_1_auipc_result_2), .AUIPC_result_2(mem_wb_1_auipc_result_2),
    .SLTIU(ex_mem_1_sltiu_2), .SLTIU_2(mem_wb_1_sltiu_2), .LESS(ex_mem_1_less_2), .LESS_2(mem_wb_1_less_2));
  or or_10 (or_10_out, ~halt, Go);  // OR_Gate
  or or_11 (or_11_out[0], mem_wb_1_u_type_2, mem_wb_1_memtoreg_2);
  D_Flip_Flop #(.trigger("rising"), .Pre_Clr_Positions("ABOVE_BELOW"), .NegatePresetClear("false"), .enable("true"), .NewFFLayout("true")) d_ff_2 (
    .clk(mem_wb_1_halt_2), .D(1'b1), .Q(halt), .en(1'b1), .reset(Go));  // open: Qn, preset
  // Probe on mem_wb_1_auipc_result_2
  or or_12 (or_11_out[1], mem_wb_1_jalr_2, mem_wb_1_jal_2, mem_wb_1_u_type_2);
  Multiplexer #(.select(2), .width(32), .disabled("Z"), .enable("false")) multiplexer_9 (
    .in0(mem_wb_1_aluresult_2), .in1(mem_wb_1_readdata_2), .in2(mem_wb_1_pc_4_2),
    .in3(mem_wb_1_auipc_result_2), .out(multiplexer_9_out), .sel(or_11_out));
  // Probe on multiplexer_9_out
  Counter #(.width(16), .max('hffff), .ongoal("wrap"), .trigger("rising"), .behavior("new")) counter_2 (
    .count(BranchSuc), .Q(\条件分支成功数 ), .clk(and_8_out), .clr(RST));  // open: load, D, carry, preset, down
  and and_8 (and_8_out, ~halt, CLK);  // AND_Gate
  Counter #(.width(16), .max('hffff), .ongoal("wrap"), .trigger("rising"), .behavior("new")) counter_3 (
    .count(Flush), .Q(\插入气泡数 ), .clk(and_9_out), .clr(RST));  // open: load, D, carry, preset, down
  and and_9 (and_9_out, ~halt, CLK);  // AND_Gate
  assign bit_extender_7_out = {{31{1'b0}}, mem_wb_1_less_2};  // Bit_Extender bit_extender_7
  Multiplexer #(.select(1), .width(32), .disabled("Z"), .enable("false")) multiplexer_10 (
    .in0(multiplexer_9_out), .in1(bit_extender_7_out), .out(RDin), .sel(mem_wb_1_sltiu_2));
  Counter #(.width(16), .max('hffff), .ongoal("wrap"), .trigger("rising"), .behavior("new")) counter_4 (
    .count(\无条件跳转 ), .Q(\无条件分支数 ), .clk(and_10_out), .clr(RST));  // open: load, D, carry, preset, down
  and and_10 (and_10_out, ~halt, CLK);  // AND_Gate
  Counter #(.width(16), .max('hffff), .ongoal("wrap"), .trigger("rising"), .behavior("new")) counter_5 (
    .count(CLK), .Q(\总周期数 ), .clk(and_11_out), .clr(RST));  // open: load, D, carry, preset, down
  and and_11 (and_11_out, ~halt, CLK);  // AND_Gate
  Counter #(.width(16), .max('hffff), .ongoal("wrap"), .trigger("rising"), .behavior("new")) counter_6 (
    .count(stall), .Q(\LoadUse次数 ), .clk(and_12_out), .clr(RST));  // open: load, D, carry, preset, down
  and and_12 (and_12_out, ~halt, CLK);  // AND_Gate

  // Other names for the same wires on the sheet: IR[31:0] = ID_IR; MEM_PC[31:0] = M_PC; WB_RegWrite = RegWrite

  // Notes on the sheet:
  //   中断源
  //   时空图监测，可删除
  //   中断等待指示
  //   数码管输出
  //   指令存储器
  //   指令探针
  //   contents of rom_1 (hex, n*v repeats v):
  //   fff00293 313 1900413 841413 9700493 940533 2200893 73 5484b3 494b313 fe0306e3 a00893 73
  //   指令字
  //   J
  //   RS1_used
  //   I
  //   S
  //   B
  //   U_Type
  //   RS2_used
  //   JALR
  //   Beq
  //   Bne
  //   MemToReg
  //   MemWrite
  //   AluOP
  //   AluSrc
  //   RegWrite
  //   S_type
  //   Uret
  //   LB
  //   BLTU
  //   JAL
  //   控制位
  //   ecall
  //   imm_1
  //   imm_2
  //   rd
  //   IR
  //   PC
  //   PC+4
  //   流水调试日志用
  //   暂停节拍，不能为0
  //   戳工具置1进入计数暂停模式，ctrl+k时钟自动运行到对应节拍暂停
  //   ctrl+k关闭时钟连续运行，将控制位置零，进入单步调试模式调试
  //   可计数暂停的时钟源
  //   BranchTaken
  //   U_type
  //   为方便自动评测，需要输出流水线各段保存的PC值，注意是PC不是PC+4，另外ID段寄存器写入信息，Mem段内存写入信息也要输出
  //   EX.RegWrite
  //   LB
  //   JALR
  //   JAL
  //   MemToReg
  //   MemWrite
  //   RegWrite
  //   rd
  //   IR
  //   PC
  //   PC+4
  //   数据存储器
  //   MEM.RegWrite
  //   U_Type
  //   JALR
  //   JAL
  //   MemToReg
  //   RegWrite
  //   halt
  //   ALUResult
  //   ReadData
  //   Mem.rd
endmodule

module \重定向流水线  (
  output RegWrite,
  output MemWrite,
  output [31:0] IF_PC,
  output [31:0] ID_PC,
  output [31:0] EX_PC,
  output [31:0] M_PC,
  output [31:0] WB_PC,
  output [31:0] RDin,
  output [31:0] MDin,
  output [31:0] LedData
);

  wire and_1_out, and_2_out, and_3_out, and_4_out, and_5_out, and_7_out, and_8_out, and_9_out, and_10_out,
       and_11_out, and_12_out, BranchSuc, BranchTaken, CLK, clock_1_out, clock_2_out, comparator_1_eq,
       comparator_1_lt, comparator_2_eq, d_ff_1_q, ecall, Equ, EX_ecall, EX_halt, ex_mem_1_halt_2,
       ex_mem_1_jal_2, ex_mem_1_jalr_2, ex_mem_1_less_2, ex_mem_1_memtoreg_2, ex_mem_1_regwrite_2,
       ex_mem_1_sltiu_2, ex_mem_1_u_type_2, Flush, Go, halt, id_ex_1_alusrc_2, id_ex_1_beq_2, id_ex_1_bltu_2,
       id_ex_1_bne_2, id_ex_1_jal_2, id_ex_1_lb_2, id_ex_1_memtoreg_2, id_ex_1_memwrite_2,
       id_ex_1_regwrite_2, id_ex_1_sltiu_2, id_ex_1_u_type_2, IR1, IR2, IR3, JAL, JALR, LB, Less,
       mem_wb_1_halt_2, mem_wb_1_jal_2, mem_wb_1_jalr_2, mem_wb_1_less_2, mem_wb_1_memtoreg_2,
       mem_wb_1_sltiu_2, mem_wb_1_u_type_2, nand_1_out, not_1_out, not_2_out, or_1_out, or_2_out, or_3_out,
       or_4_out, or_9_out, or_10_out, RST, S_type, stall, W1, W2, W3, \单周期硬布线控制器_1_alu_src ,
       \单周期硬布线控制器_1_beq , \单周期硬布线控制器_1_bltu , \单周期硬布线控制器_1_bne , \单周期硬布线控制器_1_lb , \单周期硬布线控制器_1_memtoreg ,
       \单周期硬布线控制器_1_memwrite , \单周期硬布线控制器_1_regwrite , \单周期硬布线控制器_1_rs1_used , \单周期硬布线控制器_1_rs2_used ,
       \单周期硬布线控制器_1_sltiu , \单周期硬布线控制器_1_u_type , \单周期硬布线控制器_1_uret , \无条件跳转 ;
  wire [1:0] id_ex_1_jalr_2, id_ex_1_rs1_forward_2, id_ex_1_rs2_forward_2, or_12_out,
       \重定向处理逻辑_1_rs1_forward , \重定向处理逻辑_1_rs2_forward ;
  wire [3:0] id_ex_1_aluop_2, \单周期硬布线控制器_1_alu_op ;
  wire [4:0] ex_mem_1_rd_2, id_ex_1_rd_2, multiplexer_2_out, multiplexer_3_out, WB_rd;
  wire [12:0] CNT_num;
  wire [15:0] \LoadUse次数 , multiplexer_10_out, \总周期数 , \插入气泡数 , \无条件分支数 , \条件分支成功数 ;
  wire [31:0] adder_2_out, ALU_addr, AUIPC_Res, bit_extender_1_out, bit_extender_2_out, bit_extender_3_out,
       bit_extender_4_out, bit_extender_5_out, bit_extender_6_out, bit_extender_7_out, bit_extender_8_out,
       EX_IR, ex_mem_1_pc_4_2, ex_mem_1_result_2, id_ex_1_auipc_result_2, id_ex_1_imm_1_2, id_ex_1_imm_2_2,
       id_ex_1_pc_4_2, id_ex_1_r1_2, id_ex_1_r2_2, ID_IR, if_id_1_pc_4_2, IF_IR, jumpAddr, MEM_ALURes,
       MEM_IR, mem_wb_1_aluresult_2, mem_wb_1_auipc_result_2, mem_wb_1_pc_4_2, mem_wb_1_readdata_2, MemData,
       multiplexer_1_out, multiplexer_4_out, multiplexer_5_out, multiplexer_6_out, multiplexer_7_out,
       multiplexer_8_out, multiplexer_9_out, multiplexer_12_out, multiplexer_13_out, PC_4, regifile_1_r1,
       regifile_1_r2, shifter_1_out, shifter_2_out, WB_IR;

  Button \u_总复位  (.out(RST));
  Button _1 (.out(IR1));
  Button _2 (.out(IR2));
  Button _3 (.out(IR3));
  // Probe on \总周期数 
  // Probe on \总周期数 
  \重定向处理逻辑  \u_重定向处理逻辑_1  (
    .RS1_used(\单周期硬布线控制器_1_rs1_used ), .EX_RegWrite(id_ex_1_regwrite_2), .EX_MemToReg(id_ex_1_memtoreg_2),
    .IR(ID_IR), .RS2_used(\单周期硬布线控制器_1_rs2_used ), .MEM_RegWrite(ex_mem_1_regwrite_2), .EX_rd(id_ex_1_rd_2),
    .Ecall(ecall), .BranchTaken(BranchTaken), .MEM_rd(ex_mem_1_rd_2), .Stall(stall), .Flush(Flush),
    .RS1_Forward(\重定向处理逻辑_1_rs1_forward ), .RS2_Forward(\重定向处理逻辑_1_rs2_forward ));
  and and_1 (and_1_out, ~halt, ~stall);  // AND_Gate
  or or_1 (or_1_out, and_1_out, Go);
  Button \u_继续运行  (.out(Go));
  LED #(.active("true")) led_1 (.in(W1));
  LED #(.active("true")) led_2 (.in(W2));
  LED #(.active("true")) led_3 (.in(W3));
  Hex_Digit_Display hex_digit_display_1 (.value(LedData[31:28]));  // open: dp
  // Probe on IF_PC[19:0]
  // RiscV_Probe riscv_probe_1: pin names not known; wires that end beside it: IF_IR
  Multiplexer #(.select(2), .width(32), .disabled("Z"), .enable("false")) multiplexer_1 (
    .in0(PC_4), .in1(ALU_addr), .in2(jumpAddr), .out(multiplexer_1_out), .sel(id_ex_1_jalr_2));  // open: in3
  Hex_Digit_Display hex_digit_display_2 (.value(LedData[27:24]));  // open: dp
  Hex_Digit_Display hex_digit_display_3 (.value(LedData[23:20]));  // open: dp
  // Probe on ID_PC[19:0]
  // RiscV_Probe riscv_probe_2: pin names not known; wires that end beside it: ID_IR
  Register #(.width(32), .trigger("rising"), .Select("low")) PC (
    .D(multiplexer_1_out), .en(or_1_out), .Q(IF_PC), .clk(CLK), .clr(RST));
  Hex_Digit_Display hex_digit_display_4 (.value(LedData[15:12]));  // open: dp
  Hex_Digit_Display hex_digit_display_5 (.value(LedData[19:16]));  // open: dp
  Adder #(.width(32)) adder_1 (.a(IF_PC), .b(32'h4), .out(PC_4));  // open: cin, cout
  // RiscV_Probe riscv_probe_3: pin names not known; wires that end beside it: IF_IR
  Hex_Digit_Display hex_digit_display_6 (.value(LedData[7:4]));  // open: dp
  Hex_Digit_Display hex_digit_display_7 (.value(LedData[11:8]));  // open: dp
  Clock #(.highDuration(1), .lowDuration(1)) clock_1 (.out(clock_1_out));
  // Probe on EX_PC[19:0]
  // RiscV_Probe riscv_probe_4: pin names not known; wires that end beside it: clock_1_out, EX_IR, CLK
  ROM #(.addrWidth(10), .dataWidth(32), .Select("high")) rom_1 (.addr(IF_PC[11:2]), .data(IF_IR));
  and and_2 (and_2_out, ~stall, or_2_out);  // AND_Gate
  or or_2 (or_2_out, ~halt, Go);  // OR_Gate
  Hex_Digit_Display hex_digit_display_8 (.value(LedData[3:0]));  // open: dp
  or or_3 (or_3_out, id_ex_1_jalr_2[1], id_ex_1_jalr_2[0]);
  IF_ID if_id_1 (
    .IR(IF_IR), .PC(IF_PC), .PC_4(PC_4), .IR_2(ID_IR), .PC_2(ID_PC), .PC_4_2(if_id_1_pc_4_2),
    .branch(or_3_out), .reset(RST), .en(and_2_out), .clk(CLK));  // open: ID_PredictJump, IF_PredictJump
  // Probe on \总周期数 
  // Probe on M_PC[19:0]
  // RiscV_Probe riscv_probe_5: pin names not known; wires that end beside it: MEM_IR
  \单周期硬布线控制器  \u_单周期硬布线控制器_1  (
    .Funct({ID_IR[30], ID_IR[25], ID_IR[14:12]}), .OP(ID_IR[6:2]), .ALU_OP(\单周期硬布线控制器_1_alu_op ),
    .MemToReg(\单周期硬布线控制器_1_memtoreg ), .MemWrite(\单周期硬布线控制器_1_memwrite ), .ALU_SRC(\单周期硬布线控制器_1_alu_src ),
    .RegWrite(\单周期硬布线控制器_1_regwrite ), .ecall(ecall), .S_type(S_type), .JALR(JALR), .BEQ(\单周期硬布线控制器_1_beq ),
    .JAL(JAL), .BNE(\单周期硬布线控制器_1_bne ), .in_3(ID_IR[21]), .uret(\单周期硬布线控制器_1_uret ),
    .BLTU(\单周期硬布线控制器_1_bltu ), .LB(\单周期硬布线控制器_1_lb ), .U_Type(\单周期硬布线控制器_1_u_type ),
    .rs1_used(\单周期硬布线控制器_1_rs1_used ), .rs2_used(\单周期硬布线控制器_1_rs2_used ), .SLTIU(\单周期硬布线控制器_1_sltiu ));  // open: CSR
  Multiplexer #(.select(1), .width(5), .disabled("Z"), .enable("false")) multiplexer_2 (
    .in0(ID_IR[19:15]), .in1(5'b10001), .out(multiplexer_2_out), .sel(ecall));
  Multiplexer #(.select(1), .width(5), .disabled("Z"), .enable("false")) multiplexer_3 (
    .in0(ID_IR[24:20]), .in1(5'b01010), .out(multiplexer_3_out), .sel(ecall));
  assign bit_extender_1_out = {{12{ID_IR[31]}}, ID_IR[31:12]};  // Bit_Extender bit_extender_1
  // Probe on \总周期数 
  // Probe on \无条件分支数 
  // Probe on \条件分支成功数 
  // Probe on \插入气泡数 
  // Probe on \LoadUse次数 
  // Probe on multiplexer_2_out
  // Probe on multiplexer_3_out
  assign bit_extender_2_out = {{20{ID_IR[31]}}, ID_IR[31:20]};  // Bit_Extender bit_extender_2
  assign bit_extender_3_out = {{20{ID_IR[31]}}, {ID_IR[31:25], ID_IR[11:7]}};  // Bit_Extender bit_extender_3
  assign bit_extender_4_out = {{20{ID_IR[31]}}, {ID_IR[31], ID_IR[7], ID_IR[30:25], ID_IR[11:8]}};  // Bit_Extender bit_extender_4
  assign bit_extender_5_out = {{12{ID_IR[31]}}, {ID_IR[31], ID_IR[19:12], ID_IR[20], ID_IR[30:21]}};  // Bit_Extender bit_extender_5
  Shifter #(.width(32), .shift("ll")) shifter_1 (.in(bit_extender_1_out), .\dist (5'b01100), .out(shifter_1_out));
  // Probe on IF_PC[11:0]
  // Probe on WB_PC[19:0]
  // RiscV_Probe riscv_probe_6: pin names not known; wires that end beside it: WB_IR
  not not_1 (not_1_out, CLK);
  Multiplexer #(.select(1), .width(32), .disabled("Z"), .enable("false")) multiplexer_4 (
    .in0(bit_extender_2_out), .in1(bit_extender_3_out), .out(multiplexer_4_out), .sel(S_type));
  Multiplexer #(.select(1), .width(32), .disabled("Z"), .enable("false")) multiplexer_5 (
    .in0(bit_extender_4_out), .in1(bit_extender_5_out), .out(multiplexer_5_out), .sel(JAL));
  // Probe on EX_PC[11:0]
  // Probe on ID_PC[11:0]
  Regifile regifile_1 (
    .Din(RDin), .Clk(not_1_out), .R1(regifile_1_r1), .R2(regifile_1_r2), .WE(RegWrite), .W_num(WB_rd),
    .R1_num(multiplexer_2_out), .R2_num(multiplexer_3_out));
  or or_4 (or_4_out, ~halt, Go);  // OR_Gate
  Adder #(.width(32)) adder_2 (.a(shifter_1_out), .b(ID_PC), .out(adder_2_out));  // open: cin, cout
  // Probe on adder_2_out
  // Probe on M_PC[11:0]
  D_Flip_Flop #(.trigger("high"), .Pre_Clr_Positions("LEGACY"), .NegatePresetClear("false"), .enable("true"), .NewFFLayout("false")) d_ff_1 (.Q(d_ff_1_q));  // open: clk, D, Qn, preset, en, reset
  // Probe on 13'hc
  ID_EX id_ex_1 (
    .BEQ(\单周期硬布线控制器_1_beq ), .BNE(\单周期硬布线控制器_1_bne ), .MemToReg(\单周期硬布线控制器_1_memtoreg ),
    .MemWrite(\单周期硬布线控制器_1_memwrite ), .AluSrc(\单周期硬布线控制器_1_alu_src ), .RegWrite(\单周期硬布线控制器_1_regwrite ),
    .S_type(S_type), .ecall(ecall), .Jal(JAL), .Jalr(JALR), .LB(\单周期硬布线控制器_1_lb ), .BLTU(\单周期硬布线控制器_1_bltu ),
    .Uret(\单周期硬布线控制器_1_uret ), .AluOP(\单周期硬布线控制器_1_alu_op ), .rd(ID_IR[11:7]), .R1(regifile_1_r1),
    .R2(regifile_1_r2), .imm_1(multiplexer_4_out), .imm_2(multiplexer_5_out), .PC(ID_PC),
    .PC_4(if_id_1_pc_4_2), .IR(ID_IR), .RS1_Forward(\重定向处理逻辑_1_rs1_forward ),
    .RS2_Forward(\重定向处理逻辑_1_rs2_forward ), .BEQ_2(id_ex_1_beq_2), .BNE_2(id_ex_1_bne_2),
    .MemToReg_2(id_ex_1_memtoreg_2), .MemWrite_2(id_ex_1_memwrite_2), .AluSrc_2(id_ex_1_alusrc_2),
    .RegWrite_2(id_ex_1_regwrite_2), .ecall_2(EX_ecall), .Jal_2(id_ex_1_jal_2), .Jalr_2(id_ex_1_jalr_2[0]),
    .LB_2(id_ex_1_lb_2), .BLTU_2(id_ex_1_bltu_2), .AluOP_2(id_ex_1_aluop_2), .rd_2(id_ex_1_rd_2),
    .R1_2(id_ex_1_r1_2), .R2_2(id_ex_1_r2_2), .imm_1_2(id_ex_1_imm_1_2), .imm_2_2(id_ex_1_imm_2_2),
    .PC_2(EX_PC), .PC_4_2(id_ex_1_pc_4_2), .IR_2(EX_IR), .RS1_Forward_2(id_ex_1_rs1_forward_2),
    .RS2_Forward_2(id_ex_1_rs2_forward_2), .reset(RST), .flush(Flush), .en(or_4_out), .clk(CLK),
    .U_Type(\单周期硬布线控制器_1_u_type ), .U_Type_2(id_ex_1_u_type_2), .AUIPC_result(adder_2_out),
    .AUIPC_result_2(id_ex_1_auipc_result_2), .SLTIU(\单周期硬布线控制器_1_sltiu ), .SLTIU_2(id_ex_1_sltiu_2));  // open: S_type_2, Uret_2, ID_PredictJump, EX_PredictJump
  // Probe on WB_PC[11:0]
  Comparator #(.width(13), .mode("twosComplement")) comparator_1 (
    .a(CNT_num), .b(13'hc), .eq(comparator_1_eq), .lt(comparator_1_lt));  // open: gt
  Clock #(.highDuration(1), .lowDuration(1)) clock_2 (.out(clock_2_out));
  Multiplexer #(.select(2), .width(32), .disabled("Z"), .enable("false")) multiplexer_6 (
    .in0(id_ex_1_r1_2), .in1(RDin), .in2(MEM_ALURes), .out(multiplexer_6_out), .sel(id_ex_1_rs1_forward_2));  // open: in3
  // Probe on id_ex_1_auipc_result_2
  nand nand_1 (nand_1_out, d_ff_1_q, comparator_1_eq);
  Counter #(.width(13), .max('h1fff), .ongoal("stay"), .trigger("rising"), .behavior("old")) counter_1 (
    .count(comparator_1_lt), .Q(CNT_num), .clk(clock_2_out));  // open: load, D, carry, clr, preset
  Multiplexer #(.select(2), .width(32), .disabled("Z"), .enable("false")) multiplexer_7 (
    .in0(id_ex_1_r2_2), .in1(RDin), .in2(MEM_ALURes), .out(multiplexer_7_out), .sel(id_ex_1_rs2_forward_2));  // open: in3
  assign CLK = nand_1_out ? clock_2_out : 1'bz;  // Controlled_Buffer controlled_buffer_1
  or or_5 (id_ex_1_jalr_2[1], id_ex_1_jal_2, BranchSuc);
  and and_3 (and_3_out, id_ex_1_bne_2, ~Equ);  // AND_Gate
  Pull_Resistor #(.pull(1)) pull_resistor_1 (.node(CLK));
  or or_6 (BranchSuc, and_3_out, and_4_out, and_5_out);
  and and_4 (and_4_out, Equ, id_ex_1_beq_2);
  and and_5 (and_5_out, id_ex_1_bltu_2, Less);
  Multiplexer #(.select(1), .width(32), .disabled("Z"), .enable("false")) multiplexer_8 (
    .in0(multiplexer_7_out), .in1(id_ex_1_imm_1_2), .out(multiplexer_8_out), .sel(id_ex_1_alusrc_2));
  Shifter #(.width(32), .shift("ll")) shifter_2 (.in(id_ex_1_imm_2_2), .\dist (5'b00001), .out(shifter_2_out));
  Comparator #(.width(32), .mode("twosComplement")) comparator_2 (
    .a(multiplexer_6_out), .b(32'h22), .eq(comparator_2_eq));  // open: gt, lt
  or or_7 (BranchTaken, id_ex_1_jalr_2[1], id_ex_1_jalr_2[0]);
  ALU alu_1 (
    .X(multiplexer_6_out), .Y(multiplexer_8_out), .AluOP(id_ex_1_aluop_2), .Equal(Equ), .Result(ALU_addr),
    .out_6(Less));  // open: Result_2, out_4
  not not_2 (not_2_out, comparator_2_eq);
  and and_6 (EX_halt, not_2_out, EX_ecall);
  and and_7 (and_7_out, comparator_2_eq, EX_ecall);
  or or_8 (\无条件跳转 , id_ex_1_jalr_2[0], id_ex_1_jal_2);
  Adder #(.width(32)) adder_3 (.a(shifter_2_out), .b(EX_PC), .out(jumpAddr));  // open: cin, cout
  Register #(.width(32), .trigger("rising"), .Select("low")) register_1 (
    .D(multiplexer_7_out), .en(and_7_out), .Q(LedData), .clk(CLK), .clr(RST));
  EX_MEM ex_mem_1 (
    .Jal(id_ex_1_jal_2), .Jalr(id_ex_1_jalr_2[0]), .MemToReg(id_ex_1_memtoreg_2),
    .MemWrite(id_ex_1_memwrite_2), .LB(id_ex_1_lb_2), .RegWrite(id_ex_1_regwrite_2), .halt(EX_halt),
    .rd(id_ex_1_rd_2), .Result(ALU_addr), .WriteData(multiplexer_7_out), .IR(EX_IR), .PC(EX_PC),
    .PC_4(id_ex_1_pc_4_2), .Jal_2(ex_mem_1_jal_2), .Jalr_2(ex_mem_1_jalr_2),
    .MemToReg_2(ex_mem_1_memtoreg_2), .MemWrite_2(MemWrite), .LB_2(LB), .RegWrite_2(ex_mem_1_regwrite_2),
    .halt_2(ex_mem_1_halt_2), .rd_2(ex_mem_1_rd_2), .Result_2(ex_mem_1_result_2), .WriteData_2(MDin),
    .IR_2(MEM_IR), .PC_2(M_PC), .PC_4_2(ex_mem_1_pc_4_2), .reset(RST), .en(or_9_out), .clk(CLK),
    .U_Type(id_ex_1_u_type_2), .U_Type_2(ex_mem_1_u_type_2), .AUIPC_result(id_ex_1_auipc_result_2),
    .AUIPC_result_2(AUIPC_Res), .SLTIU(id_ex_1_sltiu_2), .SLTIU_2(ex_mem_1_sltiu_2), .LESS(Less),
    .LESS_2(ex_mem_1_less_2));
  or or_9 (or_9_out, ~halt, Go);  // OR_Gate
  // Probe on AUIPC_Res
  Multiplexer #(.select(1), .width(32), .disabled("Z"), .enable("false")) multiplexer_9 (
    .in0(ex_mem_1_result_2), .in1(AUIPC_Res), .out(multiplexer_9_out), .sel(ex_mem_1_u_type_2));
  assign bit_extender_6_out = {{31{1'b0}}, ex_mem_1_less_2};  // Bit_Extender bit_extender_6
  RAM #(.addrWidth(10), .dataWidth(32), .bus("separate"), .Select("high")) ram_1 (
    .addr(ex_mem_1_result_2[11:2]), .din(MDin), .data(MemData), .str(MemWrite), .sel(1'b1), .clk(CLK),
    .ld(1'b1), .clr(RST));
  Multiplexer #(.select(1), .width(16), .disabled("Z"), .enable("false")) multiplexer_10 (
    .in0(MemData[15:0]), .in1(MemData[31:16]), .out(multiplexer_10_out), .sel(ex_mem_1_result_2[1]));
  Multiplexer #(.select(1), .width(32), .disabled("Z"), .enable("false")) multiplexer_11 (
    .in0(multiplexer_9_out), .in1(bit_extender_6_out), .out(MEM_ALURes), .sel(ex_mem_1_sltiu_2));
  Multiplexer #(.select(1), .width(32), .disabled("Z"), .enable("false")) multiplexer_12 (
    .in0(MemData), .in1(bit_extender_7_out), .out(multiplexer_12_out), .sel(LB));
  assign bit_extender_7_out = {{16{multiplexer_10_out[15]}}, multiplexer_10_out};  // Bit_Extender bit_extender_7
  MEM_WB mem_wb_1 (
    .Jal(ex_mem_1_jal_2), .Jalr(ex_mem_1_jalr_2), .MemToReg(ex_mem_1_memtoreg_2),
    .RegWrite(ex_mem_1_regwrite_2), .halt(ex_mem_1_halt_2), .rd(ex_mem_1_rd_2),
    .ALUResult(ex_mem_1_result_2), .ReadData(multiplexer_12_out), .IR(MEM_IR), .PC(M_PC),
    .PC_4(ex_mem_1_pc_4_2), .Jal_2(mem_wb_1_jal_2), .Jalr_2(mem_wb_1_jalr_2),
    .MemToReg_2(mem_wb_1_memtoreg_2), .RegWrite_2(RegWrite), .halt_2(mem_wb_1_halt_2), .rd_2(WB_rd),
    .ALUResult_2(mem_wb_1_aluresult_2), .ReadData_2(mem_wb_1_readdata_2), .IR_2(WB_IR), .PC_2(WB_PC),
    .PC_4_2(mem_wb_1_pc_4_2), .reset(RST), .en(or_10_out), .clk(CLK), .U_Type(ex_mem_1_u_type_2),
    .U_Type_2(mem_wb_1_u_type_2), .AUIPC_result(AUIPC_Res), .AUIPC_result_2(mem_wb_1_auipc_result_2),
    .SLTIU(ex_mem_1_sltiu_2), .SLTIU_2(mem_wb_1_sltiu_2), .LESS(ex_mem_1_less_2), .LESS_2(mem_wb_1_less_2));
  or or_10 (or_10_out, ~halt, Go);  // OR_Gate
  D_Flip_Flop #(.trigger("rising"), .Pre_Clr_Positions("ABOVE_BELOW"), .NegatePresetClear("false"), .enable("true"), .NewFFLayout("true")) d_ff_2 (
    .clk(mem_wb_1_halt_2), .D(1'b1), .Q(halt), .en(1'b1), .reset(Go));  // open: Qn, preset
  // Probe on mem_wb_1_auipc_result_2
  or or_11 (or_12_out[1], mem_wb_1_jalr_2, mem_wb_1_jal_2, mem_wb_1_u_type_2);
  or or_12 (or_12_out[0], mem_wb_1_u_type_2, mem_wb_1_memtoreg_2);
  Multiplexer #(.select(2), .width(32), .disabled("Z"), .enable("false")) multiplexer_13 (
    .in0(mem_wb_1_aluresult_2), .in1(mem_wb_1_readdata_2), .in2(mem_wb_1_pc_4_2),
    .in3(mem_wb_1_auipc_result_2), .out(multiplexer_13_out), .sel(or_12_out));
  // Probe on multiplexer_13_out
  Counter #(.width(16), .max('hffff), .ongoal("wrap"), .trigger("rising"), .behavior("new")) counter_2 (
    .count(BranchSuc), .Q(\条件分支成功数 ), .clk(and_8_out), .clr(RST));  // open: load, D, carry, preset, down
  and and_8 (and_8_out, ~halt, CLK);  // AND_Gate
  Counter #(.width(16), .max('hffff), .ongoal("wrap"), .trigger("rising"), .behavior("new")) counter_3 (
    .count(Flush), .Q(\插入气泡数 ), .clk(and_9_out), .clr(RST));  // open: load, D, carry, preset, down
  and and_9 (and_9_out, ~halt, CLK);  // AND_Gate
  Multiplexer #(.select(1), .width(32), .disabled("Z"), .enable("false")) multiplexer_14 (
    .in0(multiplexer_13_out), .in1(bit_extender_8_out), .out(RDin), .sel(mem_wb_1_sltiu_2));
  assign bit_extender_8_out = {{31{1'b0}}, mem_wb_1_less_2};  // Bit_Extender bit_extender_8
  Counter #(.width(16), .max('hffff), .ongoal("wrap"), .trigger("rising"), .behavior("new")) counter_4 (
    .count(\无条件跳转 ), .Q(\无条件分支数 ), .clk(and_10_out), .clr(RST));  // open: load, D, carry, preset, down
  and and_10 (and_10_out, ~halt, CLK);  // AND_Gate
  Counter #(.width(16), .max('hffff), .ongoal("wrap"), .trigger("rising"), .behavior("new")) counter_5 (
    .count(CLK), .Q(\总周期数 ), .clk(and_11_out), .clr(RST));  // open: load, D, carry, preset, down
  and and_11 (and_11_out, ~halt, CLK);  // AND_Gate
  Counter #(.width(16), .max('hffff), .ongoal("wrap"), .trigger("rising"), .behavior("new")) counter_6 (
    .count(stall), .Q(\LoadUse次数 ), .clk(and_12_out), .clr(RST));  // open: load, D, carry, preset, down
  and and_12 (and_12_out, ~halt, CLK);  // AND_Gate

  // Other names for the same wires on the sheet: IR[31:0] = ID_IR; MEM_PC[31:0] = M_PC; WB_RegWrite = RegWrite

  // Notes on the sheet:
  //   中断源
  //   时空图监测，可删除
  //   中断等待指示
  //   数码管输出
  //   指令存储器
  //   指令探针
  //   contents of rom_1 (hex, n*v repeats v):
  //   fff00293 313 1900413 841413 9700493 940533 2200893 73 5484b3 494b313 fe0306e3 a00893 73
  //   指令字
  //   J
  //   U_Type
  //   RS1_used
  //   I
  //   S
  //   B
  //   RS2_used
  //   JALR
  //   Beq
  //   Bne
  //   MemToReg
  //   MemWrite
  //   AluOP
  //   AluSrc
  //   RegWrite
  //   U_Type
  //   S_type
  //   Uret
  //   LB
  //   BLTU
  //   JAL
  //   控制位
  //   ecall
  //   imm_1
  //   imm_2
  //   rd
  //   IR
  //   PC
  //   PC+4
  //   流水调试日志用
  //   暂停节拍，不能为0
  //   戳工具置1进入计数暂停模式，ctrl+k时钟自动运行到对应节拍暂停
  //   ctrl+k关闭时钟连续运行，将控制位置零，进入单步调试模式调试
  //   可计数暂停的时钟源
  //   BranchTaken
  //   EX.MemToReg
  //   U_Type
  //   为方便自动评测，需要输出流水线各段保存的PC值，注意是PC不是PC+4，另外ID段寄存器写入信息，Mem段内存写入信息也要输出
  //   EX.RegWrite
  //   LB
  //   JALR
  //   JAL
  //   MemToReg
  //   MemWrite
  //   RegWrite
  //   rd
  //   IR
  //   PC
  //   PC+4
  //   数据存储器
  //   MEM.RegWrite
  //   JALR
  //   JAL
  //   U_Type
  //   MemToReg
  //   RegWrite
  //   halt
  //   ALUResult
  //   ReadData
  //   Mem.rd
endmodule

module \中断按键参考电路  (
  input  \同步清零信号 ,
  output \与中断屏蔽位与 
);

  wire \_1号中断_out , and_1_out, clock_1_out, d_ff_1_q, or_1_out, or_2_out;

  Clock #(.highDuration(1), .lowDuration(1)) clock_1 (.out(clock_1_out));
  Button \_1号中断  (.out(\_1号中断_out ));
  or or_1 (or_1_out, \与中断屏蔽位与 , d_ff_1_q);
  LED #(.active("true")) \_1号中断等待指示灯  (.in(or_1_out));
  D_Flip_Flop #(.trigger("rising"), .Pre_Clr_Positions("LEGACY"), .NegatePresetClear("false"), .enable("true"), .NewFFLayout("false")) d_ff_1 (
    .clk(\_1号中断_out ), .D(1'b1), .Q(d_ff_1_q), .reset(\与中断屏蔽位与 ));  // open: Qn, preset, en
  or or_2 (or_2_out, d_ff_1_q, \与中断屏蔽位与 );
  and and_1 (and_1_out, or_2_out, ~\同步清零信号 );  // AND_Gate
  D_Flip_Flop #(.trigger("rising"), .Pre_Clr_Positions("LEGACY"), .NegatePresetClear("false"), .enable("true"), .NewFFLayout("false")) IR1 (
    .clk(clock_1_out), .D(and_1_out), .Q(\与中断屏蔽位与 ));  // open: Qn, preset, en, reset

  // Notes on the sheet:
  //   中断信号采样参考电路
  //   Reset 
endmodule

module \单周期_单级中断  (
  input  IR1,
  input  IR2,
  input  IR3,
  output RegWrite,
  output MemWrite,
  output [31:0] PC,
  output [31:0] IR,
  output [31:0] RDin,
  output [31:0] MDin,
  output [31:0] LedData
);

  wire AluSrc, and_1_out, and_2_out, and_3_out, and_4_out, and_5_out, and_6_out, and_7_out, AUIPC, Beq, BLTU,
       Bne, CLK, comparator_1_eq, comparator_2_eq, comparator_3_eq, comparator_4_eq, comparator_5_eq,
       comparator_6_eq, d_ff_2_q, d_ff_3_q, d_ff_4_q, ecall, Equ, Go, halt, IE, Interrupt, IR1_q, IR1_Reset,
       IR1_t, IR2_q, IR2_Reset, IR2_t, IR3_q, IR3_Reset, IR3_t, IRA, IRB, IRC, JAL, JALR, LB, Less, MemToReg,
       not_1_out, not_2_out, not_3_out, not_4_out, not_5_out, or_1_out, or_8_out, or_9_out, or_10_out,
       or_11_out, or_12_out, priority_encoder_2_gs, RST, S_type, URET, W1, W2, W3;
  wire [1:0] IR_id, or_13_out, priority_encoder_1_out, register_2_q;
  wire [3:0] \单周期硬布线控制器_1_alu_op ;
  wire [4:0] multiplexer_2_out, multiplexer_3_out;
  wire [7:0] multiplexer_6_out;
  wire [15:0] \总周期数 ;
  wire [31:0] adder_2_out, adder_3_out, ALUResult, AUIPC_Result, bit_extender_1_out, bit_extender_2_out,
       bit_extender_3_out, bit_extender_4_out, bit_extender_5_out, bit_extender_6_out, EPC, MemData,
       multiplexer_4_out, multiplexer_5_out, multiplexer_9_out, multiplexer_10_out, mux_out, PC_4, PC_Next,
       PC_Ori, regifile_1_r1, shifter_1_out, shifter_2_out, shifter_3_out;

  Clock #(.highDuration(1), .lowDuration(1)) clock_1 (.out(CLK));
  Button _1 (.out(IRA));
  Button _2 (.out(IRB));
  Button _3 (.out(IRC));
  Button \u_继续运行  (.out(Go));
  LED #(.active("true")) led_1 (.in(W1));
  LED #(.active("true")) led_2 (.in(W2));
  LED #(.active("true")) led_3 (.in(W3));
  Multiplexer #(.select(2), .width(32), .disabled("Z"), .enable("false")) multiplexer_1 (
    .in0(PC_4), .in1(ALUResult), .in2(adder_3_out), .in3(adder_2_out), .out(PC_Ori),
    .sel(priority_encoder_1_out));
  Hex_Digit_Display hex_digit_display_1 (.value(LedData[31:28]));  // open: dp
  Priority_Encoder #(.select(2), .disabled("Z")) priority_encoder_1 (
    .in0(1'b1), .in1(JALR), .in2(JAL), .in3(or_1_out), .out(priority_encoder_1_out));  // open: gs, en_out, en_in
  not not_1 (not_1_out, halt);
  Hex_Digit_Display hex_digit_display_2 (.value(LedData[23:20]));  // open: dp
  Hex_Digit_Display hex_digit_display_3 (.value(LedData[27:24]));  // open: dp
  or or_1 (or_1_out, and_1_out, and_2_out, and_3_out);
  Register #(.width(32), .trigger("rising"), .Select("low")) u_PC (
    .D(PC_Next), .en(not_1_out), .Q(PC), .clk(CLK), .clr(RST));
  Hex_Digit_Display hex_digit_display_4 (.value(LedData[19:16]));  // open: dp
  Hex_Digit_Display hex_digit_display_5 (.value(LedData[15:12]));  // open: dp
  and and_1 (and_1_out, BLTU, Less);
  and and_2 (and_2_out, Beq, Equ);
  and and_3 (and_3_out, ~Equ, Bne);  // AND_Gate
  // RiscV_Probe riscv_probe_1: pin names not known; wires that end beside it: IR
  Adder #(.width(32)) adder_1 (.a(PC), .b(32'h4), .out(PC_4));  // open: cin, cout
  Hex_Digit_Display hex_digit_display_6 (.value(LedData[7:4]));  // open: dp
  Hex_Digit_Display hex_digit_display_7 (.value(LedData[11:8]));  // open: dp
  // Probe on \总周期数 
  ROM #(.addrWidth(10), .dataWidth(32), .Select("high")) rom_1 (.addr(PC[11:2]), .data(IR));
  Hex_Digit_Display hex_digit_display_8 (.value(LedData[3:0]));  // open: dp
  Multiplexer #(.select(1), .width(5), .disabled("Z"), .enable("false")) multiplexer_2 (
    .in0(IR[19:15]), .in1(5'b10001), .out(multiplexer_2_out), .sel(ecall));
  Multiplexer #(.select(1), .width(5), .disabled("Z"), .enable("false")) multiplexer_3 (
    .in0(IR[24:20]), .in1(5'b01010), .out(multiplexer_3_out), .sel(ecall));
  \单周期硬布线控制器  \u_单周期硬布线控制器_1  (
    .Funct({IR[30], IR[25], IR[14:12]}), .OP(IR[6:2]), .ALU_OP(\单周期硬布线控制器_1_alu_op ), .MemToReg(MemToReg),
    .MemWrite(MemWrite), .ALU_SRC(AluSrc), .RegWrite(RegWrite), .ecall(ecall), .S_type(S_type), .JALR(JALR),
    .BEQ(Beq), .JAL(JAL), .BNE(Bne), .in_3(IR[21]), .uret(URET), .BLTU(BLTU), .LB(LB), .U_Type(AUIPC));  // open: rs1_used, rs2_used, CSR, SLTIU
  // Probe on multiplexer_2_out
  // Probe on multiplexer_3_out
  // Probe on IR[11:7]
  assign bit_extender_1_out = {{20{IR[31]}}, IR[31:20]};  // Bit_Extender bit_extender_1
  assign bit_extender_2_out = {{20{IR[31]}}, {IR[31:25], IR[11:7]}};  // Bit_Extender bit_extender_2
  assign bit_extender_3_out = {{20{IR[31]}}, {IR[31], IR[7], IR[30:25], IR[11:8]}};  // Bit_Extender bit_extender_3
  assign bit_extender_4_out = {{12{IR[31]}}, {IR[31], IR[19:12], IR[20], IR[30:21]}};  // Bit_Extender bit_extender_4
  or or_2 (IR1_t, IR1, IRA);
  Multiplexer #(.select(1), .width(32), .disabled("Z"), .enable("false")) multiplexer_4 (
    .in0(bit_extender_1_out), .in1(bit_extender_2_out), .out(multiplexer_4_out), .sel(S_type));
  Shifter #(.width(32), .shift("ll")) shifter_1 (.in(bit_extender_3_out), .\dist (5'b00001), .out(shifter_1_out));
  Shifter #(.width(32), .shift("ll")) shifter_2 (.in(bit_extender_4_out), .\dist (5'b00001), .out(shifter_2_out));
  assign bit_extender_5_out = {{12{IR[31]}}, IR[31:12]};  // Bit_Extender bit_extender_5
  or or_3 (IR2_t, IR2, IRB);
  Regifile regifile_1 (
    .Din(RDin), .Clk(CLK), .R1(regifile_1_r1), .R2(MDin), .WE(RegWrite), .W_num(IR[11:7]),
    .R1_num(multiplexer_2_out), .R2_num(multiplexer_3_out));
  Adder #(.width(32)) adder_2 (.a(shifter_1_out), .b(PC), .out(adder_2_out));  // open: cin, cout
  Adder #(.width(32)) adder_3 (.a(PC), .b(shifter_2_out), .out(adder_3_out));  // open: cin, cout
  Shifter #(.width(32), .shift("ll")) shifter_3 (.in(bit_extender_5_out), .\dist (5'b01100), .out(shifter_3_out));
  Button button_1 (.out(RST));
  Multiplexer #(.select(1), .width(32), .disabled("Z"), .enable("false")) multiplexer_5 (
    .in0(MDin), .in1(multiplexer_4_out), .out(multiplexer_5_out), .sel(AluSrc));
  Adder #(.width(32)) adder_4 (.a(shifter_3_out), .b(PC), .out(AUIPC_Result));  // open: cin, cout
  or or_4 (IR3_t, IR3, IRC);
  ALU alu_1 (
    .X(regifile_1_r1), .Y(multiplexer_5_out), .AluOP(\单周期硬布线控制器_1_alu_op ), .Equal(Equ), .Result(ALUResult),
    .out_6(Less));  // open: Result_2, out_4
  Comparator #(.width(32), .mode("twosComplement")) comparator_1 (
    .a(regifile_1_r1), .b(32'h22), .eq(comparator_1_eq));  // open: gt, lt
  not not_2 (not_2_out, CLK);
  not not_3 (not_3_out, comparator_1_eq);
  D_Flip_Flop #(.trigger("rising"), .Pre_Clr_Positions("ABOVE_BELOW"), .NegatePresetClear("false"), .enable("true"), .NewFFLayout("true")) d_ff_1 (
    .clk(not_2_out), .D(not_3_out), .Q(halt), .en(ecall), .reset(Go));  // open: Qn, preset
  and and_4 (and_4_out, comparator_1_eq, ecall);
  Register #(.width(32), .trigger("rising"), .Select("low")) register_1 (
    .D(MDin), .en(and_4_out), .Q(LedData), .clk(CLK));  // open: clr
  RAM #(.addrWidth(10), .dataWidth(32), .bus("separate"), .Select("high")) ram_1 (
    .addr(ALUResult[11:2]), .din(MDin), .data(MemData), .str(MemWrite), .sel(1'b1), .clk(CLK), .ld(1'b1),
    .clr(RST));
  Multiplexer #(.select(2), .width(8), .disabled("Z"), .enable("false")) multiplexer_6 (
    .in0(MemData[7:0]), .in1(MemData[15:8]), .in2(MemData[23:16]), .in3(MemData[31:24]),
    .out(multiplexer_6_out), .sel(ALUResult[1:0]));
  Multiplexer #(.select(1), .width(32), .disabled("Z"), .enable("false")) multiplexer_7 (
    .in0(MemData), .in1(bit_extender_6_out), .out(mux_out), .sel(LB));
  assign bit_extender_6_out = {{24{multiplexer_6_out[7]}}, multiplexer_6_out};  // Bit_Extender bit_extender_6
  LED #(.active("true")) \_1号中断等待指示灯  (.in(W1));
  or or_5 (W1, IR1_q, d_ff_2_q);
  or or_6 (W2, IR2_q, d_ff_3_q);
  LED #(.active("true")) \_2号中断等待指示灯  (.in(W2));
  LED #(.active("true")) \_3号中断等待指示灯  (.in(W3));
  or or_7 (W3, IR3_q, d_ff_4_q);
  Comparator #(.width(16), .mode("twosComplement")) comparator_2 (
    .a(\总周期数 ), .b({16{1'b0}}), .eq(comparator_2_eq));  // open: gt, lt
  D_Flip_Flop #(.trigger("rising"), .Pre_Clr_Positions("LEGACY"), .NegatePresetClear("false"), .enable("true"), .NewFFLayout("false")) d_ff_2 (
    .clk(IR1_t), .D(1'b1), .Q(d_ff_2_q), .reset(IR1_q));  // open: Qn, preset, en
  D_Flip_Flop #(.trigger("rising"), .Pre_Clr_Positions("LEGACY"), .NegatePresetClear("false"), .enable("true"), .NewFFLayout("false")) d_ff_3 (
    .clk(IR2_t), .D(1'b1), .Q(d_ff_3_q), .reset(IR2_q));  // open: Qn, preset, en
  D_Flip_Flop #(.trigger("rising"), .Pre_Clr_Positions("LEGACY"), .NegatePresetClear("false"), .enable("true"), .NewFFLayout("false")) d_ff_4 (
    .clk(IR3_t), .D(1'b1), .Q(d_ff_4_q), .reset(IR3_q));  // open: Qn, preset, en
  not not_4 (not_4_out, Interrupt);
  or or_8 (or_8_out, Interrupt, URET, comparator_2_eq);
  or or_9 (or_9_out, d_ff_2_q, IR1_q);
  or or_10 (or_10_out, d_ff_3_q, IR2_q);
  or or_11 (or_11_out, d_ff_4_q, IR3_q);
  not not_5 (not_5_out, halt);
  Register #(.width(1), .trigger("rising"), .Select("low")) u_IE (
    .D(not_4_out), .en(or_8_out), .Q(IE), .clk(CLK), .clr(RST));
  and and_5 (and_5_out, or_9_out, ~IR1_Reset);  // AND_Gate
  and and_6 (and_6_out, or_10_out, ~IR2_Reset);  // AND_Gate
  and and_7 (and_7_out, or_11_out, ~IR3_Reset);  // AND_Gate
  Counter #(.width(16), .max('hffff), .ongoal("wrap"), .trigger("rising"), .behavior("new")) counter_1 (
    .count(not_5_out), .Q(\总周期数 ), .clk(CLK));  // open: load, D, carry, clr, preset, down
  Comparator #(.width(16), .mode("twosComplement")) comparator_3 (
    .a(16'h23b), .b(\总周期数 ), .eq(comparator_3_eq));  // open: gt, lt
  Comparator #(.width(16), .mode("twosComplement")) comparator_4 (
    .a(\总周期数 ), .b(16'h1), .eq(comparator_4_eq));  // open: gt, lt
  Comparator #(.width(16), .mode("twosComplement")) comparator_5 (
    .a(\总周期数 ), .b(16'h4), .eq(comparator_5_eq));  // open: gt, lt
  Comparator #(.width(16), .mode("twosComplement")) comparator_6 (
    .a(\总周期数 ), .b(16'h7), .eq(comparator_6_eq));  // open: gt, lt
  D_Flip_Flop #(.trigger("rising"), .Pre_Clr_Positions("LEGACY"), .NegatePresetClear("false"), .enable("true"), .NewFFLayout("false")) u_IR1 (
    .clk(CLK), .D(and_5_out), .Q(IR1_q), .reset(RST));  // open: Qn, preset, en
  D_Flip_Flop #(.trigger("rising"), .Pre_Clr_Positions("LEGACY"), .NegatePresetClear("false"), .enable("true"), .NewFFLayout("false")) u_IR2 (
    .clk(CLK), .D(and_6_out), .Q(IR2_q), .reset(RST));  // open: Qn, preset, en
  D_Flip_Flop #(.trigger("rising"), .Pre_Clr_Positions("LEGACY"), .NegatePresetClear("false"), .enable("true"), .NewFFLayout("false")) u_IR3 (
    .clk(CLK), .D(and_7_out), .Q(IR3_q), .reset(RST));  // open: Qn, preset, en
  Register #(.width(2), .trigger("rising"), .Select("low")) register_2 (
    .D(IR_id), .en(Interrupt), .Q(register_2_q), .clk(CLK), .clr(RST));
  Demultiplexer #(.select(2), .width(1), .tristate("false"), .disabled("Z"), .enable("false")) demultiplexer_1 (
    .out1(IR1_Reset), .out2(IR2_Reset), .out3(IR3_Reset), .in(URET), .sel(register_2_q));  // open: out0
  Register #(.width(32), .trigger("rising"), .Select("low")) u_EPC (
    .D(PC_Ori), .en(Interrupt), .Q(EPC), .clk(CLK), .clr(RST));
  or or_12 (or_12_out, comparator_3_eq, comparator_4_eq);
  assign IRA = or_12_out ? ~CLK : 1'bz;  // Controlled_Inverter controlled_inverter_1
  assign IRB = comparator_5_eq ? ~CLK : 1'bz;  // Controlled_Inverter controlled_inverter_2
  assign IRC = comparator_6_eq ? ~CLK : 1'bz;  // Controlled_Inverter controlled_inverter_3
  Priority_Encoder #(.select(2), .disabled("Z")) priority_encoder_2 (
    .in1(IR1_q), .in2(IR2_q), .in3(IR3_q), .out(IR_id), .gs(priority_encoder_2_gs));  // open: in0, en_out, en_in
  or or_13 (or_13_out[0], MemToReg, AUIPC);
  Pull_Resistor #(.pull(0)) pull_resistor_1 (.node(IRA));
  Pull_Resistor #(.pull(0)) pull_resistor_2 (.node(IRB));
  Pull_Resistor #(.pull(0)) pull_resistor_3 (.node(IRC));
  and and_8 (Interrupt, priority_encoder_2_gs, IE);
  Multiplexer #(.select(2), .width(32), .disabled("Z"), .enable("false")) multiplexer_8 (
    .in0(ALUResult), .in1(mux_out), .in2(PC_4), .in3(AUIPC_Result), .out(RDin), .sel(or_13_out));
  or or_14 (or_13_out[1], AUIPC, JAL, JALR);
  Multiplexer #(.select(2), .width(32), .disabled("Z"), .enable("false")) multiplexer_9 (
    .in1(32'h30ac), .in2(32'h3150), .in3(32'h31f4), .out(multiplexer_9_out), .sel(IR_id));  // open: in0
  Multiplexer #(.select(1), .width(32), .disabled("Z"), .enable("false")) multiplexer_10 (
    .in0(PC_Ori), .in1(multiplexer_9_out), .out(multiplexer_10_out), .sel(Interrupt));
  Multiplexer #(.select(1), .width(32), .disabled("Z"), .enable("false")) multiplexer_11 (
    .in0(multiplexer_10_out), .in1(EPC), .out(PC_Next), .sel(URET));

  // Notes on the sheet:
  //   中断源
  //   中断等待指示
  //   总复位信号应将除ROM以外所有存储组件全部清零
  //   数码管输出
  //   指令探针
  //   指令存储器
  //   数码管输出应该用寄存器锁存，否则显示数据只能一闪而过
  //   contents of rom_1 (hex, n*v repeats v):
  //   7d000113 100413 1f41993 41f9d993 433 c00913 800b13 140413 f47413 800293 100313 499993 89e9b3 1300533
  //   2200893 73 406282b3 fe0294e3 140413 f00f93 1f47433 1c41413 800293 100313 49d993 89e9b3 1300533
  //   2200893 73 406282b3 fe0294e3 1c45413 406b0b33 b0463 f95ff06f 2b3 fff2c293 1029293 fff2e293 500533
  //   2200893 73 f5dff06f 1112023 410113 a12023 410113 812023 410113 1312023 410113 1412023 410113 1512023
  //   410113 1612023 410113 100b13 300a13 100a93 1600433 441413 14469b3 1300533 2200893 73 fe0416e3
  //   415a0a33 fe0a10e3 ffc10113 12b03 ffc10113 12a83 ffc10113 12a03 ffc10113 12983 ffc10113 12403
  //   ffc10113 12503 ffc10113 12883 200073 1112023 410113 a12023 410113 812023 410113 1312023 410113
  //   1412023 410113 1512023 410113 1612023 410113 200b13 300a13 100a93 1600433 441413 14469b3 1300533
  //   2200893 73 fe0416e3 415a0a33 fe0a10e3 ffc10113 12b03 ffc10113 12a83 ffc10113 12a03 ffc10113 12983
  //   ffc10113 12403 ffc10113 12503 ffc10113 12883 200073 1112023 410113 a12023 410113 812023 410113
  //   1312023 410113 1412023 410113 1512023 410113 1612023 410113 300b13 300a13 100a93 1600433 441413
  //   14469b3 1300533 2200893 73 fe0416e3 415a0a33 fe0a10e3 ffc10113 12b03 ffc10113 12a83 ffc10113 12a03
  //   ffc10113 12983 ffc10113 12403 ffc10113 12503 ffc10113 12883 200073
  //   JAL
  //   JALR
  //   指令字
  //   S
  //   J
  //   U_Type
  //   Beq
  //   Bne
  //   MemToReg
  //   MemWrite
  //   AluOP
  //   AluSrc
  //   RegWrite
  //   S_type
  //   ecall
  //   I
  //   B
  //   清零按钮
  //   为方便自动评测，需要输出PC，IR，寄存器堆写如数据RDin
  //   RAM写使能MemWrite、RAM写入数据MDin等信号
  //   数据存储器
  //   单级中断测试信号模拟器
  //   Reset 
  //   Reset 
  //   Reset 
endmodule

module \单周期_多级中断  (
  input  IR1,
  input  IR2,
  input  IR3,
  output RegWrite,
  output MemWrite,
  output [31:0] PC,
  output [31:0] IR,
  output [31:0] RDin,
  output [31:0] MDin,
  output [31:0] LedData
);

  wire AluSrcB, and_1_out, and_2_out, and_3_out, and_4_out, and_5_out, and_6_out, and_7_out, and_10_out,
       and_11_out, and_12_out, and_13_out, and_14_out, and_15_out, AUIPC, Beq, BLTU, Bne, CLK,
       comparator_1_eq, comparator_2_eq, comparator_3_eq, comparator_4_eq, comparator_5_eq, comparator_6_eq,
       comparator_7_eq, comparator_8_eq, comparator_9_eq, CSR, CSRRCI, CSRRSI, d_ff_2_q, d_ff_3_q, d_ff_4_q,
       decoder_2_out0, decoder_2_out1, decoder_2_out2, ecall, Equ, Go, halt, IE, Interrupt, IR1_q, IR1_Reset,
       IR1_t, IR2_q, IR2_Reset, IR2_t, IR3_q, IR3_Reset, IR3_t, IRA, IRB, IRC, JAL, JALR, LB, Less, MemToReg,
       not_1_out, not_2_out, not_3_out, not_4_out, or_1_out, or_5_out, or_10_out, or_11_out, or_12_out,
       or_13_out, or_14_out, or_16_out, or_17_out, Priority, priority_encoder_2_gs, pull_resistor_1_node,
       pull_resistor_2_node, pull_resistor_3_node, RST, S_type, URET, W1, W2, W3;
  wire [1:0] adder_5_out, exist, IR_id, IR_id_CUR, IRNum1_q, IRNum2_q, IRNum3_q, multiplexer_8_out, or_9_out,
       priority_encoder_1_out;
  wire [3:0] \单周期硬布线控制器_1_alu_op ;
  wire [4:0] multiplexer_2_out, multiplexer_3_out;
  wire [7:0] multiplexer_6_out;
  wire [15:0] \总周期数 ;
  wire [31:0] adder_2_out, adder_3_out, ALUResult, AUIPC_Result, bit_extender_1_out, bit_extender_2_out,
       bit_extender_3_out, bit_extender_4_out, bit_extender_5_out, bit_extender_6_out, EPC, EPC1_q, EPC2_q,
       EPC3_q, MemData, multiplexer_4_out, multiplexer_5_out, multiplexer_12_out, multiplexer_13_out,
       mux_out, PC_4, PC_Next, PC_Ori, regifile_1_r1, shifter_1_out, shifter_2_out, shifter_3_out;

  Clock #(.highDuration(1), .lowDuration(1)) clock_1 (.out(CLK));
  Button _1 (.out(IRA));
  Button _2 (.out(IRB));
  Button _3 (.out(IRC));
  Button \u_继续运行  (.out(Go));
  LED #(.active("true")) led_1 (.in(W1));
  LED #(.active("true")) led_2 (.in(W2));
  LED #(.active("true")) led_3 (.in(W3));
  Multiplexer #(.select(2), .width(32), .disabled("Z"), .enable("false")) multiplexer_1 (
    .in0(PC_4), .in1(ALUResult), .in2(adder_3_out), .in3(adder_2_out), .out(PC_Ori),
    .sel(priority_encoder_1_out));
  Hex_Digit_Display hex_digit_display_1 (.value(LedData[31:28]));  // open: dp
  Priority_Encoder #(.select(2), .disabled("Z")) priority_encoder_1 (
    .in0(1'b1), .in1(JALR), .in2(JAL), .in3(or_1_out), .out(priority_encoder_1_out));  // open: gs, en_out, en_in
  not not_1 (not_1_out, halt);
  Hex_Digit_Display hex_digit_display_2 (.value(LedData[27:24]));  // open: dp
  Hex_Digit_Display hex_digit_display_3 (.value(LedData[23:20]));  // open: dp
  or or_1 (or_1_out, and_1_out, and_2_out, and_3_out);
  Register #(.width(32), .trigger("rising"), .Select("low")) u_PC (
    .D(PC_Next), .en(not_1_out), .Q(PC), .clk(CLK), .clr(RST));
  Hex_Digit_Display hex_digit_display_4 (.value(LedData[19:16]));  // open: dp
  Hex_Digit_Display hex_digit_display_5 (.value(LedData[15:12]));  // open: dp
  and and_1 (and_1_out, BLTU, Less);
  and and_2 (and_2_out, Beq, Equ);
  and and_3 (and_3_out, ~Equ, Bne);  // AND_Gate
  // RiscV_Probe riscv_probe_1: pin names not known; wires that end beside it: IR
  Adder #(.width(32)) adder_1 (.a(PC), .b(32'h4), .out(PC_4));  // open: cin, cout
  Hex_Digit_Display hex_digit_display_6 (.value(LedData[11:8]));  // open: dp
  Hex_Digit_Display hex_digit_display_7 (.value(LedData[7:4]));  // open: dp
  // Probe on \总周期数 
  ROM #(.addrWidth(10), .dataWidth(32), .Select("high")) rom_1 (.addr(PC[11:2]), .data(IR));
  Hex_Digit_Display hex_digit_display_8 (.value(LedData[3:0]));  // open: dp
  Multiplexer #(.select(1), .width(5), .disabled("Z"), .enable("false")) multiplexer_2 (
    .in0(IR[19:15]), .in1(5'b10001), .out(multiplexer_2_out), .sel(ecall));
  Multiplexer #(.select(1), .width(5), .disabled("Z"), .enable("false")) multiplexer_3 (
    .in0(IR[24:20]), .in1(5'b01010), .out(multiplexer_3_out), .sel(ecall));
  \单周期硬布线控制器  \u_单周期硬布线控制器_1  (
    .Funct({IR[30], IR[25], IR[14:12]}), .OP(IR[6:2]), .ALU_OP(\单周期硬布线控制器_1_alu_op ), .MemToReg(MemToReg),
    .MemWrite(MemWrite), .ALU_SRC(AluSrcB), .RegWrite(RegWrite), .ecall(ecall), .S_type(S_type), .JALR(JALR),
    .BEQ(Beq), .JAL(JAL), .BNE(Bne), .in_3(IR[21]), .uret(URET), .BLTU(BLTU), .LB(LB), .U_Type(AUIPC),
    .CSR(CSR));  // open: rs1_used, rs2_used, SLTIU
  // Probe on multiplexer_2_out
  // Probe on multiplexer_3_out
  // Probe on IR[11:7]
  assign bit_extender_1_out = {{20{IR[31]}}, IR[31:20]};  // Bit_Extender bit_extender_1
  assign bit_extender_2_out = {{20{IR[31]}}, {IR[31:25], IR[11:7]}};  // Bit_Extender bit_extender_2
  assign bit_extender_3_out = {{20{IR[31]}}, {IR[31], IR[7], IR[30:25], IR[11:8]}};  // Bit_Extender bit_extender_3
  assign bit_extender_4_out = {{12{IR[31]}}, {IR[31], IR[19:12], IR[20], IR[30:21]}};  // Bit_Extender bit_extender_4
  assign bit_extender_5_out = {{12{IR[31]}}, IR[31:12]};  // Bit_Extender bit_extender_5
  or or_2 (IR1_t, IR1, IRA);
  Multiplexer #(.select(1), .width(32), .disabled("Z"), .enable("false")) multiplexer_4 (
    .in0(bit_extender_1_out), .in1(bit_extender_2_out), .out(multiplexer_4_out), .sel(S_type));
  Shifter #(.width(32), .shift("ll")) shifter_1 (.in(bit_extender_3_out), .\dist (5'b00001), .out(shifter_1_out));
  Shifter #(.width(32), .shift("ll")) shifter_2 (.in(bit_extender_4_out), .\dist (5'b00001), .out(shifter_2_out));
  Shifter #(.width(32), .shift("ll")) shifter_3 (.in(bit_extender_5_out), .\dist (5'b01100), .out(shifter_3_out));
  or or_3 (IR2_t, IR2, IRB);
  Regifile regifile_1 (
    .Din(RDin), .Clk(CLK), .R1(regifile_1_r1), .R2(MDin), .WE(RegWrite), .W_num(IR[11:7]),
    .R1_num(multiplexer_2_out), .R2_num(multiplexer_3_out));
  Adder #(.width(32)) adder_2 (.a(shifter_1_out), .b(PC), .out(adder_2_out));  // open: cin, cout
  Adder #(.width(32)) adder_3 (.a(PC), .b(shifter_2_out), .out(adder_3_out));  // open: cin, cout
  Button button_1 (.out(RST));
  Multiplexer #(.select(1), .width(32), .disabled("Z"), .enable("false")) multiplexer_5 (
    .in0(MDin), .in1(multiplexer_4_out), .out(multiplexer_5_out), .sel(AluSrcB));
  Adder #(.width(32)) adder_4 (.a(shifter_3_out), .b(PC), .out(AUIPC_Result));  // open: cin, cout
  or or_4 (IR3_t, IR3, IRC);
  ALU alu_1 (
    .X(regifile_1_r1), .Y(multiplexer_5_out), .AluOP(\单周期硬布线控制器_1_alu_op ), .Equal(Equ), .Result(ALUResult),
    .out_6(Less));  // open: Result_2, out_4
  Comparator #(.width(32), .mode("twosComplement")) comparator_1 (
    .a(regifile_1_r1), .b(32'h22), .eq(comparator_1_eq));  // open: gt, lt
  not not_2 (not_2_out, CLK);
  not not_3 (not_3_out, comparator_1_eq);
  D_Flip_Flop #(.trigger("rising"), .Pre_Clr_Positions("ABOVE_BELOW"), .NegatePresetClear("false"), .enable("true"), .NewFFLayout("true")) d_ff_1 (
    .clk(not_2_out), .D(not_3_out), .Q(halt), .en(ecall), .reset(Go));  // open: Qn, preset
  and and_4 (and_4_out, comparator_1_eq, ecall);
  Register #(.width(32), .trigger("rising"), .Select("low")) register_1 (
    .D(MDin), .en(and_4_out), .Q(LedData), .clk(CLK));  // open: clr
  RAM #(.addrWidth(10), .dataWidth(32), .bus("separate"), .Select("high")) ram_1 (
    .addr(ALUResult[11:2]), .din(MDin), .data(MemData), .str(MemWrite), .sel(1'b1), .clk(CLK), .ld(1'b1),
    .clr(RST));
  Multiplexer #(.select(2), .width(8), .disabled("Z"), .enable("false")) multiplexer_6 (
    .in0(MemData[7:0]), .in1(MemData[15:8]), .in2(MemData[23:16]), .in3(MemData[31:24]),
    .out(multiplexer_6_out), .sel(ALUResult[1:0]));
  Multiplexer #(.select(1), .width(32), .disabled("Z"), .enable("false")) multiplexer_7 (
    .in0(MemData), .in1(bit_extender_6_out), .out(mux_out), .sel(LB));
  assign bit_extender_6_out = {{24{multiplexer_6_out[7]}}, multiplexer_6_out};  // Bit_Extender bit_extender_6
  LED #(.active("true")) \_1号中断等待指示灯  (.in(W1));
  LED #(.active("true")) \_2号中断等待指示灯  (.in(W2));
  LED #(.active("true")) \_3号中断等待指示灯  (.in(W3));
  Multiplexer #(.select(1), .width(2), .disabled("Z"), .enable("false")) multiplexer_8 (
    .in0(2'b11), .in1(2'b01), .out(multiplexer_8_out), .sel(Interrupt));
  Pull_Resistor #(.pull(0)) pull_resistor_1 (.node(pull_resistor_1_node));
  Adder #(.width(2)) adder_5 (.a(exist), .b(multiplexer_8_out), .out(adder_5_out));  // open: cin, cout
  or or_5 (or_5_out, Interrupt, URET);
  or or_6 (W1, IR1_q, d_ff_2_q);
  or or_7 (W2, IR2_q, d_ff_3_q);
  or or_8 (W3, IR3_q, d_ff_4_q);
  not not_4 (not_4_out, halt);
  Comparator #(.width(16), .mode("twosComplement")) comparator_2 (
    .a(\总周期数 ), .b({16{1'b0}}), .eq(comparator_2_eq));  // open: gt, lt
  Pull_Resistor #(.pull(0)) pull_resistor_2 (.node(pull_resistor_2_node));
  Pull_Resistor #(.pull(0)) pull_resistor_3 (.node(pull_resistor_3_node));
  Decoder #(.select(2), .tristate("false"), .disabled("Z"), .enable("false")) decoder_1 (
    .out1(pull_resistor_2_node), .out2(pull_resistor_3_node), .out3(pull_resistor_1_node), .sel(IR_id));  // open: out0
  Register #(.width(2), .trigger("rising"), .Select("low")) register_2 (
    .D(adder_5_out), .en(or_5_out), .Q(exist), .clk(CLK), .clr(RST));
  D_Flip_Flop #(.trigger("rising"), .Pre_Clr_Positions("LEGACY"), .NegatePresetClear("false"), .enable("true"), .NewFFLayout("false")) d_ff_2 (
    .clk(IR1_t), .D(1'b1), .Q(d_ff_2_q), .reset(IR1_q));  // open: Qn, preset, en
  D_Flip_Flop #(.trigger("rising"), .Pre_Clr_Positions("LEGACY"), .NegatePresetClear("false"), .enable("true"), .NewFFLayout("false")) d_ff_3 (
    .clk(IR2_t), .D(1'b1), .Q(d_ff_3_q), .reset(IR2_q));  // open: Qn, preset, en
  D_Flip_Flop #(.trigger("rising"), .Pre_Clr_Positions("LEGACY"), .NegatePresetClear("false"), .enable("true"), .NewFFLayout("false")) d_ff_4 (
    .clk(IR3_t), .D(1'b1), .Q(d_ff_4_q), .reset(IR3_q));  // open: Qn, preset, en
  or or_9 (or_9_out[0], MemToReg, AUIPC);
  Counter #(.width(16), .max('hffff), .ongoal("wrap"), .trigger("rising"), .behavior("new")) counter_1 (
    .count(not_4_out), .Q(\总周期数 ), .clk(CLK));  // open: load, D, carry, clr, preset, down
  or or_10 (or_10_out, CSRRSI, ~Interrupt);  // OR_Gate
  or or_11 (or_11_out, Interrupt, URET, comparator_2_eq, CSRRCI, CSRRSI);
  Comparator #(.width(3), .mode("twosComplement")) comparator_3 (
    .a(3'b111), .b(IR[14:12]), .eq(comparator_3_eq));  // open: gt, lt
  Comparator #(.width(3), .mode("twosComplement")) comparator_4 (
    .a(IR[14:12]), .b(3'b110), .eq(comparator_4_eq));  // open: gt, lt
  and and_5 (and_5_out, pull_resistor_2_node, Interrupt);
  and and_6 (and_6_out, pull_resistor_3_node, Interrupt);
  and and_7 (and_7_out, pull_resistor_1_node, Interrupt);
  Decoder #(.select(2), .tristate("false"), .disabled("Z"), .enable("false")) decoder_2 (
    .out0(decoder_2_out0), .out1(decoder_2_out1), .out2(decoder_2_out2), .sel(exist));  // open: out3
  or or_12 (or_12_out, d_ff_2_q, IR1_q);
  or or_13 (or_13_out, d_ff_3_q, IR2_q);
  or or_14 (or_14_out, d_ff_4_q, IR3_q);
  Multiplexer #(.select(2), .width(32), .disabled("Z"), .enable("false")) multiplexer_9 (
    .in0(ALUResult), .in1(mux_out), .in2(PC_4), .in3(AUIPC_Result), .out(RDin), .sel(or_9_out));
  or or_15 (or_9_out[1], AUIPC, JAL, JALR);
  Register #(.width(1), .trigger("rising"), .Select("low")) u_IE (
    .D(or_10_out), .en(or_11_out), .Q(IE), .clk(CLK), .clr(RST));
  and and_8 (CSRRCI, comparator_3_eq, CSR);
  and and_9 (CSRRSI, CSR, comparator_4_eq);
  Register #(.width(32), .trigger("rising"), .Select("low")) EPC1 (
    .D(PC_Ori), .en(and_5_out), .Q(EPC1_q), .clk(CLK), .clr(RST));
  Register #(.width(32), .trigger("rising"), .Select("low")) EPC2 (
    .D(PC_Ori), .en(and_6_out), .Q(EPC2_q), .clk(CLK), .clr(RST));
  Register #(.width(32), .trigger("rising"), .Select("low")) EPC3 (
    .D(PC_Ori), .en(and_7_out), .Q(EPC3_q), .clk(CLK), .clr(RST));
  and and_10 (and_10_out, decoder_2_out0, Interrupt);
  and and_11 (and_11_out, decoder_2_out1, Interrupt);
  and and_12 (and_12_out, decoder_2_out2, Interrupt);
  Comparator #(.width(16), .mode("twosComplement")) comparator_5 (
    .a(16'h258), .b(\总周期数 ), .eq(comparator_5_eq));  // open: gt, lt
  Comparator #(.width(16), .mode("twosComplement")) comparator_6 (
    .a(\总周期数 ), .b(16'h1), .eq(comparator_6_eq));  // open: gt, lt
  Comparator #(.width(16), .mode("twosComplement")) comparator_7 (
    .a(\总周期数 ), .b(16'h4), .eq(comparator_7_eq));  // open: gt, lt
  Comparator #(.width(16), .mode("twosComplement")) comparator_8 (
    .a(\总周期数 ), .b(16'h7), .eq(comparator_8_eq));  // open: gt, lt
  Comparator #(.width(16), .mode("twosComplement")) comparator_9 (
    .a(\总周期数 ), .b(16'h241), .eq(comparator_9_eq));  // open: gt, lt
  and and_13 (and_13_out, or_12_out, ~IR1_Reset);  // AND_Gate
  and and_14 (and_14_out, or_13_out, ~IR2_Reset);  // AND_Gate
  and and_15 (and_15_out, or_14_out, ~IR3_Reset);  // AND_Gate
  Multiplexer #(.select(2), .width(32), .disabled("Z"), .enable("false")) multiplexer_10 (
    .in1(EPC1_q), .in2(EPC2_q), .in3(EPC3_q), .out(EPC), .sel(IR_id_CUR));  // open: in0
  Register #(.width(2), .trigger("rising"), .Select("low")) IRNum1 (
    .D(IR_id), .en(and_10_out), .Q(IRNum1_q), .clk(CLK), .clr(RST));
  Register #(.width(2), .trigger("rising"), .Select("low")) IRNum2 (
    .D(IR_id), .en(and_11_out), .Q(IRNum2_q), .clk(CLK), .clr(RST));
  Register #(.width(2), .trigger("rising"), .Select("low")) IRNum3 (
    .D(IR_id), .en(and_12_out), .Q(IRNum3_q), .clk(CLK), .clr(RST));
  or or_16 (or_16_out, comparator_5_eq, comparator_6_eq);
  assign IRA = or_16_out ? ~CLK : 1'bz;  // Controlled_Inverter controlled_inverter_1
  assign IRB = comparator_7_eq ? ~CLK : 1'bz;  // Controlled_Inverter controlled_inverter_2
  or or_17 (or_17_out, comparator_8_eq, comparator_9_eq);
  assign IRC = or_17_out ? ~CLK : 1'bz;  // Controlled_Inverter controlled_inverter_3
  D_Flip_Flop #(.trigger("rising"), .Pre_Clr_Positions("LEGACY"), .NegatePresetClear("false"), .enable("true"), .NewFFLayout("false")) u_IR1 (
    .clk(CLK), .D(and_13_out), .Q(IR1_q), .reset(RST));  // open: Qn, preset, en
  D_Flip_Flop #(.trigger("rising"), .Pre_Clr_Positions("LEGACY"), .NegatePresetClear("false"), .enable("true"), .NewFFLayout("false")) u_IR2 (
    .clk(CLK), .D(and_14_out), .Q(IR2_q), .reset(RST));  // open: Qn, preset, en
  D_Flip_Flop #(.trigger("rising"), .Pre_Clr_Positions("LEGACY"), .NegatePresetClear("false"), .enable("true"), .NewFFLayout("false")) u_IR3 (
    .clk(CLK), .D(and_15_out), .Q(IR3_q), .reset(RST));  // open: Qn, preset, en
  Multiplexer #(.select(2), .width(2), .disabled("Z"), .enable("false")) multiplexer_11 (
    .in1(IRNum1_q), .in2(IRNum2_q), .in3(IRNum3_q), .out(IR_id_CUR), .sel(exist));  // open: in0
  Pull_Resistor #(.pull(0)) pull_resistor_4 (.node(IRA));
  Pull_Resistor #(.pull(0)) pull_resistor_5 (.node(IRB));
  Pull_Resistor #(.pull(0)) pull_resistor_6 (.node(IRC));
  Priority_Encoder #(.select(2), .disabled("Z")) priority_encoder_2 (
    .in1(IR1_q), .in2(IR2_q), .in3(IR3_q), .out(IR_id), .gs(priority_encoder_2_gs));  // open: in0, en_out, en_in
  Demultiplexer #(.select(2), .width(1), .tristate("false"), .disabled("Z"), .enable("false")) demultiplexer_1 (
    .out1(IR1_Reset), .out2(IR2_Reset), .out3(IR3_Reset), .in(URET), .sel(IR_id));  // open: out0
  Comparator #(.width(2), .mode("unsigned")) comparator_10 (.a(IR_id_CUR), .b(IR_id), .lt(Priority));  // open: gt, eq
  Pull_Resistor #(.pull(1)) pull_resistor_7 (.node(Priority));
  Multiplexer #(.select(2), .width(32), .disabled("Z"), .enable("false")) multiplexer_12 (
    .in1(32'h30ac), .in2(32'h3158), .in3(32'h3204), .out(multiplexer_12_out), .sel(IR_id));  // open: in0
  and and_16 (Interrupt, priority_encoder_2_gs, Priority, IE);
  Pull_Resistor #(.pull(0)) pull_resistor_8 (.node(IR1_Reset));
  Pull_Resistor #(.pull(0)) pull_resistor_9 (.node(IR2_Reset));
  Pull_Resistor #(.pull(0)) pull_resistor_10 (.node(IR3_Reset));
  Multiplexer #(.select(1), .width(32), .disabled("Z"), .enable("false")) multiplexer_13 (
    .in0(PC_Ori), .in1(multiplexer_12_out), .out(multiplexer_13_out), .sel(Interrupt));
  Multiplexer #(.select(1), .width(32), .disabled("Z"), .enable("false")) multiplexer_14 (
    .in0(multiplexer_13_out), .in1(EPC), .out(PC_Next), .sel(URET));

  // Other names for the same wires on the sheet: Funt3[2:0] = IR[14:12]

  // Notes on the sheet:
  //   中断源
  //   中断等待指示
  //   总复位信号应将除ROM以外所有存储组件全部清零
  //   数码管输出
  //   指令探针
  //   指令存储器
  //   数码管输出应该用寄存器锁存，否则显示数据只能一闪而过
  //   contents of rom_1 (hex, n*v repeats v):
  //   100493 100006f 100493 200913 300993 100006f 100493 200913 300993 100006f 100493 200913 300993
  //   100006f 100493 200913 300993 408000ef 100413 100493 1f49493 900533 2200893 73 24d493 48463 fedff06f
  //   900533 2200893 73 100493 249493 900533 2200893 73 48463 fedff06f 100493 1f49493 900533 2200893 73
  //   4034d493 900533 2200893 73 4044d493 900533 2200893 73 4044d493 900533 2200893 73 4044d493 900533
  //   2200893 73 4044d493 900533 2200893 73 4044d493 900533 2200893 73 4044d493 900533 2200893 73 4044d493
  //   900533 2200893 73 100413 1f41993 41f9d993 433 c00913 300b13 140413 f47413 800293 100313 499993
  //   89e9b3 1300533 2200893 73 406282b3 fe0294e3 140413 f00f93 1f47433 1c41413 800293 100313 49d993
  //   89e9b3 1300533 2200893 73 406282b3 fe0294e3 1c45413 406b0b33 b0463 f95ff06f 2b3 fff2c293 829293
  //   ff2e293 500533 2200893 73 fff00413 493 84a023 140413 448493 84a023 140413 448493 84a023 140413
  //   448493 84a023 140413 448493 84a023 140413 448493 84a023 140413 448493 84a023 140413 448493 84a023
  //   140413 448493 84a023 140413 448493 84a023 140413 448493 84a023 140413 448493 84a023 140413 448493
  //   84a023 140413 448493 84a023 140413 448493 84a023 140413 448493 84a023 140413 448493 140413 433
  //   3c00493 42983 4aa03 149a2b3 28663 134a023 1442023 ffc48493 fe9412e3 800533 2200893 73 440413 3c00493
  //   fc9416e3 a00893 73 13 430497 900533 2200893 73 430497 900533 2200893 73 430497 900533 2200893 73
  //   430497 900533 2200893 73 430497 900533 2200893 73 430497 900533 2200893 73 430497 900533 2200893 73
  //   430497 900533 2200893 73 a00893 73 fff00293 313 1900413 841413 9700493 940533 2200893 73 5484b3
  //   494b313 fe0306e3 a00893 73 313 1000e13 8400493 849493 8348493 400913 891913 490913 849493 8248493
  //   849493 8148493 891913 490913 891913 490913 932023 12484b3 430313 fffe0e13 fe0e18e3 2000e13 313 31483
  //   900533 2200893 73 230313 fffe0e13 fe0e14e3 a00893 73 ff100493 900533 2200893 73 148493 fe9068e3
  //   900533 2200893 73 a00893 73 413 140413 800533 2200893 73 240413 800533 2200893 73 340413 800533
  //   2200893 73 440413 800533 2200893 73 540413 800533 2200893 73 640413 800533 2200893 73 740413 800533
  //   2200893 73 840413 800533 2200893 2200893 73 8067
  //   JAL
  //   JALR
  //   指令字
  //   S
  //   J
  //   U_Type
  //   Beq
  //   Bne
  //   MemToReg
  //   MemWrite
  //   AluOP
  //   AluSrcB
  //   RegWrite
  //   S_type
  //   ecall
  //   I
  //   B
  //   清零按钮
  //   为方便自动评测，需要输出PC，IR，寄存器堆写如数据RDin
  //   RAM写使能MemWrite、RAM写入数据MDin等信号
  //   数据存储器
  //   多级中断测试信号模拟器
  //   Reset 
  //   Reset 
  //   Reset 
endmodule

module \封装正确性测试  (
);

  wire IR1, IR2, IR3, MemW, RegW;
  wire [31:0] EX_PC, ID_PC, IF_PC, IR, LED, MDin, MDinr, MEM_PC, PC, RDin, RDinr, WB_PC;

  \单周期RISC_V  \u_单周期risc_v_1  (
    .IR1(IR1), .IR2(IR2), .IR3(IR3), .RegWrite(RegW), .MemWrite(MemW), .PC(PC), .IR(IR), .RDin(RDin),
    .MDin(MDin), .LedData(LED));
  \气泡流水线  \u_气泡流水线_1  (
    .RegWrite(RegW), .MemWrite(MemW), .IF_PC(IF_PC), .ID_PC(ID_PC), .EX_PC(EX_PC), .M_PC(MEM_PC),
    .WB_PC(WB_PC), .RDin(RDinr), .MDin(MDinr), .LedData(LED));
  \动态分支预测  \u_动态分支预测_1  ();  // open: RegWrite, MemWrite, IF_PC, ID_PC, EX_PC, M_PC, WB_PC, RDin, MDin, LedData
  \单周期_单级中断  \u_单周期_单级中断_1  (
    .IR1(IR1), .IR2(IR2), .IR3(IR3), .RegWrite(RegW), .MemWrite(MemW), .PC(PC), .IR(IR), .RDin(RDin),
    .MDin(MDin), .LedData(LED));
  \理想流水线  \u_理想流水线_1  (
    .RegWrite(RegW), .MemWrite(MemW), .IF_PC(IF_PC), .ID_PC(ID_PC), .EX_PC(EX_PC), .M_PC(MEM_PC),
    .WB_PC(WB_PC), .RDin(RDinr), .MDin(MDinr), .LedData(LED));
  \重定向流水线  \u_重定向流水线_1  (
    .RegWrite(RegW), .MemWrite(MemW), .IF_PC(IF_PC), .ID_PC(ID_PC), .EX_PC(EX_PC), .M_PC(MEM_PC),
    .WB_PC(WB_PC), .RDin(RDinr), .MDin(MDinr), .LedData(LED));
  \单周期_多级中断  \u_单周期_多级中断_1  (
    .IR1(IR1), .IR2(IR2), .IR3(IR3), .RegWrite(RegW), .MemWrite(MemW), .PC(PC), .IR(IR), .RDin(RDin),
    .MDin(MDin), .LedData(LED));

  // Notes on the sheet:
  //   单周期封装测试
  //   气泡流水封装测试
  //   单周期+单级中断封装测试
  //   请检查上面封装有无位宽不匹配，引脚标签是否和连接的标签相对应，否则无法在educoder平台上正确测试
  //   理想流水封装测试
  //   重定向流水封装测试
  //   单周期+多级中断封装测试
endmodule

module IF_ID (
  input  [31:0] IR,
  input  [31:0] PC,
  input  [31:0] PC_4,
  input  IF_PredictJump,
  input  branch,
  input  reset,
  input  en,
  input  clk,
  output [31:0] IR_2,
  output [31:0] PC_2,
  output [31:0] PC_4_2,
  output ID_PredictJump
);

  wire multiplexer_4_out, or_1_out;
  wire [31:0] multiplexer_1_out, multiplexer_2_out, multiplexer_3_out;

  Multiplexer #(.select(1), .width(32), .disabled("Z"), .enable("false")) multiplexer_1 (
    .in0(IR), .in1({32{1'b0}}), .out(multiplexer_1_out), .sel(or_1_out));
  Multiplexer #(.select(1), .width(32), .disabled("Z"), .enable("false")) multiplexer_2 (
    .in0(PC), .in1({32{1'b0}}), .out(multiplexer_2_out), .sel(or_1_out));
  Multiplexer #(.select(1), .width(32), .disabled("Z"), .enable("false")) multiplexer_3 (
    .in0(PC_4), .in1({32{1'b0}}), .out(multiplexer_3_out), .sel(or_1_out));
  Multiplexer #(.select(1), .width(1), .disabled("Z"), .enable("false")) multiplexer_4 (
    .in0(IF_PredictJump), .in1(1'b0), .out(multiplexer_4_out), .sel(or_1_out));
  or or_1 (or_1_out, branch, reset);
  Register #(.width(32), .trigger("rising"), .Select("low")) register_1 (
    .D(multiplexer_1_out), .en(en), .Q(IR_2), .clk(clk));  // open: clr
  Register #(.width(32), .trigger("rising"), .Select("low")) register_2 (
    .D(multiplexer_2_out), .en(en), .Q(PC_2), .clk(clk));  // open: clr
  Register #(.width(32), .trigger("rising"), .Select("low")) register_3 (
    .D(multiplexer_3_out), .en(en), .Q(PC_4_2), .clk(clk));  // open: clr
  Register #(.width(1), .trigger("rising"), .Select("low")) register_4 (
    .D(multiplexer_4_out), .en(en), .Q(ID_PredictJump), .clk(clk));  // open: clr
endmodule

module ID_EX (
  input  SLTIU,
  input  U_Type,
  input  BEQ,
  input  BNE,
  input  MemToReg,
  input  MemWrite,
  input  AluSrc,
  input  RegWrite,
  input  S_type,
  input  ecall,
  input  Jal,
  input  Jalr,
  input  LB,
  input  BLTU,
  input  Uret,
  input  [3:0] AluOP,
  input  [4:0] rd,
  input  [31:0] R1,
  input  [31:0] R2,
  input  [31:0] imm_1,
  input  [31:0] imm_2,
  input  [31:0] PC,
  input  [31:0] PC_4,
  input  [31:0] IR,
  input  [31:0] AUIPC_result,
  input  [1:0] RS1_Forward,
  input  [1:0] RS2_Forward,
  input  ID_PredictJump,
  input  reset,
  input  flush,
  input  en,
  input  clk,
  output SLTIU_2,
  output U_Type_2,
  output BEQ_2,
  output BNE_2,
  output MemToReg_2,
  output MemWrite_2,
  output AluSrc_2,
  output RegWrite_2,
  output S_type_2,
  output ecall_2,
  output Jal_2,
  output Jalr_2,
  output LB_2,
  output BLTU_2,
  output Uret_2,
  output [3:0] AluOP_2,
  output [4:0] rd_2,
  output [31:0] R1_2,
  output [31:0] R2_2,
  output [31:0] imm_1_2,
  output [31:0] imm_2_2,
  output [31:0] PC_2,
  output [31:0] PC_4_2,
  output [31:0] IR_2,
  output [31:0] AUIPC_result_2,
  output [1:0] RS1_Forward_2,
  output [1:0] RS2_Forward_2,
  output EX_PredictJump
);

  wire multiplexer_1_out, multiplexer_2_out, multiplexer_3_out, multiplexer_4_out, multiplexer_5_out,
       multiplexer_6_out, multiplexer_7_out, multiplexer_8_out, multiplexer_9_out, multiplexer_10_out,
       multiplexer_11_out, multiplexer_12_out, multiplexer_13_out, multiplexer_14_out, multiplexer_15_out,
       multiplexer_28_out, or_1_out;
  wire [1:0] multiplexer_26_out, multiplexer_27_out;
  wire [3:0] multiplexer_16_out;
  wire [4:0] multiplexer_17_out;
  wire [31:0] multiplexer_18_out, multiplexer_19_out, multiplexer_20_out, multiplexer_21_out,
       multiplexer_22_out, multiplexer_23_out, multiplexer_24_out, multiplexer_25_out;

  Multiplexer #(.select(1), .width(1), .disabled("Z"), .enable("false")) multiplexer_1 (
    .in0(SLTIU), .in1(1'b0), .out(multiplexer_1_out), .sel(or_1_out));
  Multiplexer #(.select(1), .width(1), .disabled("Z"), .enable("false")) multiplexer_2 (
    .in0(U_Type), .in1(1'b0), .out(multiplexer_2_out), .sel(or_1_out));
  Multiplexer #(.select(1), .width(1), .disabled("Z"), .enable("false")) multiplexer_3 (
    .in0(BEQ), .in1(1'b0), .out(multiplexer_3_out), .sel(or_1_out));
  Multiplexer #(.select(1), .width(1), .disabled("Z"), .enable("false")) multiplexer_4 (
    .in0(BNE), .in1(1'b0), .out(multiplexer_4_out), .sel(or_1_out));
  Multiplexer #(.select(1), .width(1), .disabled("Z"), .enable("false")) multiplexer_5 (
    .in0(MemToReg), .in1(1'b0), .out(multiplexer_5_out), .sel(or_1_out));
  Multiplexer #(.select(1), .width(1), .disabled("Z"), .enable("false")) multiplexer_6 (
    .in0(MemWrite), .in1(1'b0), .out(multiplexer_6_out), .sel(or_1_out));
  Multiplexer #(.select(1), .width(1), .disabled("Z"), .enable("false")) multiplexer_7 (
    .in0(AluSrc), .in1(1'b0), .out(multiplexer_7_out), .sel(or_1_out));
  Multiplexer #(.select(1), .width(1), .disabled("Z"), .enable("false")) multiplexer_8 (
    .in0(RegWrite), .in1(1'b0), .out(multiplexer_8_out), .sel(or_1_out));
  Multiplexer #(.select(1), .width(1), .disabled("Z"), .enable("false")) multiplexer_9 (
    .in0(S_type), .in1(1'b0), .out(multiplexer_9_out), .sel(or_1_out));
  Multiplexer #(.select(1), .width(1), .disabled("Z"), .enable("false")) multiplexer_10 (
    .in0(ecall), .in1(1'b0), .out(multiplexer_10_out), .sel(or_1_out));
  Multiplexer #(.select(1), .width(1), .disabled("Z"), .enable("false")) multiplexer_11 (
    .in0(Jal), .in1(1'b0), .out(multiplexer_11_out), .sel(or_1_out));
  Multiplexer #(.select(1), .width(1), .disabled("Z"), .enable("false")) multiplexer_12 (
    .in0(Jalr), .in1(1'b0), .out(multiplexer_12_out), .sel(or_1_out));
  Multiplexer #(.select(1), .width(1), .disabled("Z"), .enable("false")) multiplexer_13 (
    .in0(LB), .in1(1'b0), .out(multiplexer_13_out), .sel(or_1_out));
  Multiplexer #(.select(1), .width(1), .disabled("Z"), .enable("false")) multiplexer_14 (
    .in0(BLTU), .in1(1'b0), .out(multiplexer_14_out), .sel(or_1_out));
  Multiplexer #(.select(1), .width(1), .disabled("Z"), .enable("false")) multiplexer_15 (
    .in0(Uret), .in1(1'b0), .out(multiplexer_15_out), .sel(or_1_out));
  Multiplexer #(.select(1), .width(4), .disabled("Z"), .enable("false")) multiplexer_16 (
    .in0(AluOP), .in1(4'b0000), .out(multiplexer_16_out), .sel(or_1_out));
  Multiplexer #(.select(1), .width(5), .disabled("Z"), .enable("false")) multiplexer_17 (
    .in0(rd), .in1({5{1'b0}}), .out(multiplexer_17_out), .sel(or_1_out));
  Multiplexer #(.select(1), .width(32), .disabled("Z"), .enable("false")) multiplexer_18 (
    .in0(R1), .in1({32{1'b0}}), .out(multiplexer_18_out), .sel(or_1_out));
  Multiplexer #(.select(1), .width(32), .disabled("Z"), .enable("false")) multiplexer_19 (
    .in0(R2), .in1({32{1'b0}}), .out(multiplexer_19_out), .sel(or_1_out));
  Multiplexer #(.select(1), .width(32), .disabled("Z"), .enable("false")) multiplexer_20 (
    .in0(imm_1), .in1({32{1'b0}}), .out(multiplexer_20_out), .sel(or_1_out));
  Multiplexer #(.select(1), .width(32), .disabled("Z"), .enable("false")) multiplexer_21 (
    .in0(imm_2), .in1({32{1'b0}}), .out(multiplexer_21_out), .sel(or_1_out));
  Multiplexer #(.select(1), .width(32), .disabled("Z"), .enable("false")) multiplexer_22 (
    .in0(PC), .in1({32{1'b0}}), .out(multiplexer_22_out), .sel(or_1_out));
  Multiplexer #(.select(1), .width(32), .disabled("Z"), .enable("false")) multiplexer_23 (
    .in0(PC_4), .in1({32{1'b0}}), .out(multiplexer_23_out), .sel(or_1_out));
  Multiplexer #(.select(1), .width(32), .disabled("Z"), .enable("false")) multiplexer_24 (
    .in0(IR), .in1({32{1'b0}}), .out(multiplexer_24_out), .sel(or_1_out));
  Multiplexer #(.select(1), .width(32), .disabled("Z"), .enable("false")) multiplexer_25 (
    .in0(AUIPC_result), .in1({32{1'b0}}), .out(multiplexer_25_out), .sel(or_1_out));
  Multiplexer #(.select(1), .width(2), .disabled("Z"), .enable("false")) multiplexer_26 (
    .in0(RS1_Forward), .in1(2'b00), .out(multiplexer_26_out), .sel(or_1_out));
  Multiplexer #(.select(1), .width(2), .disabled("Z"), .enable("false")) multiplexer_27 (
    .in0(RS2_Forward), .in1(2'b00), .out(multiplexer_27_out), .sel(or_1_out));
  Multiplexer #(.select(1), .width(1), .disabled("Z"), .enable("false")) multiplexer_28 (
    .in0(ID_PredictJump), .in1(1'b0), .out(multiplexer_28_out), .sel(or_1_out));
  or or_1 (or_1_out, reset, flush);
  Register #(.width(1), .trigger("rising"), .Select("low")) register_1 (
    .D(multiplexer_1_out), .en(en), .Q(SLTIU_2), .clk(clk));  // open: clr
  Register #(.width(1), .trigger("rising"), .Select("low")) register_2 (
    .D(multiplexer_2_out), .en(en), .Q(U_Type_2), .clk(clk));  // open: clr
  Register #(.width(1), .trigger("rising"), .Select("low")) register_3 (
    .D(multiplexer_3_out), .en(en), .Q(BEQ_2), .clk(clk));  // open: clr
  Register #(.width(1), .trigger("rising"), .Select("low")) register_4 (
    .D(multiplexer_4_out), .en(en), .Q(BNE_2), .clk(clk));  // open: clr
  Register #(.width(1), .trigger("rising"), .Select("low")) register_5 (
    .D(multiplexer_5_out), .en(en), .Q(MemToReg_2), .clk(clk));  // open: clr
  Register #(.width(1), .trigger("rising"), .Select("low")) register_6 (
    .D(multiplexer_6_out), .en(en), .Q(MemWrite_2), .clk(clk));  // open: clr
  Register #(.width(1), .trigger("rising"), .Select("low")) register_7 (
    .D(multiplexer_7_out), .en(en), .Q(AluSrc_2), .clk(clk));  // open: clr
  Register #(.width(1), .trigger("rising"), .Select("low")) register_8 (
    .D(multiplexer_8_out), .en(en), .Q(RegWrite_2), .clk(clk));  // open: clr
  Register #(.width(1), .trigger("rising"), .Select("low")) register_9 (
    .D(multiplexer_9_out), .en(en), .Q(S_type_2), .clk(clk));  // open: clr
  Register #(.width(1), .trigger("rising"), .Select("low")) register_10 (
    .D(multiplexer_10_out), .en(en), .Q(ecall_2), .clk(clk));  // open: clr
  Register #(.width(1), .trigger("rising"), .Select("low")) register_11 (
    .D(multiplexer_11_out), .en(en), .Q(Jal_2), .clk(clk));  // open: clr
  Register #(.width(1), .trigger("rising"), .Select("low")) register_12 (
    .D(multiplexer_12_out), .en(en), .Q(Jalr_2), .clk(clk));  // open: clr
  Register #(.width(1), .trigger("rising"), .Select("low")) register_13 (
    .D(multiplexer_13_out), .en(en), .Q(LB_2), .clk(clk));  // open: clr
  Register #(.width(1), .trigger("rising"), .Select("low")) register_14 (
    .D(multiplexer_14_out), .en(en), .Q(BLTU_2), .clk(clk));  // open: clr
  Register #(.width(1), .trigger("rising"), .Select("low")) register_15 (
    .D(multiplexer_15_out), .Q(Uret_2), .clk(clk));  // open: en, clr
  Register #(.width(4), .trigger("rising"), .Select("low")) register_16 (
    .D(multiplexer_16_out), .en(en), .Q(AluOP_2), .clk(clk));  // open: clr
  Register #(.width(5), .trigger("rising"), .Select("low")) register_17 (
    .D(multiplexer_17_out), .en(en), .Q(rd_2), .clk(clk));  // open: clr
  Register #(.width(32), .trigger("rising"), .Select("low")) register_18 (
    .D(multiplexer_18_out), .en(en), .Q(R1_2), .clk(clk));  // open: clr
  Register #(.width(32), .trigger("rising"), .Select("low")) register_19 (
    .D(multiplexer_19_out), .en(en), .Q(R2_2), .clk(clk));  // open: clr
  Register #(.width(32), .trigger("rising"), .Select("low")) register_20 (
    .D(multiplexer_20_out), .en(en), .Q(imm_1_2), .clk(clk));  // open: clr
  Register #(.width(32), .trigger("rising"), .Select("low")) register_21 (
    .D(multiplexer_21_out), .en(en), .Q(imm_2_2), .clk(clk));  // open: clr
  Register #(.width(32), .trigger("rising"), .Select("low")) register_22 (
    .D(multiplexer_22_out), .en(en), .Q(PC_2), .clk(clk));  // open: clr
  Register #(.width(32), .trigger("rising"), .Select("low")) register_23 (
    .D(multiplexer_23_out), .en(en), .Q(PC_4_2), .clk(clk));  // open: clr
  Register #(.width(32), .trigger("rising"), .Select("low")) register_24 (
    .D(multiplexer_24_out), .en(en), .Q(IR_2), .clk(clk));  // open: clr
  Register #(.width(32), .trigger("rising"), .Select("low")) register_25 (
    .D(multiplexer_25_out), .en(en), .Q(AUIPC_result_2), .clk(clk));  // open: clr
  Register #(.width(2), .trigger("rising"), .Select("low")) register_26 (
    .D(multiplexer_26_out), .en(en), .Q(RS1_Forward_2), .clk(clk));  // open: clr
  Register #(.width(2), .trigger("rising"), .Select("low")) register_27 (
    .D(multiplexer_27_out), .en(en), .Q(RS2_Forward_2), .clk(clk));  // open: clr
  Register #(.width(1), .trigger("rising"), .Select("low")) register_28 (
    .D(multiplexer_28_out), .en(en), .Q(EX_PredictJump), .clk(clk));  // open: clr
endmodule

module EX_MEM (
  input  LESS,
  input  SLTIU,
  input  U_Type,
  input  Jal,
  input  Jalr,
  input  MemToReg,
  input  MemWrite,
  input  LB,
  input  RegWrite,
  input  halt,
  input  [4:0] rd,
  input  [31:0] Result,
  input  [31:0] WriteData,
  input  [31:0] IR,
  input  [31:0] PC,
  input  [31:0] AUIPC_result,
  input  [31:0] PC_4,
  input  reset,
  input  en,
  input  clk,
  output LESS_2,
  output SLTIU_2,
  output U_Type_2,
  output Jal_2,
  output Jalr_2,
  output MemToReg_2,
  output MemWrite_2,
  output LB_2,
  output RegWrite_2,
  output halt_2,
  output [4:0] rd_2,
  output [31:0] Result_2,
  output [31:0] WriteData_2,
  output [31:0] IR_2,
  output [31:0] PC_2,
  output [31:0] AUIPC_result_2,
  output [31:0] PC_4_2
);

  wire multiplexer_1_out, multiplexer_2_out, multiplexer_3_out, multiplexer_4_out, multiplexer_5_out,
       multiplexer_6_out, multiplexer_7_out, multiplexer_8_out, multiplexer_9_out, multiplexer_10_out;
  wire [4:0] multiplexer_11_out;
  wire [31:0] multiplexer_12_out, multiplexer_13_out, multiplexer_14_out, multiplexer_15_out,
       multiplexer_16_out, multiplexer_17_out;

  Multiplexer #(.select(1), .width(1), .disabled("Z"), .enable("false")) multiplexer_1 (
    .in0(LESS), .in1(1'b0), .out(multiplexer_1_out), .sel(reset));
  Multiplexer #(.select(1), .width(1), .disabled("Z"), .enable("false")) multiplexer_2 (
    .in0(SLTIU), .in1(1'b0), .out(multiplexer_2_out), .sel(reset));
  Multiplexer #(.select(1), .width(1), .disabled("Z"), .enable("false")) multiplexer_3 (
    .in0(U_Type), .in1(1'b0), .out(multiplexer_3_out), .sel(reset));
  Multiplexer #(.select(1), .width(1), .disabled("Z"), .enable("false")) multiplexer_4 (
    .in0(Jal), .in1(1'b0), .out(multiplexer_4_out), .sel(reset));
  Multiplexer #(.select(1), .width(1), .disabled("Z"), .enable("false")) multiplexer_5 (
    .in0(Jalr), .in1(1'b0), .out(multiplexer_5_out), .sel(reset));
  Multiplexer #(.select(1), .width(1), .disabled("Z"), .enable("false")) multiplexer_6 (
    .in0(MemToReg), .in1(1'b0), .out(multiplexer_6_out), .sel(reset));
  Multiplexer #(.select(1), .width(1), .disabled("Z"), .enable("false")) multiplexer_7 (
    .in0(MemWrite), .in1(1'b0), .out(multiplexer_7_out), .sel(reset));
  Multiplexer #(.select(1), .width(1), .disabled("Z"), .enable("false")) multiplexer_8 (
    .in0(LB), .in1(1'b0), .out(multiplexer_8_out), .sel(reset));
  Multiplexer #(.select(1), .width(1), .disabled("Z"), .enable("false")) multiplexer_9 (
    .in0(RegWrite), .in1(1'b0), .out(multiplexer_9_out), .sel(reset));
  Multiplexer #(.select(1), .width(1), .disabled("Z"), .enable("false")) multiplexer_10 (
    .in0(halt), .in1(1'b0), .out(multiplexer_10_out), .sel(reset));
  Multiplexer #(.select(1), .width(5), .disabled("Z"), .enable("false")) multiplexer_11 (
    .in0(rd), .in1({5{1'b0}}), .out(multiplexer_11_out), .sel(reset));
  Multiplexer #(.select(1), .width(32), .disabled("Z"), .enable("false")) multiplexer_12 (
    .in0(Result), .in1({32{1'b0}}), .out(multiplexer_12_out), .sel(reset));
  Multiplexer #(.select(1), .width(32), .disabled("Z"), .enable("false")) multiplexer_13 (
    .in0(WriteData), .in1({32{1'b0}}), .out(multiplexer_13_out), .sel(reset));
  Multiplexer #(.select(1), .width(32), .disabled("Z"), .enable("false")) multiplexer_14 (
    .in0(IR), .in1({32{1'b0}}), .out(multiplexer_14_out), .sel(reset));
  Multiplexer #(.select(1), .width(32), .disabled("Z"), .enable("false")) multiplexer_15 (
    .in0(PC), .in1({32{1'b0}}), .out(multiplexer_15_out), .sel(reset));
  Multiplexer #(.select(1), .width(32), .disabled("Z"), .enable("false")) multiplexer_16 (
    .in0(AUIPC_result), .in1({32{1'b0}}), .out(multiplexer_16_out), .sel(reset));
  Multiplexer #(.select(1), .width(32), .disabled("Z"), .enable("false")) multiplexer_17 (
    .in0(PC_4), .in1({32{1'b0}}), .out(multiplexer_17_out), .sel(reset));
  Register #(.width(1), .trigger("rising"), .Select("low")) register_1 (
    .D(multiplexer_1_out), .en(en), .Q(LESS_2), .clk(clk));  // open: clr
  Register #(.width(1), .trigger("rising"), .Select("low")) register_2 (
    .D(multiplexer_2_out), .en(en), .Q(SLTIU_2), .clk(clk));  // open: clr
  Register #(.width(1), .trigger("rising"), .Select("low")) register_3 (
    .D(multiplexer_3_out), .en(en), .Q(U_Type_2), .clk(clk));  // open: clr
  Register #(.width(1), .trigger("rising"), .Select("low")) register_4 (
    .D(multiplexer_4_out), .en(en), .Q(Jal_2), .clk(clk));  // open: clr
  Register #(.width(1), .trigger("rising"), .Select("low")) register_5 (
    .D(multiplexer_5_out), .en(en), .Q(Jalr_2), .clk(clk));  // open: clr
  Register #(.width(1), .trigger("rising"), .Select("low")) register_6 (
    .D(multiplexer_6_out), .en(en), .Q(MemToReg_2), .clk(clk));  // open: clr
  Register #(.width(1), .trigger("rising"), .Select("low")) register_7 (
    .D(multiplexer_7_out), .en(en), .Q(MemWrite_2), .clk(clk));  // open: clr
  Register #(.width(1), .trigger("rising"), .Select("low")) register_8 (
    .D(multiplexer_8_out), .en(en), .Q(LB_2), .clk(clk));  // open: clr
  Register #(.width(1), .trigger("rising"), .Select("low")) register_9 (
    .D(multiplexer_9_out), .en(en), .Q(RegWrite_2), .clk(clk));  // open: clr
  Register #(.width(1), .trigger("rising"), .Select("low")) register_10 (
    .D(multiplexer_10_out), .en(en), .Q(halt_2), .clk(clk));  // open: clr
  Register #(.width(5), .trigger("rising"), .Select("low")) register_11 (
    .D(multiplexer_11_out), .en(en), .Q(rd_2), .clk(clk));  // open: clr
  Register #(.width(32), .trigger("rising"), .Select("low")) register_12 (
    .D(multiplexer_12_out), .en(en), .Q(Result_2), .clk(clk));  // open: clr
  Register #(.width(32), .trigger("rising"), .Select("low")) register_13 (
    .D(multiplexer_13_out), .en(en), .Q(WriteData_2), .clk(clk));  // open: clr
  Register #(.width(32), .trigger("rising"), .Select("low")) register_14 (
    .D(multiplexer_14_out), .en(en), .Q(IR_2), .clk(clk));  // open: clr
  Register #(.width(32), .trigger("rising"), .Select("low")) register_15 (
    .D(multiplexer_15_out), .en(en), .Q(PC_2), .clk(clk));  // open: clr
  Register #(.width(32), .trigger("rising"), .Select("low")) register_16 (
    .D(multiplexer_16_out), .en(en), .Q(AUIPC_result_2), .clk(clk));  // open: clr
  Register #(.width(32), .trigger("rising"), .Select("low")) register_17 (
    .D(multiplexer_17_out), .en(en), .Q(PC_4_2), .clk(clk));  // open: clr
endmodule

module MEM_WB (
  input  LESS,
  input  SLTIU,
  input  U_Type,
  input  Jal,
  input  Jalr,
  input  MemToReg,
  input  RegWrite,
  input  halt,
  input  [4:0] rd,
  input  [31:0] ALUResult,
  input  [31:0] ReadData,
  input  [31:0] IR,
  input  [31:0] PC,
  input  [31:0] AUIPC_result,
  input  [31:0] PC_4,
  input  reset,
  input  en,
  input  clk,
  output LESS_2,
  output SLTIU_2,
  output U_Type_2,
  output Jal_2,
  output Jalr_2,
  output MemToReg_2,
  output RegWrite_2,
  output halt_2,
  output [4:0] rd_2,
  output [31:0] ALUResult_2,
  output [31:0] ReadData_2,
  output [31:0] IR_2,
  output [31:0] PC_2,
  output [31:0] AUIPC_result_2,
  output [31:0] PC_4_2
);

  wire multiplexer_1_out, multiplexer_2_out, multiplexer_3_out, multiplexer_4_out, multiplexer_5_out,
       multiplexer_6_out, multiplexer_7_out, multiplexer_8_out;
  wire [4:0] multiplexer_9_out;
  wire [31:0] multiplexer_10_out, multiplexer_11_out, multiplexer_12_out, multiplexer_13_out,
       multiplexer_14_out, multiplexer_15_out;

  Multiplexer #(.select(1), .width(1), .disabled("Z"), .enable("false")) multiplexer_1 (
    .in0(LESS), .in1(1'b0), .out(multiplexer_1_out), .sel(reset));
  Multiplexer #(.select(1), .width(1), .disabled("Z"), .enable("false")) multiplexer_2 (
    .in0(SLTIU), .in1(1'b0), .out(multiplexer_2_out), .sel(reset));
  Multiplexer #(.select(1), .width(1), .disabled("Z"), .enable("false")) multiplexer_3 (
    .in0(U_Type), .in1(1'b0), .out(multiplexer_3_out), .sel(reset));
  Multiplexer #(.select(1), .width(1), .disabled("Z"), .enable("false")) multiplexer_4 (
    .in0(Jal), .in1(1'b0), .out(multiplexer_4_out), .sel(reset));
  Multiplexer #(.select(1), .width(1), .disabled("Z"), .enable("false")) multiplexer_5 (
    .in0(Jalr), .in1(1'b0), .out(multiplexer_5_out), .sel(reset));
  Multiplexer #(.select(1), .width(1), .disabled("Z"), .enable("false")) multiplexer_6 (
    .in0(MemToReg), .in1(1'b0), .out(multiplexer_6_out), .sel(reset));
  Multiplexer #(.select(1), .width(1), .disabled("Z"), .enable("false")) multiplexer_7 (
    .in0(RegWrite), .in1(1'b0), .out(multiplexer_7_out), .sel(reset));
  Multiplexer #(.select(1), .width(1), .disabled("Z"), .enable("false")) multiplexer_8 (
    .in0(halt), .in1(1'b0), .out(multiplexer_8_out), .sel(reset));
  Multiplexer #(.select(1), .width(5), .disabled("Z"), .enable("false")) multiplexer_9 (
    .in0(rd), .in1({5{1'b0}}), .out(multiplexer_9_out), .sel(reset));
  Multiplexer #(.select(1), .width(32), .disabled("Z"), .enable("false")) multiplexer_10 (
    .in0(ALUResult), .in1({32{1'b0}}), .out(multiplexer_10_out), .sel(reset));
  Multiplexer #(.select(1), .width(32), .disabled("Z"), .enable("false")) multiplexer_11 (
    .in0(ReadData), .in1({32{1'b0}}), .out(multiplexer_11_out), .sel(reset));
  Multiplexer #(.select(1), .width(32), .disabled("Z"), .enable("false")) multiplexer_12 (
    .in0(IR), .in1({32{1'b0}}), .out(multiplexer_12_out), .sel(reset));
  Multiplexer #(.select(1), .width(32), .disabled("Z"), .enable("false")) multiplexer_13 (
    .in0(PC), .in1({32{1'b0}}), .out(multiplexer_13_out), .sel(reset));
  Multiplexer #(.select(1), .width(32), .disabled("Z"), .enable("false")) multiplexer_14 (
    .in0(AUIPC_result), .in1({32{1'b0}}), .out(multiplexer_14_out), .sel(reset));
  Multiplexer #(.select(1), .width(32), .disabled("Z"), .enable("false")) multiplexer_15 (
    .in0(PC_4), .in1({32{1'b0}}), .out(multiplexer_15_out), .sel(reset));
  Register #(.width(1), .trigger("rising"), .Select("low")) register_1 (
    .D(multiplexer_1_out), .en(en), .Q(LESS_2), .clk(clk));  // open: clr
  Register #(.width(1), .trigger("rising"), .Select("low")) register_2 (
    .D(multiplexer_2_out), .en(en), .Q(SLTIU_2), .clk(clk));  // open: clr
  Register #(.width(1), .trigger("rising"), .Select("low")) register_3 (
    .D(multiplexer_3_out), .en(en), .Q(U_Type_2), .clk(clk));  // open: clr
  Register #(.width(1), .trigger("rising"), .Select("low")) register_4 (
    .D(multiplexer_4_out), .en(en), .Q(Jal_2), .clk(clk));  // open: clr
  Register #(.width(1), .trigger("rising"), .Select("low")) register_5 (
    .D(multiplexer_5_out), .en(en), .Q(Jalr_2), .clk(clk));  // open: clr
  Register #(.width(1), .trigger("rising"), .Select("low")) register_6 (
    .D(multiplexer_6_out), .en(en), .Q(MemToReg_2), .clk(clk));  // open: clr
  Register #(.width(1), .trigger("rising"), .Select("low")) register_7 (
    .D(multiplexer_7_out), .en(en), .Q(RegWrite_2), .clk(clk));  // open: clr
  Register #(.width(1), .trigger("rising"), .Select("low")) register_8 (
    .D(multiplexer_8_out), .en(en), .Q(halt_2), .clk(clk));  // open: clr
  Register #(.width(5), .trigger("rising"), .Select("low")) register_9 (
    .D(multiplexer_9_out), .Q(rd_2), .clk(clk));  // open: en, clr
  Register #(.width(32), .trigger("rising"), .Select("low")) register_10 (
    .D(multiplexer_10_out), .en(en), .Q(ALUResult_2), .clk(clk));  // open: clr
  Register #(.width(32), .trigger("rising"), .Select("low")) register_11 (
    .D(multiplexer_11_out), .en(en), .Q(ReadData_2), .clk(clk));  // open: clr
  Register #(.width(32), .trigger("rising"), .Select("low")) register_12 (
    .D(multiplexer_12_out), .en(en), .Q(IR_2), .clk(clk));  // open: clr
  Register #(.width(32), .trigger("rising"), .Select("low")) register_13 (
    .D(multiplexer_13_out), .en(en), .Q(PC_2), .clk(clk));  // open: clr
  Register #(.width(32), .trigger("rising"), .Select("low")) register_14 (
    .D(multiplexer_14_out), .en(en), .Q(AUIPC_result_2), .clk(clk));  // open: clr
  Register #(.width(32), .trigger("rising"), .Select("low")) register_15 (
    .D(multiplexer_15_out), .en(en), .Q(PC_4_2), .clk(clk));  // open: clr
endmodule
module \重定向处理逻辑  (
  input  RS1_used,
  input  EX_RegWrite,
  input  EX_MemToReg,
  input  [31:0] IR,
  input  RS2_used,
  input  MEM_RegWrite,
  input  [4:0] EX_rd,
  input  Ecall,
  input  BranchTaken,
  input  [4:0] MEM_rd,
  output Stall,
  output Flush,
  output [1:0] RS1_Forward,
  output [1:0] RS2_Forward
);

  wire and_1_out, and_2_out, and_3_out, and_4_out, and_5_out, and_6_out, and_7_out, and_8_out, and_9_out,
       and_10_out, and_11_out, and_12_out, and_13_out, and_14_out, and_15_out, and_16_out, and_17_out,
       and_18_out, and_23_out, and_24_out, comparator_1_eq, comparator_2_eq, comparator_3_eq,
       comparator_4_eq, comparator_5_eq, comparator_6_eq, comparator_7_eq, comparator_8_eq, comparator_9_eq,
       comparator_10_eq, comparator_11_eq, comparator_12_eq, comparator_13_eq, comparator_14_eq,
       comparator_15_eq, comparator_16_eq, Ecall1, Ecall2, Ecall3, Ecall4, or_3_out, or_5_out;

  Comparator #(.width(5), .mode("twosComplement")) comparator_1 (
    .a(EX_rd), .b(IR[19:15]), .eq(comparator_1_eq));  // open: gt, lt
  Comparator #(.width(5), .mode("twosComplement")) comparator_2 (
    .a(IR[19:15]), .b({5{1'b0}}), .eq(comparator_2_eq));  // open: gt, lt
  Comparator #(.width(5), .mode("twosComplement")) comparator_3 (
    .a({5{1'b0}}), .b(IR[24:20]), .eq(comparator_3_eq));  // open: gt, lt
  Comparator #(.width(5), .mode("twosComplement")) comparator_4 (
    .a(IR[24:20]), .b(EX_rd), .eq(comparator_4_eq));  // open: gt, lt
  Comparator #(.width(5), .mode("twosComplement")) comparator_5 (
    .a(EX_rd), .b(IR[19:15]), .eq(comparator_5_eq));  // open: gt, lt
  Comparator #(.width(5), .mode("twosComplement")) comparator_6 (
    .a(IR[19:15]), .b({5{1'b0}}), .eq(comparator_6_eq));  // open: gt, lt
  Comparator #(.width(5), .mode("twosComplement")) comparator_7 (
    .a({5{1'b0}}), .b(IR[19:15]), .eq(comparator_7_eq));  // open: gt, lt
  Comparator #(.width(5), .mode("twosComplement")) comparator_8 (
    .a(IR[19:15]), .b(MEM_rd), .eq(comparator_8_eq));  // open: gt, lt
  Comparator #(.width(5), .mode("twosComplement")) comparator_9 (
    .a(EX_rd), .b(IR[24:20]), .eq(comparator_9_eq));  // open: gt, lt
  Comparator #(.width(5), .mode("twosComplement")) comparator_10 (
    .a(IR[24:20]), .b({5{1'b0}}), .eq(comparator_10_eq));  // open: gt, lt
  Comparator #(.width(5), .mode("twosComplement")) comparator_11 (
    .a({5{1'b0}}), .b(IR[24:20]), .eq(comparator_11_eq));  // open: gt, lt
  Comparator #(.width(5), .mode("twosComplement")) comparator_12 (
    .a(IR[24:20]), .b(MEM_rd), .eq(comparator_12_eq));  // open: gt, lt
  and and_1 (and_1_out, Ecall, EX_RegWrite);
  and and_2 (and_2_out, Ecall, MEM_RegWrite);
  and and_3 (and_3_out, Ecall, EX_RegWrite);
  and and_4 (and_4_out, Ecall, MEM_RegWrite);
  and and_5 (and_5_out, RS1_used, ~comparator_2_eq);  // AND_Gate
  and and_6 (and_6_out, ~comparator_3_eq, RS2_used);  // AND_Gate
  and and_7 (and_7_out, comparator_5_eq, ~comparator_6_eq);  // AND_Gate
  and and_8 (and_8_out, ~comparator_7_eq, comparator_8_eq);  // AND_Gate
  and and_9 (and_9_out, comparator_9_eq, ~comparator_10_eq);  // AND_Gate
  and and_10 (and_10_out, ~comparator_11_eq, comparator_12_eq);  // AND_Gate
  Comparator #(.width(5), .mode("twosComplement")) comparator_13 (
    .a(EX_rd), .b(5'b10001), .eq(comparator_13_eq));  // open: gt, lt
  Comparator #(.width(5), .mode("twosComplement")) comparator_14 (
    .a(MEM_rd), .b(5'b10001), .eq(comparator_14_eq));  // open: gt, lt
  Comparator #(.width(5), .mode("twosComplement")) comparator_15 (
    .a(EX_rd), .b(5'b01010), .eq(comparator_15_eq));  // open: gt, lt
  Comparator #(.width(5), .mode("twosComplement")) comparator_16 (
    .a(MEM_rd), .b(5'b01010), .eq(comparator_16_eq));  // open: gt, lt
  and and_11 (and_11_out, comparator_1_eq, and_5_out, EX_MemToReg);
  and and_12 (and_12_out, EX_MemToReg, and_6_out, comparator_4_eq);
  and and_13 (and_13_out, and_7_out, and_14_out);
  and and_14 (and_14_out, EX_RegWrite, RS1_used);
  and and_15 (and_15_out, RS1_used, MEM_RegWrite);
  and and_16 (and_16_out, and_15_out, and_8_out);
  and and_17 (and_17_out, EX_RegWrite, RS2_used);
  and and_18 (and_18_out, RS2_used, MEM_RegWrite);
  and and_19 (Ecall1, comparator_13_eq, and_1_out);
  and and_20 (Ecall2, and_2_out, comparator_14_eq);
  and and_21 (Ecall3, comparator_15_eq, and_3_out);
  and and_22 (Ecall4, and_4_out, comparator_16_eq);
  or or_1 (Stall, and_11_out, and_12_out);
  or or_2 (RS1_Forward[1], Ecall1, and_13_out);
  or or_3 (or_3_out, and_16_out, Ecall2);
  or or_4 (RS2_Forward[1], Ecall3, and_23_out);
  and and_23 (and_23_out, and_9_out, and_17_out);
  and and_24 (and_24_out, and_18_out, and_10_out);
  or or_5 (or_5_out, and_24_out, Ecall4);
  and and_25 (RS1_Forward[0], ~RS1_Forward[1], or_3_out);  // AND_Gate
  and and_26 (RS2_Forward[0], ~RS2_Forward[1], or_5_out);  // AND_Gate
  or or_6 (Flush, Stall, BranchTaken);

  // Other names for the same wires on the sheet: RS1[4:0] = IR[19:15]; RS2[4:0] = IR[24:20]; LoadUse = Stall

  // Notes on the sheet:
  //   LoadUse处理逻辑
  //   寄存器处理逻辑
  //   重定向处理输入
  //   重定向处理输出
endmodule

module \气泡处理逻辑  (
  input  BranchTaken,
  input  [31:0] IR,
  input  Ecall,
  input  RS1_used,
  input  EX_RegWrite,
  input  [4:0] EX_rd,
  input  RS2_used,
  input  MEM_RegWrite,
  input  [4:0] MEM_rd,
  output stall,
  output flush
);

  wire and_1_out, and_2_out, and_3_out, and_4_out, and_5_out, and_6_out, comparator_1_eq, comparator_2_eq,
       comparator_3_eq, comparator_4_eq, comparator_5_eq, comparator_6_eq, comparator_7_eq, comparator_8_eq,
       comparator_9_eq, comparator_10_eq, comparator_11_eq, comparator_12_eq, or_1_out, or_2_out;

  Comparator #(.width(5), .mode("twosComplement")) comparator_1 (
    .a({5{1'b0}}), .b(IR[19:15]), .eq(comparator_1_eq));  // open: gt, lt
  Comparator #(.width(5), .mode("twosComplement")) comparator_2 (
    .a(IR[19:15]), .b(EX_rd), .eq(comparator_2_eq));  // open: gt, lt
  Comparator #(.width(5), .mode("twosComplement")) comparator_3 (
    .a({5{1'b0}}), .b(IR[19:15]), .eq(comparator_3_eq));  // open: gt, lt
  Comparator #(.width(5), .mode("twosComplement")) comparator_4 (
    .a(IR[19:15]), .b(MEM_rd), .eq(comparator_4_eq));  // open: gt, lt
  Comparator #(.width(5), .mode("twosComplement")) comparator_5 (
    .a({5{1'b0}}), .b(IR[24:20]), .eq(comparator_5_eq));  // open: gt, lt
  Comparator #(.width(5), .mode("twosComplement")) comparator_6 (
    .a(IR[24:20]), .b(EX_rd), .eq(comparator_6_eq));  // open: gt, lt
  Comparator #(.width(5), .mode("twosComplement")) comparator_7 (
    .a({5{1'b0}}), .b(IR[24:20]), .eq(comparator_7_eq));  // open: gt, lt
  Comparator #(.width(5), .mode("twosComplement")) comparator_8 (
    .a(IR[24:20]), .b(MEM_rd), .eq(comparator_8_eq));  // open: gt, lt
  Comparator #(.width(5), .mode("twosComplement")) comparator_9 (
    .a(5'b10001), .b(EX_rd), .eq(comparator_9_eq));  // open: gt, lt
  Comparator #(.width(5), .mode("twosComplement")) comparator_10 (
    .a(EX_rd), .b(5'b01010), .eq(comparator_10_eq));  // open: gt, lt
  Comparator #(.width(5), .mode("twosComplement")) comparator_11 (
    .a(5'b10001), .b(MEM_rd), .eq(comparator_11_eq));  // open: gt, lt
  Comparator #(.width(5), .mode("twosComplement")) comparator_12 (
    .a(MEM_rd), .b(5'b01010), .eq(comparator_12_eq));  // open: gt, lt
  or or_1 (or_1_out, comparator_9_eq, comparator_10_eq);
  or or_2 (or_2_out, comparator_11_eq, comparator_12_eq);
  and and_1 (and_1_out, RS1_used, ~comparator_1_eq, comparator_2_eq, EX_RegWrite);  // AND_Gate
  and and_2 (and_2_out, RS1_used, ~comparator_3_eq, comparator_4_eq, MEM_RegWrite);  // AND_Gate
  and and_3 (and_3_out, RS2_used, ~comparator_5_eq, comparator_6_eq, EX_RegWrite);  // AND_Gate
  and and_4 (and_4_out, RS2_used, ~comparator_7_eq, comparator_8_eq, MEM_RegWrite);  // AND_Gate
  and and_5 (and_5_out, or_1_out, Ecall);
  and and_6 (and_6_out, Ecall, or_2_out);
  or or_3 (stall, and_1_out, and_2_out, and_3_out, and_4_out, and_5_out, and_6_out);
  or or_4 (flush, stall, BranchTaken);

  // Other names for the same wires on the sheet: DataHazzard = stall; RS1[4:0] = IR[19:15]; RS2[4:0] = IR[24:20]

  // Notes on the sheet:
  //   气泡处理逻辑输入
  //   气泡处理逻辑输出
endmodule

module \重定向流水中断  (
  output RegWrite,
  output MemWrite,
  output [31:0] IF_PC,
  output [31:0] ID_PC,
  output [31:0] EX_PC,
  output [31:0] M_PC,
  output [31:0] WB_PC,
  output [31:0] RDin,
  output [31:0] MDin,
  output [31:0] LedData
);

  wire and_1_out, and_2_out, and_3_out, and_4_out, and_5_out, and_7_out, and_8_out, and_9_out, and_10_out,
       and_12_out, and_13_out, and_14_out, and_15_out, and_16_out, and_17_out, BranchSuc, BranchTaken, CLK,
       clock_1_out, clock_2_out, comparator_1_eq, comparator_2_eq, comparator_3_eq, comparator_4_eq,
       comparator_6_eq, comparator_6_lt, comparator_7_eq, counter_2_q, d_ff_1_q, d_ff_2_q, d_ff_3_q,
       d_ff_4_q, ecall, Equ, EX_ecall, EX_halt, ex_mem_1_halt_2, ex_mem_1_jal_2, ex_mem_1_jalr_2,
       ex_mem_1_memtoreg_2, ex_mem_1_regwrite_2, EX_URET, Flush, Go, halt, id_ex_1_alusrc_2, id_ex_1_beq_2,
       id_ex_1_bltu_2, id_ex_1_bne_2, id_ex_1_jal_2, id_ex_1_lb_2, id_ex_1_memtoreg_2, id_ex_1_memwrite_2,
       id_ex_1_regwrite_2, ID_URET, IE, IF_URET, INT, Interrupt, IR1, IR1_q, IR1_Reset, IR2, IR2_q,
       IR2_Reset, IR3, IR3_q, IR3_Reset, IRA, IRB, IRC, JAL, LBU, Less, mem_wb_1_halt_2, mem_wb_1_jal_2,
       mem_wb_1_jalr_2, multiplexer_7_out, nand_1_out, not_1_out, not_2_out, not_4_out, or_1_out, or_5_out,
       or_6_out, or_7_out, or_8_out, or_9_out, or_10_out, or_11_out, or_12_out, or_13_out, or_14_out,
       or_19_out, or_20_out, or_21_out, priority_encoder_1_gs, register_1_q, RST, S_type, stall, W1, W2, W3,
       \单周期硬布线控制器_1_alu_src , \单周期硬布线控制器_1_beq , \单周期硬布线控制器_1_bltu , \单周期硬布线控制器_1_bne , \单周期硬布线控制器_1_jalr ,
       \单周期硬布线控制器_1_lb , \单周期硬布线控制器_1_memtoreg , \单周期硬布线控制器_1_memwrite , \单周期硬布线控制器_1_regwrite ,
       \单周期硬布线控制器_1_rs1_used , \单周期硬布线控制器_1_rs2_used , \单周期硬布线控制器_1_uret , \无条件跳转 ;
  wire [1:0] id_ex_1_jalr_2, id_ex_1_rs1_forward_2, id_ex_1_rs2_forward_2, IR_id, mem_wb_1_memtoreg_2,
       register_5_q, \重定向处理逻辑_1_rs1_forward , \重定向处理逻辑_1_rs2_forward ;
  wire [2:0] register_2_q;
  wire [3:0] id_ex_1_aluop_2, \单周期硬布线控制器_1_alu_op ;
  wire [4:0] ex_mem_1_rd_2, id_ex_1_rd_2, multiplexer_4_out, multiplexer_5_out, WB_rd;
  wire [7:0] multiplexer_14_out;
  wire [12:0] CNT_num;
  wire [15:0] \LoadUse次数 , \总周期数 , \插入气泡数 , \无条件分支数 , \条件分支成功数 ;
  wire [31:0] ALU_addr, bit_extender_1_out, bit_extender_2_out, bit_extender_3_out, bit_extender_4_out,
       bit_extender_5_out, EPC, EX_IR, ex_mem_1_pc_4_2, id_ex_1_imm_1_2, id_ex_1_imm_2_2, id_ex_1_pc_4_2,
       id_ex_1_r1_2, id_ex_1_r2_2, ID_IR, if_id_1_pc_4_2, IF_IR, INT_addr, jumpAddr, MEM_ALURes, MEM_IR,
       mem_wb_1_aluresult_2, mem_wb_1_pc_4_2, mem_wb_1_readdata_2, MemData, multiplexer_1_out,
       multiplexer_2_out, multiplexer_8_out, multiplexer_9_out, multiplexer_10_out, multiplexer_11_out,
       multiplexer_12_out, multiplexer_13_out, multiplexer_15_out, PC_4, PC_q, regifile_1_r1, regifile_1_r2,
       shifter_1_out, WB_IR;

  Button \u_总复位  (.out(RST));
  Button _1 (.out(IR1));
  Button _2 (.out(IR2));
  Button _3 (.out(IR3));
  // Probe on \总周期数 
  // Probe on \总周期数 
  Button \u_继续运行  (.out(Go));
  LED #(.active("true")) led_1 (.in(W1));
  LED #(.active("true")) led_2 (.in(W2));
  LED #(.active("true")) led_3 (.in(W3));
  Hex_Digit_Display hex_digit_display_1 (.value(LedData[31:28]));  // open: dp
  // Probe on IF_PC[19:0]
  // RiscV_Probe riscv_probe_1: pin names not known; wires that end beside it: IF_IR
  Multiplexer #(.select(2), .width(32), .disabled("Z"), .enable("false")) multiplexer_1 (
    .in0(PC_4), .in1(ALU_addr), .in2(jumpAddr), .out(multiplexer_1_out), .sel(id_ex_1_jalr_2));  // open: in3
  Hex_Digit_Display hex_digit_display_2 (.value(LedData[23:20]));  // open: dp
  Hex_Digit_Display hex_digit_display_3 (.value(LedData[27:24]));  // open: dp
  // Probe on ID_PC[19:0]
  // RiscV_Probe riscv_probe_2: pin names not known; wires that end beside it: ID_IR
  \重定向处理逻辑  \u_重定向处理逻辑_1  (
    .RS1_used(\单周期硬布线控制器_1_rs1_used ), .EX_RegWrite(id_ex_1_regwrite_2), .EX_MemToReg(id_ex_1_memtoreg_2),
    .IR(ID_IR), .RS2_used(\单周期硬布线控制器_1_rs2_used ), .MEM_RegWrite(ex_mem_1_regwrite_2), .EX_rd(id_ex_1_rd_2),
    .Ecall(ecall), .BranchTaken(BranchTaken), .MEM_rd(ex_mem_1_rd_2), .Stall(stall), .Flush(Flush),
    .RS1_Forward(\重定向处理逻辑_1_rs1_forward ), .RS2_Forward(\重定向处理逻辑_1_rs2_forward ));
  and and_1 (and_1_out, ~halt, ~stall);  // AND_Gate
  or or_1 (or_1_out, and_1_out, Go);
  Multiplexer #(.select(1), .width(32), .disabled("Z"), .enable("false")) multiplexer_2 (
    .in0(multiplexer_1_out), .in1(EPC), .out(multiplexer_2_out), .sel(IF_URET));
  LED #(.active("true")) \_1号中断等待指示灯  (.in(W1));
  LED #(.active("true")) \_2号中断等待指示灯  (.in(W2));
  LED #(.active("true")) \_3号中断等待指示灯  (.in(W3));
  Hex_Digit_Display hex_digit_display_4 (.value(LedData[15:12]));  // open: dp
  Hex_Digit_Display hex_digit_display_5 (.value(LedData[19:16]));  // open: dp
  Register #(.width(32), .trigger("rising"), .Select("low")) PC (
    .D(multiplexer_2_out), .en(or_1_out), .Q(PC_q), .clk(CLK), .clr(RST));
  D_Flip_Flop #(.trigger("rising"), .Pre_Clr_Positions("LEGACY"), .NegatePresetClear("false"), .enable("true"), .NewFFLayout("false")) d_ff_1 (
    .clk(IR1), .D(1'b1), .Q(d_ff_1_q), .reset(IR1_q));  // open: Qn, preset, en
  or or_2 (W1, IR1_q, d_ff_1_q);
  D_Flip_Flop #(.trigger("rising"), .Pre_Clr_Positions("LEGACY"), .NegatePresetClear("false"), .enable("true"), .NewFFLayout("false")) d_ff_2 (
    .clk(IR2), .D(1'b1), .Q(d_ff_2_q), .reset(IR2_q));  // open: Qn, preset, en
  or or_3 (W2, IR2_q, d_ff_2_q);
  D_Flip_Flop #(.trigger("rising"), .Pre_Clr_Positions("LEGACY"), .NegatePresetClear("false"), .enable("true"), .NewFFLayout("false")) d_ff_3 (
    .clk(IR3), .D(1'b1), .Q(d_ff_3_q), .reset(IR3_q));  // open: Qn, preset, en
  or or_4 (W3, IR3_q, d_ff_3_q);
  Comparator #(.width(16), .mode("twosComplement")) comparator_1 (
    .a(16'h23b), .b(\总周期数 ), .eq(comparator_1_eq));  // open: gt, lt
  Comparator #(.width(16), .mode("twosComplement")) comparator_2 (
    .a(\总周期数 ), .b(16'h1), .eq(comparator_2_eq));  // open: gt, lt
  Comparator #(.width(16), .mode("twosComplement")) comparator_3 (
    .a(\总周期数 ), .b(16'h4), .eq(comparator_3_eq));  // open: gt, lt
  Comparator #(.width(16), .mode("twosComplement")) comparator_4 (
    .a(\总周期数 ), .b(16'h7), .eq(comparator_4_eq));  // open: gt, lt
  Hex_Digit_Display hex_digit_display_6 (.value(LedData[7:4]));  // open: dp
  Hex_Digit_Display hex_digit_display_7 (.value(LedData[11:8]));  // open: dp
  Clock #(.highDuration(1), .lowDuration(1)) clock_1 (.out(clock_1_out));
  // Probe on EX_PC[19:0]
  // RiscV_Probe riscv_probe_3: pin names not known; wires that end beside it: clock_1_out, EX_IR, CLK
  Multiplexer #(.select(1), .width(32), .disabled("Z"), .enable("false")) multiplexer_3 (
    .in0(PC_q), .in1(INT_addr), .out(IF_PC), .sel(INT));
  Comparator #(.width(32), .mode("twosComplement")) comparator_5 (
    .a(IF_IR), .b(32'h200073), .eq(IF_URET));  // open: gt, lt
  or or_5 (or_5_out, d_ff_1_q, IR1_q);
  or or_6 (or_6_out, d_ff_2_q, IR2_q);
  or or_7 (or_7_out, d_ff_3_q, IR3_q);
  or or_8 (or_8_out, comparator_1_eq, comparator_2_eq);
  Pull_Resistor #(.pull(0)) pull_resistor_1 (.node(IRA));
  assign IRA = or_8_out ? ~CLK : 1'bz;  // Controlled_Inverter controlled_inverter_1
  Pull_Resistor #(.pull(0)) pull_resistor_2 (.node(IRB));
  assign IRB = comparator_3_eq ? ~CLK : 1'bz;  // Controlled_Inverter controlled_inverter_2
  Pull_Resistor #(.pull(0)) pull_resistor_3 (.node(IRC));
  assign IRC = comparator_4_eq ? ~CLK : 1'bz;  // Controlled_Inverter controlled_inverter_3
  Hex_Digit_Display hex_digit_display_8 (.value(LedData[3:0]));  // open: dp
  and and_2 (and_2_out, or_5_out, ~IR1_Reset);  // AND_Gate
  and and_3 (and_3_out, or_6_out, ~IR2_Reset);  // AND_Gate
  and and_4 (and_4_out, or_7_out, ~IR3_Reset);  // AND_Gate
  // Probe on \总周期数 
  // Probe on M_PC[19:0]
  // RiscV_Probe riscv_probe_4: pin names not known; wires that end beside it: MEM_IR
  Adder #(.width(32)) adder_1 (.a(IF_PC), .b(32'h4), .out(PC_4));  // open: cin, cout
  // RiscV_Probe riscv_probe_5: pin names not known; wires that end beside it: IF_IR
  D_Flip_Flop #(.trigger("rising"), .Pre_Clr_Positions("LEGACY"), .NegatePresetClear("false"), .enable("true"), .NewFFLayout("false")) u_IR1 (
    .clk(CLK), .D(and_2_out), .Q(IR1_q), .reset(RST));  // open: Qn, preset, en
  D_Flip_Flop #(.trigger("rising"), .Pre_Clr_Positions("LEGACY"), .NegatePresetClear("false"), .enable("true"), .NewFFLayout("false")) u_IR2 (
    .clk(CLK), .D(and_3_out), .Q(IR2_q), .reset(RST));  // open: Qn, preset, en
  D_Flip_Flop #(.trigger("rising"), .Pre_Clr_Positions("LEGACY"), .NegatePresetClear("false"), .enable("true"), .NewFFLayout("false")) u_IR3 (
    .clk(CLK), .D(and_4_out), .Q(IR3_q), .reset(RST));  // open: Qn, preset, en
  // Probe on \总周期数 
  // Probe on \无条件分支数 
  // Probe on \条件分支成功数 
  // Probe on \插入气泡数 
  // Probe on \LoadUse次数 
  ROM #(.addrWidth(10), .dataWidth(32), .Select("high")) rom_1 (.addr(IF_PC[11:2]), .data(IF_IR));
  and and_5 (and_5_out, ~stall, or_9_out);  // AND_Gate
  or or_9 (or_9_out, ~halt, Go);  // OR_Gate
  // Probe on IF_PC[11:0]
  // Probe on WB_PC[19:0]
  // RiscV_Probe riscv_probe_6: pin names not known; wires that end beside it: WB_IR
  or or_10 (or_10_out, id_ex_1_jalr_2[1], id_ex_1_jalr_2[0]);
  IF_ID if_id_1 (
    .IR(IF_IR), .PC(IF_PC), .PC_4(PC_4), .IR_2(ID_IR), .PC_2(ID_PC), .PC_4_2(if_id_1_pc_4_2),
    .branch(or_10_out), .reset(RST), .en(and_5_out), .clk(CLK), .ID_PredictJump(ID_URET),
    .IF_PredictJump(IF_URET));
  Priority_Encoder #(.select(2), .disabled("Z")) priority_encoder_1 (
    .in1(IR1_q), .in2(IR2_q), .in3(IR3_q), .out(IR_id), .gs(priority_encoder_1_gs));  // open: in0, en_out, en_in
  // Probe on EX_PC[11:0]
  // Probe on ID_PC[11:0]
  \单周期硬布线控制器  \u_单周期硬布线控制器_1  (
    .Funct({ID_IR[30], ID_IR[25], ID_IR[14:12]}), .OP(ID_IR[6:2]), .ALU_OP(\单周期硬布线控制器_1_alu_op ),
    .MemToReg(\单周期硬布线控制器_1_memtoreg ), .MemWrite(\单周期硬布线控制器_1_memwrite ), .ALU_SRC(\单周期硬布线控制器_1_alu_src ),
    .RegWrite(\单周期硬布线控制器_1_regwrite ), .ecall(ecall), .S_type(S_type), .JALR(\单周期硬布线控制器_1_jalr ),
    .BEQ(\单周期硬布线控制器_1_beq ), .JAL(JAL), .BNE(\单周期硬布线控制器_1_bne ), .in_3(ID_IR[21]), .uret(\单周期硬布线控制器_1_uret ),
    .BLTU(\单周期硬布线控制器_1_bltu ), .LB(\单周期硬布线控制器_1_lb ), .rs1_used(\单周期硬布线控制器_1_rs1_used ),
    .rs2_used(\单周期硬布线控制器_1_rs2_used ));  // open: U_Type, CSR, SLTIU
  Multiplexer #(.select(1), .width(5), .disabled("Z"), .enable("false")) multiplexer_4 (
    .in0(ID_IR[19:15]), .in1(5'b10001), .out(multiplexer_4_out), .sel(ecall));
  Multiplexer #(.select(1), .width(5), .disabled("Z"), .enable("false")) multiplexer_5 (
    .in0(ID_IR[24:20]), .in1(5'b01010), .out(multiplexer_5_out), .sel(ecall));
  Multiplexer #(.select(2), .width(32), .disabled("Z"), .enable("false")) multiplexer_6 (
    .in1(32'h30ac), .in2(32'h3150), .in3(32'h31f4), .out(INT_addr), .sel(IR_id));  // open: in0
  and and_6 (Interrupt, priority_encoder_1_gs, IE);
  Multiplexer #(.select(1), .width(1), .disabled("Z"), .enable("false")) multiplexer_7 (
    .in0(1'b1), .in1(CLK), .out(multiplexer_7_out), .sel(INT));
  // Probe on M_PC[11:0]
  D_Flip_Flop #(.trigger("high"), .Pre_Clr_Positions("LEGACY"), .NegatePresetClear("false"), .enable("true"), .NewFFLayout("false")) d_ff_4 (.Q(d_ff_4_q));  // open: clk, D, Qn, preset, en, reset
  // Probe on 13'hc
  // Probe on multiplexer_4_out
  // Probe on multiplexer_5_out
  assign bit_extender_1_out = {{20{ID_IR[31]}}, ID_IR[31:20]};  // Bit_Extender bit_extender_1
  assign bit_extender_2_out = {{20{ID_IR[31]}}, {ID_IR[31:25], ID_IR[11:7]}};  // Bit_Extender bit_extender_2
  assign bit_extender_3_out = {{20{ID_IR[31]}}, {ID_IR[31], ID_IR[7], ID_IR[30:25], ID_IR[11:8]}};  // Bit_Extender bit_extender_3
  assign bit_extender_4_out = {{12{ID_IR[31]}}, {ID_IR[31], ID_IR[19:12], ID_IR[20], ID_IR[30:21]}};  // Bit_Extender bit_extender_4
  Counter #(.width(1), .max('h1), .ongoal("wrap"), .trigger("rising"), .behavior("new")) counter_1 (
    .D(1'b1), .Q(INT), .clk(Interrupt), .clr(or_11_out));  // open: load, count, carry, preset, down
  or or_11 (or_11_out, RST, counter_2_q);
  Counter #(.width(1), .max('h1), .ongoal("wrap"), .trigger("rising"), .behavior("new")) counter_2 (
    .D(1'b1), .Q(counter_2_q), .clk(multiplexer_7_out), .clr(or_12_out));  // open: load, count, carry, preset, down
  or or_12 (or_12_out, counter_2_q, RST);
  // Probe on WB_PC[11:0]
  Comparator #(.width(13), .mode("twosComplement")) comparator_6 (
    .a(CNT_num), .b(13'hc), .eq(comparator_6_eq), .lt(comparator_6_lt));  // open: gt
  Clock #(.highDuration(1), .lowDuration(1)) clock_2 (.out(clock_2_out));
  not not_1 (not_1_out, CLK);
  Multiplexer #(.select(1), .width(32), .disabled("Z"), .enable("false")) multiplexer_8 (
    .in0(bit_extender_1_out), .in1(bit_extender_2_out), .out(multiplexer_8_out), .sel(S_type));
  Multiplexer #(.select(1), .width(32), .disabled("Z"), .enable("false")) multiplexer_9 (
    .in0(bit_extender_3_out), .in1(bit_extender_4_out), .out(multiplexer_9_out), .sel(JAL));
  nand nand_1 (nand_1_out, d_ff_4_q, comparator_6_eq);
  Counter #(.width(13), .max('h1fff), .ongoal("stay"), .trigger("rising"), .behavior("old")) counter_3 (
    .count(comparator_6_lt), .Q(CNT_num), .clk(clock_2_out));  // open: load, D, carry, clr, preset
  Regifile regifile_1 (
    .Din(RDin), .Clk(not_1_out), .R1(regifile_1_r1), .R2(regifile_1_r2), .WE(RegWrite), .W_num(WB_rd),
    .R1_num(multiplexer_4_out), .R2_num(multiplexer_5_out));
  or or_13 (or_13_out, ~halt, Go);  // OR_Gate
  assign CLK = nand_1_out ? clock_2_out : 1'bz;  // Controlled_Buffer controlled_buffer_1
  ID_EX id_ex_1 (
    .BEQ(\单周期硬布线控制器_1_beq ), .BNE(\单周期硬布线控制器_1_bne ), .MemToReg(\单周期硬布线控制器_1_memtoreg ),
    .MemWrite(\单周期硬布线控制器_1_memwrite ), .AluSrc(\单周期硬布线控制器_1_alu_src ), .RegWrite(\单周期硬布线控制器_1_regwrite ),
    .S_type(S_type), .ecall(ecall), .Jal(JAL), .Jalr(\单周期硬布线控制器_1_jalr ), .LB(\单周期硬布线控制器_1_lb ),
    .BLTU(\单周期硬布线控制器_1_bltu ), .Uret(\单周期硬布线控制器_1_uret ), .AluOP(\单周期硬布线控制器_1_alu_op ), .rd(ID_IR[11:7]),
    .R1(regifile_1_r1), .R2(regifile_1_r2), .imm_1(multiplexer_8_out), .imm_2(multiplexer_9_out), .PC(ID_PC),
    .PC_4(if_id_1_pc_4_2), .IR(ID_IR), .RS1_Forward(\重定向处理逻辑_1_rs1_forward ),
    .RS2_Forward(\重定向处理逻辑_1_rs2_forward ), .BEQ_2(id_ex_1_beq_2), .BNE_2(id_ex_1_bne_2),
    .MemToReg_2(id_ex_1_memtoreg_2), .MemWrite_2(id_ex_1_memwrite_2), .AluSrc_2(id_ex_1_alusrc_2),
    .RegWrite_2(id_ex_1_regwrite_2), .ecall_2(EX_ecall), .Jal_2(id_ex_1_jal_2), .Jalr_2(id_ex_1_jalr_2[0]),
    .LB_2(id_ex_1_lb_2), .BLTU_2(id_ex_1_bltu_2), .AluOP_2(id_ex_1_aluop_2), .rd_2(id_ex_1_rd_2),
    .R1_2(id_ex_1_r1_2), .R2_2(id_ex_1_r2_2), .imm_1_2(id_ex_1_imm_1_2), .imm_2_2(id_ex_1_imm_2_2),
    .PC_2(EX_PC), .PC_4_2(id_ex_1_pc_4_2), .IR_2(EX_IR), .RS1_Forward_2(id_ex_1_rs1_forward_2),
    .RS2_Forward_2(id_ex_1_rs2_forward_2), .reset(or_14_out), .flush(Flush), .en(or_13_out), .clk(CLK),
    .ID_PredictJump(ID_URET), .EX_PredictJump(EX_URET));  // open: S_type_2, Uret_2, U_Type, U_Type_2, AUIPC_result, AUIPC_result_2, SLTIU, SLTIU_2
  or or_14 (or_14_out, RST, Interrupt);
  Register #(.width(1), .trigger("rising"), .Select("low")) register_1 (
    .D(1'b0), .Q(register_1_q), .clk(not_2_out), .clr(RST), .preset(Interrupt));  // open: en, cs
  not not_2 (not_2_out, IF_URET);
  Register #(.width(1), .trigger("rising"), .Select("low")) register_2 (
    .D(BranchTaken), .Q(register_2_q[0]), .clk(CLK), .clr(RST));  // open: en
  Pull_Resistor #(.pull(1)) pull_resistor_4 (.node(CLK));
  Multiplexer #(.select(2), .width(32), .disabled("Z"), .enable("false")) multiplexer_10 (
    .in0(id_ex_1_r1_2), .in1(RDin), .in2(MEM_ALURes), .out(multiplexer_10_out), .sel(id_ex_1_rs1_forward_2));  // open: in3
  not not_3 (IE, register_1_q);
  Register #(.width(1), .trigger("rising"), .Select("low")) register_3 (
    .D(stall), .Q(register_2_q[2]), .clk(CLK), .clr(RST));  // open: en
  Multiplexer #(.select(2), .width(32), .disabled("Z"), .enable("false")) multiplexer_11 (
    .in0(id_ex_1_r2_2), .in1(RDin), .in2(MEM_ALURes), .out(multiplexer_11_out), .sel(id_ex_1_rs2_forward_2));  // open: in3
  Register #(.width(1), .trigger("rising"), .Select("low")) register_4 (
    .D(register_2_q[0]), .Q(register_2_q[1]), .clk(CLK), .clr(RST));  // open: en
  or or_15 (id_ex_1_jalr_2[1], id_ex_1_jal_2, BranchSuc);
  and and_7 (and_7_out, id_ex_1_bne_2, ~Equ);  // AND_Gate
  Register #(.width(2), .trigger("rising"), .Select("low")) register_5 (
    .D(IR_id), .Q(register_5_q), .clk(Interrupt), .clr(RST));  // open: en
  Demultiplexer #(.select(2), .width(1), .tristate("false"), .disabled("Z"), .enable("false")) demultiplexer_1 (
    .out1(IR1_Reset), .out2(IR2_Reset), .out3(IR3_Reset), .in(IF_URET), .sel(register_5_q));  // open: out0
  or or_16 (BranchSuc, and_7_out, and_9_out, and_8_out);
  and and_8 (and_8_out, id_ex_1_bltu_2, Less);
  and and_9 (and_9_out, Equ, id_ex_1_beq_2);
  Multiplexer #(.select(1), .width(32), .disabled("Z"), .enable("false")) multiplexer_12 (
    .in0(multiplexer_11_out), .in1(id_ex_1_imm_1_2), .out(multiplexer_12_out), .sel(id_ex_1_alusrc_2));
  Shifter #(.width(32), .shift("ll")) shifter_1 (.in(id_ex_1_imm_2_2), .\dist (5'b00001), .out(shifter_1_out));
  Comparator #(.width(32), .mode("twosComplement")) comparator_7 (
    .a(multiplexer_10_out), .b(32'ha), .eq(comparator_7_eq));  // open: gt, lt
  not not_4 (not_4_out, comparator_7_eq);
  Multiplexer #(.select(3), .width(32), .disabled("Z"), .enable("false")) multiplexer_13 (
    .in0(EX_PC), .in1(IF_PC), .in2(ID_PC), .in4(ID_PC), .out(multiplexer_13_out), .sel(register_2_q));  // open: in3, in5, in6, in7
  and and_10 (and_10_out, ~ID_URET, ~EX_URET);  // AND_Gate
  or or_17 (BranchTaken, id_ex_1_jalr_2[1], id_ex_1_jalr_2[0]);
  or or_18 (\无条件跳转 , id_ex_1_jalr_2[0], id_ex_1_jal_2);
  ALU alu_1 (
    .X(multiplexer_10_out), .Y(multiplexer_12_out), .AluOP(id_ex_1_aluop_2), .Equal(Equ), .Result(ALU_addr),
    .out_6(Less));  // open: Result_2, out_4
  and and_11 (EX_halt, comparator_7_eq, EX_ecall);
  and and_12 (and_12_out, not_4_out, EX_ecall);
  Register #(.width(32), .trigger("rising"), .Select("low")) u_EPC (
    .D(multiplexer_13_out), .en(and_10_out), .Q(EPC), .clk(Interrupt), .clr(RST));
  Adder #(.width(32)) adder_2 (.a(shifter_1_out), .b(EX_PC), .out(jumpAddr));  // open: cin, cout
  Register #(.width(32), .trigger("rising"), .Select("low")) register_6 (
    .D(multiplexer_11_out), .en(and_12_out), .Q(LedData), .clk(CLK), .clr(RST));
  EX_MEM ex_mem_1 (
    .Jal(id_ex_1_jal_2), .Jalr(id_ex_1_jalr_2[0]), .MemToReg(id_ex_1_memtoreg_2),
    .MemWrite(id_ex_1_memwrite_2), .LB(id_ex_1_lb_2), .RegWrite(id_ex_1_regwrite_2), .halt(EX_halt),
    .rd(id_ex_1_rd_2), .Result(ALU_addr), .WriteData(multiplexer_11_out), .IR(EX_IR), .PC(EX_PC),
    .PC_4(id_ex_1_pc_4_2), .Jal_2(ex_mem_1_jal_2), .Jalr_2(ex_mem_1_jalr_2),
    .MemToReg_2(ex_mem_1_memtoreg_2), .MemWrite_2(MemWrite), .LB_2(LBU), .RegWrite_2(ex_mem_1_regwrite_2),
    .halt_2(ex_mem_1_halt_2), .rd_2(ex_mem_1_rd_2), .Result_2(MEM_ALURes), .WriteData_2(MDin), .IR_2(MEM_IR),
    .PC_2(M_PC), .PC_4_2(ex_mem_1_pc_4_2), .reset(or_20_out), .en(or_19_out), .clk(CLK));  // open: U_Type, U_Type_2, AUIPC_result, AUIPC_result_2, SLTIU, SLTIU_2, LESS, LESS_2
  or or_19 (or_19_out, ~halt, Go);  // OR_Gate
  or or_20 (or_20_out, RST, Interrupt);
  RAM #(.addrWidth(10), .dataWidth(32), .bus("separate"), .Select("high")) ram_1 (
    .addr(MEM_ALURes[11:2]), .din(MDin), .data(MemData), .str(MemWrite), .sel(1'b1), .clk(CLK), .ld(1'b1),
    .clr(RST));
  Multiplexer #(.select(2), .width(8), .disabled("Z"), .enable("false")) multiplexer_14 (
    .in0(MemData[7:0]), .in1(MemData[15:8]), .in2(MemData[23:16]), .in3(MemData[31:24]),
    .out(multiplexer_14_out), .sel(MEM_ALURes[1:0]));
  Multiplexer #(.select(1), .width(32), .disabled("Z"), .enable("false")) multiplexer_15 (
    .in0(MemData), .in1(bit_extender_5_out), .out(multiplexer_15_out), .sel(LBU));
  assign bit_extender_5_out = {{24{multiplexer_14_out[7]}}, multiplexer_14_out};  // Bit_Extender bit_extender_5
  MEM_WB mem_wb_1 (
    .Jal(ex_mem_1_jal_2), .Jalr(ex_mem_1_jalr_2), .MemToReg(ex_mem_1_memtoreg_2),
    .RegWrite(ex_mem_1_regwrite_2), .halt(ex_mem_1_halt_2), .rd(ex_mem_1_rd_2), .ALUResult(MEM_ALURes),
    .ReadData(multiplexer_15_out), .IR(MEM_IR), .PC(M_PC), .PC_4(ex_mem_1_pc_4_2), .Jal_2(mem_wb_1_jal_2),
    .Jalr_2(mem_wb_1_jalr_2), .MemToReg_2(mem_wb_1_memtoreg_2[0]), .RegWrite_2(RegWrite),
    .halt_2(mem_wb_1_halt_2), .rd_2(WB_rd), .ALUResult_2(mem_wb_1_aluresult_2),
    .ReadData_2(mem_wb_1_readdata_2), .IR_2(WB_IR), .PC_2(WB_PC), .PC_4_2(mem_wb_1_pc_4_2), .reset(RST),
    .en(or_21_out), .clk(CLK));  // open: U_Type, U_Type_2, AUIPC_result, AUIPC_result_2, SLTIU, SLTIU_2, LESS, LESS_2
  or or_21 (or_21_out, ~halt, Go);  // OR_Gate
  D_Flip_Flop #(.trigger("rising"), .Pre_Clr_Positions("ABOVE_BELOW"), .NegatePresetClear("false"), .enable("true"), .NewFFLayout("true")) d_ff_5 (
    .clk(mem_wb_1_halt_2), .D(1'b1), .Q(halt), .en(1'b1), .reset(Go));  // open: Qn, preset
  or or_22 (mem_wb_1_memtoreg_2[1], mem_wb_1_jalr_2, mem_wb_1_jal_2);
  Multiplexer #(.select(2), .width(32), .disabled("Z"), .enable("false")) multiplexer_16 (
    .in0(mem_wb_1_aluresult_2), .in1(mem_wb_1_readdata_2), .in2(mem_wb_1_pc_4_2), .out(RDin),
    .sel(mem_wb_1_memtoreg_2));  // open: in3
  Counter #(.width(16), .max('hffff), .ongoal("wrap"), .trigger("rising"), .behavior("new")) counter_4 (
    .count(BranchSuc), .Q(\条件分支成功数 ), .clk(and_13_out), .clr(RST));  // open: load, D, carry, preset, down
  and and_13 (and_13_out, ~halt, CLK);  // AND_Gate
  Counter #(.width(16), .max('hffff), .ongoal("wrap"), .trigger("rising"), .behavior("new")) counter_5 (
    .count(Flush), .Q(\插入气泡数 ), .clk(and_14_out), .clr(RST));  // open: load, D, carry, preset, down
  and and_14 (and_14_out, ~halt, CLK);  // AND_Gate
  Counter #(.width(16), .max('hffff), .ongoal("wrap"), .trigger("rising"), .behavior("new")) counter_6 (
    .count(\无条件跳转 ), .Q(\无条件分支数 ), .clk(and_15_out), .clr(RST));  // open: load, D, carry, preset, down
  and and_15 (and_15_out, ~halt, CLK);  // AND_Gate
  Counter #(.width(16), .max('hffff), .ongoal("wrap"), .trigger("rising"), .behavior("new")) counter_7 (
    .count(CLK), .Q(\总周期数 ), .clk(and_16_out), .clr(RST));  // open: load, D, carry, preset, down
  and and_16 (and_16_out, ~halt, CLK);  // AND_Gate
  Counter #(.width(16), .max('hffff), .ongoal("wrap"), .trigger("rising"), .behavior("new")) counter_8 (
    .count(stall), .Q(\LoadUse次数 ), .clk(and_17_out), .clr(RST));  // open: load, D, carry, preset, down
  and and_17 (and_17_out, ~halt, CLK);  // AND_Gate

  // Other names for the same wires on the sheet: IR[31:0] = ID_IR; MEM_PC[31:0] = M_PC; WB_RegWrite = RegWrite

  // Notes on the sheet:
  //   中断源
  //   时空图监测，可删除
  //   中断等待指示
  //   单级中断测试信号模拟器
  //   数码管输出
  //   指令存储器
  //   指令探针
  //   Reset 
  //   Reset 
  //   Reset 
  //   contents of rom_1 (hex, n*v repeats v):
  //   7d000113 100413 1f41993 41f9d993 433 c00913 800b13 140413 f47413 800293 100313 499993 89e9b3 1300533
  //   2200893 73 406282b3 fe0294e3 140413 f00f93 1f47433 1c41413 800293 100313 49d993 89e9b3 1300533
  //   2200893 73 406282b3 fe0294e3 1c45413 406b0b33 b0463 f95ff06f 2b3 fff2c293 1029293 fff2e293 500533
  //   2200893 73 f5dff06f 1112023 410113 a12023 410113 812023 410113 1312023 410113 1412023 410113 1512023
  //   410113 1612023 410113 100b13 300a13 100a93 1600433 441413 14469b3 1300533 2200893 73 fe0416e3
  //   415a0a33 fe0a10e3 ffc10113 12b03 ffc10113 12a83 ffc10113 12a03 ffc10113 12983 ffc10113 12403
  //   ffc10113 12503 ffc10113 12883 200073 1112023 410113 a12023 410113 812023 410113 1312023 410113
  //   1412023 410113 1512023 410113 1612023 410113 200b13 300a13 100a93 1600433 441413 14469b3 1300533
  //   2200893 73 fe0416e3 415a0a33 fe0a10e3 ffc10113 12b03 ffc10113 12a83 ffc10113 12a03 ffc10113 12983
  //   ffc10113 12403 ffc10113 12503 ffc10113 12883 200073 1112023 410113 a12023 410113 812023 410113
  //   1312023 410113 1412023 410113 1512023 410113 1612023 410113 300b13 300a13 100a93 1600433 441413
  //   14469b3 1300533 2200893 73 fe0416e3 415a0a33 fe0a10e3 ffc10113 12b03 ffc10113 12a83 ffc10113 12a03
  //   ffc10113 12983 ffc10113 12403 ffc10113 12503 ffc10113 12883 200073
  //   指令字
  //   J
  //   控制位
  //   RS1_used
  //   I
  //   S
  //   B
  //   流水调试日志用
  //   暂停节拍，不能为0
  //   RS2_used
  //   JALR
  //   Beq
  //   Bne
  //   MemToReg
  //   MemWrite
  //   AluOP
  //   AluSrcB
  //   RegWrite
  //   S_type
  //   戳工具置1进入计数暂停模式，ctrl+k时钟自动运行到对应节拍暂停
  //   ctrl+k关闭时钟连续运行，将控制位置零，进入单步调试模式调试
  //   Uret
  //   LBU
  //   BLT
  //   JAL
  //   ecall
  //   imm_1
  //   imm_2
  //   rd
  //   IR
  //   PC
  //   PC+4
  //   可计数暂停的时钟源
  //   为方便自动评测，需要输出流水线各段保存的PC值，注意是PC不是PC+4，另外ID段寄存器写入信息，Mem段内存写入信息也要输出
  //   BranchTaken
  //   EX.MemToReg
  //   EX.RegWrite
  //   LBU
  //   JALR
  //   JAL
  //   MemToReg
  //   MemWrite
  //   RegWrite
  //   rd
  //   IR
  //   PC
  //   PC+4
  //   数据存储器
  //   MEM.RegWrite
  //   JALR
  //   JAL
  //   MemToReg
  //   RegWrite
  //   halt
  //   ALUResult
  //   ReadData
  //   Mem.rd
endmodule

module BHB (
  input  [31:0] IF_PC,
  input  [31:0] EX_PC,
  input  [31:0] EX_BranchAddr,
  input  BranchTaken,
  input  EX_Branch,
  input  clk,
  output [31:0] PredictAddr,
  output ID_PredictJump
);

  wire and_17_out, and_18_out, and_19_out, and_28_out, and_29_out, and_30_out, and_31_out, and_32_out,
       and_33_out, and_34_out, and_35_out, comparator_1_eq, comparator_2_eq, comparator_3_eq,
       comparator_4_eq, comparator_5_eq, comparator_6_eq, comparator_7_eq, comparator_8_eq, comparator_9_eq,
       comparator_10_eq, comparator_11_eq, comparator_12_eq, comparator_13_eq, comparator_14_eq,
       comparator_15_eq, comparator_16_eq, d_ff_1_q, d_ff_2_q, d_ff_3_q, d_ff_4_q, d_ff_5_q, d_ff_6_q,
       d_ff_7_q, d_ff_8_q, decoder_1_out0, decoder_1_out1, decoder_1_out2, decoder_1_out3, decoder_1_out4,
       decoder_1_out5, decoder_1_out6, decoder_1_out7, demultiplexer_1_out0, demultiplexer_1_out1,
       demultiplexer_1_out2, demultiplexer_1_out3, demultiplexer_1_out4, demultiplexer_1_out5,
       demultiplexer_1_out6, demultiplexer_1_out7, EX_Hit, EX_Miss, L0, L1, L2, L3, L4, L5, L6, L7, M0, M1,
       M2, M3, M4, M5, M6, M7, not_1_out, not_2_out, not_3_out, not_4_out, not_5_out, not_6_out, not_7_out,
       not_8_out, or_1_out, or_2_out, or_3_out, or_4_out, or_5_out, or_6_out, or_7_out, or_8_out, or_9_out,
       or_10_out, or_12_out, or_13_out, or_14_out, or_15_out, or_16_out, or_17_out, or_18_out, or_19_out,
       priority_encoder_1_gs, v0, v1, v2, v3, v4, v5, v6, v7, Write0, Write1, Write2, Write3, Write4, Write5,
       Write6, Write7;
  wire [0:0] controlled_buffer_9_out, controlled_buffer_10_out, controlled_buffer_11_out,
       controlled_buffer_12_out, controlled_buffer_13_out, controlled_buffer_14_out,
       controlled_buffer_15_out, controlled_buffer_16_out;
  wire [1:0] fsm_1_nextlow, fsm_2_nextlow, fsm_3_nextlow, fsm_4_nextlow, fsm_5_nextlow, fsm_6_nextlow,
       fsm_7_nextlow, fsm_8_nextlow, Predict0, Predict1, Predict2, Predict3, Predict4, Predict5, Predict6,
       Predict7;
  wire [2:0] max_1_maxid, max_2_maxid, max_3_maxid, max_4_maxid, max_5_maxid, max_6_maxid, max_7_maxid,
       priority_encoder_1_out;
  wire [15:0] C0, C1, C2, C3, C4, C5, C6, C7, max_1_max, max_2_max, max_3_max, max_4_max, max_5_max,
       max_6_max;
  wire [31:0] register_17_q, register_18_q, register_19_q, register_20_q, register_21_q, register_22_q,
       register_23_q, register_24_q, Tag0, Tag1, Tag2, Tag3, Tag4, Tag5, Tag6, Tag7;

  Register #(.width(1), .trigger("rising"), .Select("low")) register_1 (
    .D(1'b1), .en(Write5), .Q(v5), .clk(clk));  // open: clr
  Register #(.width(1), .trigger("rising"), .Select("low")) register_2 (
    .D(1'b1), .en(Write6), .Q(v6), .clk(clk));  // open: clr
  Register #(.width(1), .trigger("rising"), .Select("low")) register_3 (
    .D(1'b1), .en(Write7), .Q(v7), .clk(clk));  // open: clr
  Register #(.width(1), .trigger("rising"), .Select("low")) register_4 (
    .D(1'b1), .en(Write0), .Q(v0), .clk(clk));  // open: clr
  Register #(.width(1), .trigger("rising"), .Select("low")) register_5 (
    .D(1'b1), .en(Write1), .Q(v1), .clk(clk));  // open: clr
  Register #(.width(1), .trigger("rising"), .Select("low")) register_6 (
    .D(1'b1), .en(Write2), .Q(v2), .clk(clk));  // open: clr
  Register #(.width(1), .trigger("rising"), .Select("low")) register_7 (
    .D(1'b1), .en(Write3), .Q(v3), .clk(clk));  // open: clr
  Register #(.width(1), .trigger("rising"), .Select("low")) register_8 (
    .D(1'b1), .en(Write4), .Q(v4), .clk(clk));  // open: clr
  Register #(.width(32), .trigger("rising"), .Select("low")) register_9 (
    .D(EX_PC), .en(Write0), .Q(Tag0), .clk(clk));  // open: clr
  Register #(.width(32), .trigger("rising"), .Select("low")) register_10 (
    .D(EX_PC), .en(Write1), .Q(Tag1), .clk(clk));  // open: clr
  Register #(.width(32), .trigger("rising"), .Select("low")) register_11 (
    .D(EX_PC), .en(Write2), .Q(Tag2), .clk(clk));  // open: clr
  Register #(.width(32), .trigger("rising"), .Select("low")) register_12 (
    .D(EX_PC), .en(Write3), .Q(Tag3), .clk(clk));  // open: clr
  Register #(.width(32), .trigger("rising"), .Select("low")) register_13 (
    .D(EX_PC), .en(Write4), .Q(Tag4), .clk(clk));  // open: clr
  Register #(.width(32), .trigger("rising"), .Select("low")) register_14 (
    .D(EX_PC), .en(Write5), .Q(Tag5), .clk(clk));  // open: clr
  Register #(.width(32), .trigger("rising"), .Select("low")) register_15 (
    .D(EX_PC), .en(Write6), .Q(Tag6), .clk(clk));  // open: clr
  Register #(.width(32), .trigger("rising"), .Select("low")) register_16 (
    .D(EX_PC), .en(Write7), .Q(Tag7), .clk(clk));  // open: clr
  or or_1 (or_1_out, Write5, L5);
  or or_2 (or_2_out, Write6, L6);
  or or_3 (or_3_out, Write7, L7);
  Counter #(.width(16), .max('hffff), .ongoal("wrap"), .trigger("rising"), .behavior("new")) counter_1 (
    .Q(C0), .clk(clk), .clr(d_ff_1_q));  // open: load, D, count, carry, preset, down
  D_Flip_Flop #(.trigger("rising"), .Pre_Clr_Positions("ABOVE_BELOW"), .NegatePresetClear("false"), .enable("false"), .NewFFLayout("false")) d_ff_1 (
    .clk(clk), .D(or_4_out), .Q(d_ff_1_q));  // open: Qn, preset, reset
  or or_4 (or_4_out, Write0, L0);
  Counter #(.width(16), .max('hffff), .ongoal("wrap"), .trigger("rising"), .behavior("new")) counter_2 (
    .Q(C1), .clk(clk), .clr(d_ff_2_q));  // open: load, D, count, carry, preset, down
  D_Flip_Flop #(.trigger("rising"), .Pre_Clr_Positions("ABOVE_BELOW"), .NegatePresetClear("false"), .enable("false"), .NewFFLayout("false")) d_ff_2 (
    .clk(clk), .D(or_5_out), .Q(d_ff_2_q));  // open: Qn, preset, reset
  or or_5 (or_5_out, Write1, L1);
  Counter #(.width(16), .max('hffff), .ongoal("wrap"), .trigger("rising"), .behavior("new")) counter_3 (
    .Q(C2), .clk(clk), .clr(d_ff_3_q));  // open: load, D, count, carry, preset, down
  D_Flip_Flop #(.trigger("rising"), .Pre_Clr_Positions("ABOVE_BELOW"), .NegatePresetClear("false"), .enable("false"), .NewFFLayout("false")) d_ff_3 (
    .clk(clk), .D(or_6_out), .Q(d_ff_3_q));  // open: Qn, preset, reset
  or or_6 (or_6_out, Write2, L2);
  Counter #(.width(16), .max('hffff), .ongoal("wrap"), .trigger("rising"), .behavior("new")) counter_4 (
    .Q(C3), .clk(clk), .clr(d_ff_4_q));  // open: load, D, count, carry, preset, down
  D_Flip_Flop #(.trigger("rising"), .Pre_Clr_Positions("ABOVE_BELOW"), .NegatePresetClear("false"), .enable("false"), .NewFFLayout("false")) d_ff_4 (
    .clk(clk), .D(or_7_out), .Q(d_ff_4_q));  // open: Qn, preset, reset
  or or_7 (or_7_out, Write3, L3);
  Counter #(.width(16), .max('hffff), .ongoal("wrap"), .trigger("rising"), .behavior("new")) counter_5 (
    .Q(C4), .clk(clk), .clr(d_ff_5_q));  // open: load, D, count, carry, preset, down
  D_Flip_Flop #(.trigger("rising"), .Pre_Clr_Positions("ABOVE_BELOW"), .NegatePresetClear("false"), .enable("false"), .NewFFLayout("false")) d_ff_5 (
    .clk(clk), .D(or_8_out), .Q(d_ff_5_q));  // open: Qn, preset, reset
  or or_8 (or_8_out, Write4, L4);
  Counter #(.width(16), .max('hffff), .ongoal("wrap"), .trigger("rising"), .behavior("new")) counter_6 (
    .Q(C5), .clk(clk), .clr(d_ff_6_q));  // open: load, D, count, carry, preset, down
  D_Flip_Flop #(.trigger("rising"), .Pre_Clr_Positions("ABOVE_BELOW"), .NegatePresetClear("false"), .enable("false"), .NewFFLayout("false")) d_ff_6 (
    .clk(clk), .D(or_1_out), .Q(d_ff_6_q));  // open: Qn, preset, reset
  Counter #(.width(16), .max('hffff), .ongoal("wrap"), .trigger("rising"), .behavior("new")) counter_7 (
    .Q(C6), .clk(clk), .clr(d_ff_7_q));  // open: load, D, count, carry, preset, down
  D_Flip_Flop #(.trigger("rising"), .Pre_Clr_Positions("ABOVE_BELOW"), .NegatePresetClear("false"), .enable("false"), .NewFFLayout("false")) d_ff_7 (
    .clk(clk), .D(or_2_out), .Q(d_ff_7_q));  // open: Qn, preset, reset
  Counter #(.width(16), .max('hffff), .ongoal("wrap"), .trigger("rising"), .behavior("new")) counter_8 (
    .Q(C7), .clk(clk), .clr(d_ff_8_q));  // open: load, D, count, carry, preset, down
  D_Flip_Flop #(.trigger("rising"), .Pre_Clr_Positions("ABOVE_BELOW"), .NegatePresetClear("false"), .enable("false"), .NewFFLayout("false")) d_ff_8 (
    .clk(clk), .D(or_3_out), .Q(d_ff_8_q));  // open: Qn, preset, reset
  assign PredictAddr = L0 ? register_17_q : 32'bz;  // Controlled_Buffer controlled_buffer_1
  Register #(.width(32), .trigger("rising"), .Select("low")) register_17 (
    .D(EX_BranchAddr), .en(Write0), .Q(register_17_q), .clk(clk));  // open: clr
  assign PredictAddr = L1 ? register_18_q : 32'bz;  // Controlled_Buffer controlled_buffer_2
  Register #(.width(32), .trigger("rising"), .Select("low")) register_18 (
    .D(EX_BranchAddr), .en(Write1), .Q(register_18_q), .clk(clk));  // open: clr
  assign PredictAddr = L2 ? register_19_q : 32'bz;  // Controlled_Buffer controlled_buffer_3
  Register #(.width(32), .trigger("rising"), .Select("low")) register_19 (
    .D(EX_BranchAddr), .en(Write2), .Q(register_19_q), .clk(clk));  // open: clr
  Register #(.width(32), .trigger("rising"), .Select("low")) register_20 (
    .D(EX_BranchAddr), .en(Write3), .Q(register_20_q), .clk(clk));  // open: clr
  assign PredictAddr = L3 ? register_20_q : 32'bz;  // Controlled_Buffer controlled_buffer_4
  assign PredictAddr = L4 ? register_21_q : 32'bz;  // Controlled_Buffer controlled_buffer_5
  Register #(.width(32), .trigger("rising"), .Select("low")) register_21 (
    .D(EX_BranchAddr), .en(Write4), .Q(register_21_q), .clk(clk));  // open: clr
  assign PredictAddr = L5 ? register_22_q : 32'bz;  // Controlled_Buffer controlled_buffer_6
  Register #(.width(32), .trigger("rising"), .Select("low")) register_22 (
    .D(EX_BranchAddr), .en(Write5), .Q(register_22_q), .clk(clk));  // open: clr
  Register #(.width(32), .trigger("rising"), .Select("low")) register_23 (
    .D(EX_BranchAddr), .en(Write6), .Q(register_23_q), .clk(clk));  // open: clr
  assign PredictAddr = L6 ? register_23_q : 32'bz;  // Controlled_Buffer controlled_buffer_7
  Register #(.width(32), .trigger("rising"), .Select("low")) register_24 (
    .D(EX_BranchAddr), .en(Write7), .Q(register_24_q), .clk(clk));  // open: clr
  assign PredictAddr = L7 ? register_24_q : 32'bz;  // Controlled_Buffer controlled_buffer_8
  Comparator #(.width(32), .mode("twosComplement")) comparator_1 (
    .a(EX_PC), .b(Tag0), .eq(comparator_1_eq));  // open: gt, lt
  Comparator #(.width(32), .mode("twosComplement")) comparator_2 (
    .a(Tag0), .b(IF_PC), .eq(comparator_2_eq));  // open: gt, lt
  Comparator #(.width(32), .mode("twosComplement")) comparator_3 (
    .a(EX_PC), .b(Tag1), .eq(comparator_3_eq));  // open: gt, lt
  Comparator #(.width(32), .mode("twosComplement")) comparator_4 (
    .a(Tag1), .b(IF_PC), .eq(comparator_4_eq));  // open: gt, lt
  Comparator #(.width(32), .mode("twosComplement")) comparator_5 (
    .a(EX_PC), .b(Tag2), .eq(comparator_5_eq));  // open: gt, lt
  Comparator #(.width(32), .mode("twosComplement")) comparator_6 (
    .a(Tag2), .b(IF_PC), .eq(comparator_6_eq));  // open: gt, lt
  Comparator #(.width(32), .mode("twosComplement")) comparator_7 (
    .a(EX_PC), .b(Tag3), .eq(comparator_7_eq));  // open: gt, lt
  Comparator #(.width(32), .mode("twosComplement")) comparator_8 (
    .a(Tag3), .b(IF_PC), .eq(comparator_8_eq));  // open: gt, lt
  Comparator #(.width(32), .mode("twosComplement")) comparator_9 (
    .a(EX_PC), .b(Tag4), .eq(comparator_9_eq));  // open: gt, lt
  Comparator #(.width(32), .mode("twosComplement")) comparator_10 (
    .a(Tag4), .b(IF_PC), .eq(comparator_10_eq));  // open: gt, lt
  Comparator #(.width(32), .mode("twosComplement")) comparator_11 (
    .a(EX_PC), .b(Tag5), .eq(comparator_11_eq));  // open: gt, lt
  Comparator #(.width(32), .mode("twosComplement")) comparator_12 (
    .a(Tag5), .b(IF_PC), .eq(comparator_12_eq));  // open: gt, lt
  Comparator #(.width(32), .mode("twosComplement")) comparator_13 (
    .a(EX_PC), .b(Tag6), .eq(comparator_13_eq));  // open: gt, lt
  Comparator #(.width(32), .mode("twosComplement")) comparator_14 (
    .a(Tag6), .b(IF_PC), .eq(comparator_14_eq));  // open: gt, lt
  Comparator #(.width(32), .mode("twosComplement")) comparator_15 (
    .a(EX_PC), .b(Tag7), .eq(comparator_15_eq));  // open: gt, lt
  Comparator #(.width(32), .mode("twosComplement")) comparator_16 (
    .a(Tag7), .b(IF_PC), .eq(comparator_16_eq));  // open: gt, lt
  and and_1 (M0, comparator_1_eq, v0);
  and and_2 (L0, v0, comparator_2_eq);
  and and_3 (M1, comparator_3_eq, v1);
  and and_4 (L1, v1, comparator_4_eq);
  and and_5 (M2, comparator_5_eq, v2);
  and and_6 (L2, v2, comparator_6_eq);
  and and_7 (M3, comparator_7_eq, v3);
  and and_8 (L3, v3, comparator_8_eq);
  and and_9 (M4, comparator_9_eq, v4);
  and and_10 (L4, v4, comparator_10_eq);
  and and_11 (M5, comparator_11_eq, v5);
  and and_12 (L5, v5, comparator_12_eq);
  and and_13 (M6, comparator_13_eq, v6);
  and and_14 (L6, v6, comparator_14_eq);
  and and_15 (M7, comparator_15_eq, v7);
  and and_16 (L7, v7, comparator_16_eq);
  not not_1 (not_1_out, v0);
  not not_2 (not_2_out, v1);
  not not_3 (not_3_out, v2);
  not not_4 (not_4_out, v3);
  not not_5 (not_5_out, v4);
  not not_6 (not_6_out, v5);
  not not_7 (not_7_out, v6);
  not not_8 (not_8_out, v7);
  or or_9 (or_9_out, M0, M1, M2, M3);
  or or_10 (or_10_out, M4, M5, M6, M7);
  Priority_Encoder #(.select(3), .disabled(0)) priority_encoder_1 (
    .in0(not_1_out), .in1(not_2_out), .in2(not_3_out), .in3(not_4_out), .in4(not_5_out), .in5(not_6_out),
    .in6(not_7_out), .in7(not_8_out), .out(priority_encoder_1_out), .gs(priority_encoder_1_gs));  // open: en_out, en_in
  and and_17 (and_17_out, v0, v1, v2, v3);
  and and_18 (and_18_out, v4, v5, v6, v7);
  MAX max_1 (.X(C0), .Y(C1), .Xid(3'b000), .Yid(3'b001), .MAX(max_1_max), .MAXID(max_1_maxid));
  MAX max_2 (.X(C2), .Y(C3), .Xid(3'b010), .Yid(3'b011), .MAX(max_2_max), .MAXID(max_2_maxid));
  MAX max_3 (.X(C4), .Y(C5), .Xid(3'b100), .Yid(3'b101), .MAX(max_3_max), .MAXID(max_3_maxid));
  MAX max_4 (.X(C6), .Y(C7), .Xid(3'b110), .Yid(3'b111), .MAX(max_4_max), .MAXID(max_4_maxid));
  or or_11 (EX_Hit, or_9_out, or_10_out);
  and and_19 (and_19_out, and_17_out, and_18_out);
  MAX max_5 (.X(max_1_max), .Y(max_2_max), .Xid(max_1_maxid), .Yid(max_2_maxid), .MAX(max_5_max), .MAXID(max_5_maxid));
  MAX max_6 (.X(max_3_max), .Y(max_4_max), .Xid(max_3_maxid), .Yid(max_4_maxid), .MAX(max_6_max), .MAXID(max_6_maxid));
  not not_9 (EX_Miss, EX_Hit);
  Decoder #(.select(3), .tristate("false"), .disabled(0), .enable("true")) decoder_1 (
    .out0(decoder_1_out0), .out1(decoder_1_out1), .out2(decoder_1_out2), .out3(decoder_1_out3),
    .out4(decoder_1_out4), .out5(decoder_1_out5), .out6(decoder_1_out6), .out7(decoder_1_out7),
    .sel(priority_encoder_1_out), .en(priority_encoder_1_gs));
  Demultiplexer #(.select(3), .width(1), .tristate("false"), .disabled(0), .enable("false")) demultiplexer_1 (
    .out0(demultiplexer_1_out0), .out1(demultiplexer_1_out1), .out2(demultiplexer_1_out2),
    .out3(demultiplexer_1_out3), .out4(demultiplexer_1_out4), .out5(demultiplexer_1_out5),
    .out6(demultiplexer_1_out6), .out7(demultiplexer_1_out7), .in(and_19_out), .sel(max_7_maxid));
  MAX max_7 (.X(max_5_max), .Y(max_6_max), .Xid(max_5_maxid), .Yid(max_6_maxid), .MAXID(max_7_maxid));  // open: MAX
  or or_12 (or_12_out, decoder_1_out0, demultiplexer_1_out0);
  or or_13 (or_13_out, decoder_1_out1, demultiplexer_1_out1);
  or or_14 (or_14_out, decoder_1_out2, demultiplexer_1_out2);
  or or_15 (or_15_out, decoder_1_out3, demultiplexer_1_out3);
  or or_16 (or_16_out, decoder_1_out4, demultiplexer_1_out4);
  or or_17 (or_17_out, decoder_1_out5, demultiplexer_1_out5);
  or or_18 (or_18_out, decoder_1_out6, demultiplexer_1_out6);
  or or_19 (or_19_out, decoder_1_out7, demultiplexer_1_out7);
  and and_20 (Write0, or_12_out, EX_Miss, EX_Branch);
  and and_21 (Write1, or_13_out, EX_Miss, EX_Branch);
  and and_22 (Write2, or_14_out, EX_Miss, EX_Branch);
  and and_23 (Write3, or_15_out, EX_Miss, EX_Branch);
  and and_24 (Write4, or_16_out, EX_Miss, EX_Branch);
  and and_25 (Write5, or_17_out, EX_Miss, EX_Branch);
  and and_26 (Write6, or_18_out, EX_Miss, EX_Branch);
  and and_27 (Write7, or_19_out, EX_Miss, EX_Branch);
  assign {ID_PredictJump, controlled_buffer_9_out[0]} = L0 ? Predict0 : 2'bz;  // Controlled_Buffer controlled_buffer_9
  assign {ID_PredictJump, controlled_buffer_10_out[0]} = L1 ? Predict1 : 2'bz;  // Controlled_Buffer controlled_buffer_10
  assign {ID_PredictJump, controlled_buffer_11_out[0]} = L2 ? Predict2 : 2'bz;  // Controlled_Buffer controlled_buffer_11
  assign {ID_PredictJump, controlled_buffer_12_out[0]} = L3 ? Predict3 : 2'bz;  // Controlled_Buffer controlled_buffer_12
  assign {ID_PredictJump, controlled_buffer_13_out[0]} = L4 ? Predict4 : 2'bz;  // Controlled_Buffer controlled_buffer_13
  assign {ID_PredictJump, controlled_buffer_14_out[0]} = L5 ? Predict5 : 2'bz;  // Controlled_Buffer controlled_buffer_14
  assign {ID_PredictJump, controlled_buffer_15_out[0]} = L6 ? Predict6 : 2'bz;  // Controlled_Buffer controlled_buffer_15
  assign {ID_PredictJump, controlled_buffer_16_out[0]} = L7 ? Predict7 : 2'bz;  // Controlled_Buffer controlled_buffer_16
  Pull_Resistor #(.pull(0)) pull_resistor_1 (.node(ID_PredictJump));
  FSM fsm_1 (
    .High(Predict0[1]), .Low(Predict0[0]), .Jump(BranchTaken), .NextHigh(fsm_1_nextlow[1]),
    .NextLow(fsm_1_nextlow[0]));
  FSM fsm_2 (
    .High(Predict1[1]), .Low(Predict1[0]), .Jump(BranchTaken), .NextHigh(fsm_2_nextlow[1]),
    .NextLow(fsm_2_nextlow[0]));
  FSM fsm_3 (
    .High(Predict2[1]), .Low(Predict2[0]), .Jump(BranchTaken), .NextHigh(fsm_3_nextlow[1]),
    .NextLow(fsm_3_nextlow[0]));
  FSM fsm_4 (
    .High(Predict3[1]), .Low(Predict3[0]), .Jump(BranchTaken), .NextHigh(fsm_4_nextlow[1]),
    .NextLow(fsm_4_nextlow[0]));
  FSM fsm_5 (
    .High(Predict4[1]), .Low(Predict4[0]), .Jump(BranchTaken), .NextHigh(fsm_5_nextlow[1]),
    .NextLow(fsm_5_nextlow[0]));
  FSM fsm_6 (
    .High(Predict5[1]), .Low(Predict5[0]), .Jump(BranchTaken), .NextHigh(fsm_6_nextlow[1]),
    .NextLow(fsm_6_nextlow[0]));
  FSM fsm_7 (
    .High(Predict6[1]), .Low(Predict6[0]), .Jump(BranchTaken), .NextHigh(fsm_7_nextlow[1]),
    .NextLow(fsm_7_nextlow[0]));
  FSM fsm_8 (
    .High(Predict7[1]), .Low(Predict7[0]), .Jump(BranchTaken), .NextHigh(fsm_8_nextlow[1]),
    .NextLow(fsm_8_nextlow[0]));
  and and_28 (and_28_out, EX_Branch, M0);
  and and_29 (and_29_out, EX_Branch, M1);
  and and_30 (and_30_out, EX_Branch, M2);
  and and_31 (and_31_out, EX_Branch, M3);
  and and_32 (and_32_out, EX_Branch, M4);
  and and_33 (and_33_out, EX_Branch, M5);
  and and_34 (and_34_out, EX_Branch, M6);
  and and_35 (and_35_out, EX_Branch, M7);
  Register #(.width(2), .trigger("rising"), .Select("low")) register_25 (
    .D(fsm_1_nextlow), .en(and_28_out), .Q(Predict0), .clk(clk));  // open: clr
  Register #(.width(2), .trigger("rising"), .Select("low")) register_26 (
    .D(fsm_2_nextlow), .en(and_29_out), .Q(Predict1), .clk(clk));  // open: clr
  Register #(.width(2), .trigger("rising"), .Select("low")) register_27 (
    .D(fsm_3_nextlow), .en(and_30_out), .Q(Predict2), .clk(clk));  // open: clr
  Register #(.width(2), .trigger("rising"), .Select("low")) register_28 (
    .D(fsm_4_nextlow), .en(and_31_out), .Q(Predict3), .clk(clk));  // open: clr
  Register #(.width(2), .trigger("rising"), .Select("low")) register_29 (
    .D(fsm_5_nextlow), .en(and_32_out), .Q(Predict4), .clk(clk));  // open: clr
  Register #(.width(2), .trigger("rising"), .Select("low")) register_30 (
    .D(fsm_6_nextlow), .en(and_33_out), .Q(Predict5), .clk(clk));  // open: clr
  Register #(.width(2), .trigger("rising"), .Select("low")) register_31 (
    .D(fsm_7_nextlow), .en(and_34_out), .Q(Predict6), .clk(clk));  // open: clr
  Register #(.width(2), .trigger("rising"), .Select("low")) register_32 (
    .D(fsm_8_nextlow), .en(and_35_out), .Q(Predict7), .clk(clk));  // open: clr

  // Other names for the same wires on the sheet: JumpAddr[31:0] = PredictAddr; Tag[31:0] = EX_PC
endmodule

module \动态分支预测  (
  output RegWrite,
  output MemWrite,
  output [31:0] IF_PC,
  output [31:0] ID_PC,
  output [31:0] EX_PC,
  output [31:0] M_PC,
  output [31:0] WB_PC,
  output [31:0] RDin,
  output [31:0] MDin,
  output [31:0] LedData
);

  wire and_1_out, and_2_out, and_3_out, and_4_out, and_5_out, and_7_out, and_8_out, and_9_out, and_10_out,
       and_11_out, and_12_out, Branch, BranchSuc, BranchTaken, CLK, clock_1_out, clock_2_out,
       comparator_1_eq, comparator_1_lt, comparator_2_eq, d_ff_1_q, ecall, Equ, EX_Branch, EX_ecall, EX_halt,
       EX_JAL, EX_JALR, ex_mem_1_halt_2, ex_mem_1_jal_2, ex_mem_1_jalr_2, ex_mem_1_less_2,
       ex_mem_1_memtoreg_2, ex_mem_1_regwrite_2, ex_mem_1_sltiu_2, ex_mem_1_u_type_2, EX_PredictJump, Flush,
       Go, halt, id_ex_1_alusrc_2, id_ex_1_beq_2, id_ex_1_bltu_2, id_ex_1_bne_2, id_ex_1_lb_2,
       id_ex_1_memtoreg_2, id_ex_1_memwrite_2, id_ex_1_regwrite_2, id_ex_1_sltiu_2, id_ex_1_u_type_2, ID_JAL,
       if_id_1_id_predictjump, IF_PredictJump, IR1, IR2, IR3, LB, Less, mem_wb_1_halt_2, mem_wb_1_jal_2,
       mem_wb_1_jalr_2, mem_wb_1_less_2, mem_wb_1_memtoreg_2, mem_wb_1_sltiu_2, mem_wb_1_u_type_2,
       nand_1_out, not_1_out, not_2_out, or_1_out, or_2_out, or_3_out, or_4_out, or_11_out, or_12_out,
       PredictError, RST, S_type, stall, W1, W2, W3, \单周期硬布线控制器_1_alu_src , \单周期硬布线控制器_1_beq ,
       \单周期硬布线控制器_1_bltu , \单周期硬布线控制器_1_bne , \单周期硬布线控制器_1_jalr , \单周期硬布线控制器_1_lb , \单周期硬布线控制器_1_memtoreg ,
       \单周期硬布线控制器_1_memwrite , \单周期硬布线控制器_1_regwrite , \单周期硬布线控制器_1_rs1_used , \单周期硬布线控制器_1_rs2_used ,
       \单周期硬布线控制器_1_sltiu , \单周期硬布线控制器_1_u_type , \单周期硬布线控制器_1_uret , \无条件跳转 ;
  wire [1:0] id_ex_1_rs1_forward_2, id_ex_1_rs2_forward_2, or_14_out, \重定向处理逻辑_1_rs1_forward ,
       \重定向处理逻辑_1_rs2_forward ;
  wire [1:1] or_5_out;
  wire [3:0] id_ex_1_aluop_2, \单周期硬布线控制器_1_alu_op ;
  wire [4:0] ex_mem_1_rd_2, id_ex_1_rd_2, multiplexer_4_out, multiplexer_5_out, WB_rd;
  wire [12:0] CNT_num;
  wire [15:0] \LoadUse次数 , multiplexer_14_out, \总周期数 , \插入气泡数 , \无条件分支数 , \条件分支成功数 ;
  wire [31:0] adder_1_out, adder_3_out, ALU_addr, AUIPC_Res, bhb_1_predictaddr, bit_extender_1_out,
       bit_extender_2_out, bit_extender_3_out, bit_extender_4_out, bit_extender_5_out, bit_extender_6_out,
       bit_extender_7_out, bit_extender_8_out, EX_IR, ex_mem_1_pc_4_2, ex_mem_1_result_2, EX_RS1, EX_RS2,
       id_ex_1_auipc_result_2, id_ex_1_imm_1_2, id_ex_1_imm_2_2, id_ex_1_pc_4_2, id_ex_1_r1_2, id_ex_1_r2_2,
       ID_IR, if_id_1_pc_4_2, IF_IR, IF_PC_4, jumpAddr, MEM_ALURes, MEM_IR, mem_wb_1_aluresult_2,
       mem_wb_1_auipc_result_2, mem_wb_1_pc_4_2, mem_wb_1_readdata_2, MemData, multiplexer_1_out,
       multiplexer_2_out, multiplexer_3_out, multiplexer_6_out, multiplexer_7_out, multiplexer_8_out,
       multiplexer_12_out, multiplexer_13_out, multiplexer_16_out, multiplexer_17_out, PredictAddr,
       regifile_1_r1, regifile_1_r2, shifter_1_out, shifter_2_out, WB_IR;

  Button \u_总复位  (.out(RST));
  Button _1 (.out(IR1));
  Button _2 (.out(IR2));
  Button _3 (.out(IR3));
  // Probe on \总周期数 
  // Probe on \总周期数 
  Button \u_继续运行  (.out(Go));
  LED #(.active("true")) led_1 (.in(W1));
  LED #(.active("true")) led_2 (.in(W2));
  LED #(.active("true")) led_3 (.in(W3));
  \重定向处理逻辑  \u_重定向处理逻辑_1  (
    .RS1_used(\单周期硬布线控制器_1_rs1_used ), .EX_RegWrite(id_ex_1_regwrite_2), .EX_MemToReg(id_ex_1_memtoreg_2),
    .IR(ID_IR), .RS2_used(\单周期硬布线控制器_1_rs2_used ), .MEM_RegWrite(ex_mem_1_regwrite_2), .EX_rd(id_ex_1_rd_2),
    .Ecall(ecall), .BranchTaken(BranchTaken), .MEM_rd(ex_mem_1_rd_2), .Stall(stall), .Flush(Flush),
    .RS1_Forward(\重定向处理逻辑_1_rs1_forward ), .RS2_Forward(\重定向处理逻辑_1_rs2_forward ));
  Adder #(.width(32)) adder_1 (.a(EX_PC), .b(32'h4), .out(adder_1_out));  // open: cin, cout
  Hex_Digit_Display hex_digit_display_1 (.value(LedData[31:28]));  // open: dp
  // Probe on IF_PC[19:0]
  // RiscV_Probe riscv_probe_1: pin names not known; wires that end beside it: IF_IR
  and and_1 (and_1_out, ~halt, ~stall);  // AND_Gate
  or or_1 (or_1_out, and_1_out, Go);
  // Probe on PredictAddr
  Multiplexer #(.select(2), .width(32), .disabled("Z"), .enable("false")) multiplexer_1 (
    .in0(adder_1_out), .in1(ALU_addr), .in2(jumpAddr), .out(multiplexer_1_out), .sel({or_5_out[1], EX_JALR}));  // open: in3
  Hex_Digit_Display hex_digit_display_2 (.value(LedData[27:24]));  // open: dp
  Hex_Digit_Display hex_digit_display_3 (.value(LedData[23:20]));  // open: dp
  // Probe on ID_PC[19:0]
  // RiscV_Probe riscv_probe_2: pin names not known; wires that end beside it: ID_IR
  Multiplexer #(.select(1), .width(32), .disabled("Z"), .enable("false")) multiplexer_2 (
    .in0(PredictAddr), .in1(multiplexer_1_out), .out(multiplexer_2_out), .sel(PredictError));
  Hex_Digit_Display hex_digit_display_4 (.value(LedData[15:12]));  // open: dp
  Hex_Digit_Display hex_digit_display_5 (.value(LedData[19:16]));  // open: dp
  Register #(.width(32), .trigger("rising"), .Select("low")) PC (
    .D(multiplexer_2_out), .en(or_1_out), .Q(IF_PC), .clk(CLK), .clr(RST));
  Hex_Digit_Display hex_digit_display_6 (.value(LedData[7:4]));  // open: dp
  Hex_Digit_Display hex_digit_display_7 (.value(LedData[11:8]));  // open: dp
  Clock #(.highDuration(1), .lowDuration(1)) clock_1 (.out(clock_1_out));
  // Probe on EX_PC[19:0]
  // RiscV_Probe riscv_probe_3: pin names not known; wires that end beside it: clock_1_out, EX_IR, CLK
  Adder #(.width(32)) adder_2 (.a(IF_PC), .b(32'h4), .out(IF_PC_4));  // open: cin, cout
  Hex_Digit_Display hex_digit_display_8 (.value(LedData[3:0]));  // open: dp
  ROM #(.addrWidth(10), .dataWidth(32), .Select("high")) rom_1 (.addr(IF_PC[11:2]), .data(IF_IR));
  // RiscV_Probe riscv_probe_4: pin names not known; wires that end beside it: IF_IR
  and and_2 (and_2_out, ~stall, or_2_out);  // AND_Gate
  or or_2 (or_2_out, ~halt, Go);  // OR_Gate
  // Probe on \总周期数 
  // Probe on M_PC[19:0]
  // RiscV_Probe riscv_probe_5: pin names not known; wires that end beside it: MEM_IR
  IF_ID if_id_1 (
    .IR(IF_IR), .PC(IF_PC), .PC_4(IF_PC_4), .IR_2(ID_IR), .PC_2(ID_PC), .PC_4_2(if_id_1_pc_4_2),
    .branch(PredictError), .reset(RST), .en(and_2_out), .clk(CLK), .ID_PredictJump(if_id_1_id_predictjump),
    .IF_PredictJump(IF_PredictJump));
  // Probe on \总周期数 
  // Probe on \无条件分支数 
  // Probe on \条件分支成功数 
  // Probe on \插入气泡数 
  // Probe on \LoadUse次数 
  Multiplexer #(.select(2), .width(32), .disabled("Z"), .enable("false")) multiplexer_3 (
    .in0(IF_PC), .in1(ALU_addr), .in2(jumpAddr), .out(multiplexer_3_out), .sel({EX_JAL, EX_JALR}));  // open: in3
  // Probe on IF_PC[11:0]
  // Probe on WB_PC[19:0]
  // RiscV_Probe riscv_probe_6: pin names not known; wires that end beside it: WB_IR
  \单周期硬布线控制器  \u_单周期硬布线控制器_1  (
    .Funct({ID_IR[30], ID_IR[25], ID_IR[14:12]}), .OP(ID_IR[6:2]), .ALU_OP(\单周期硬布线控制器_1_alu_op ),
    .MemToReg(\单周期硬布线控制器_1_memtoreg ), .MemWrite(\单周期硬布线控制器_1_memwrite ), .ALU_SRC(\单周期硬布线控制器_1_alu_src ),
    .RegWrite(\单周期硬布线控制器_1_regwrite ), .ecall(ecall), .S_type(S_type), .JALR(\单周期硬布线控制器_1_jalr ),
    .BEQ(\单周期硬布线控制器_1_beq ), .JAL(ID_JAL), .BNE(\单周期硬布线控制器_1_bne ), .in_3(ID_IR[21]),
    .uret(\单周期硬布线控制器_1_uret ), .BLTU(\单周期硬布线控制器_1_bltu ), .LB(\单周期硬布线控制器_1_lb ),
    .U_Type(\单周期硬布线控制器_1_u_type ), .rs1_used(\单周期硬布线控制器_1_rs1_used ), .rs2_used(\单周期硬布线控制器_1_rs2_used ),
    .SLTIU(\单周期硬布线控制器_1_sltiu ));  // open: CSR
  Multiplexer #(.select(1), .width(5), .disabled("Z"), .enable("false")) multiplexer_4 (
    .in0(ID_IR[19:15]), .in1(5'b10001), .out(multiplexer_4_out), .sel(ecall));
  Multiplexer #(.select(1), .width(5), .disabled("Z"), .enable("false")) multiplexer_5 (
    .in0(ID_IR[24:20]), .in1(5'b01010), .out(multiplexer_5_out), .sel(ecall));
  assign bit_extender_1_out = {{12{ID_IR[31]}}, ID_IR[31:12]};  // Bit_Extender bit_extender_1
  Multiplexer #(.select(1), .width(32), .disabled("Z"), .enable("false")) multiplexer_6 (
    .in0(multiplexer_3_out), .in1(jumpAddr), .out(multiplexer_6_out), .sel(Branch));
  // Probe on ID_PC[11:0]
  // Probe on EX_PC[11:0]
  // Probe on multiplexer_4_out
  // Probe on multiplexer_5_out
  assign bit_extender_2_out = {{20{ID_IR[31]}}, ID_IR[31:20]};  // Bit_Extender bit_extender_2
  Multiplexer #(.select(1), .width(32), .disabled("Z"), .enable("false")) multiplexer_7 (
    .in0(bit_extender_2_out), .in1(bit_extender_3_out), .out(multiplexer_7_out), .sel(S_type));
  assign bit_extender_3_out = {{20{ID_IR[31]}}, {ID_IR[31:25], ID_IR[11:7]}};  // Bit_Extender bit_extender_3
  assign bit_extender_4_out = {{20{ID_IR[31]}}, {ID_IR[31], ID_IR[7], ID_IR[30:25], ID_IR[11:8]}};  // Bit_Extender bit_extender_4
  Multiplexer #(.select(1), .width(32), .disabled("Z"), .enable("false")) multiplexer_8 (
    .in0(bit_extender_4_out), .in1(bit_extender_5_out), .out(multiplexer_8_out), .sel(ID_JAL));
  assign bit_extender_5_out = {{12{ID_IR[31]}}, {ID_IR[31], ID_IR[19:12], ID_IR[20], ID_IR[30:21]}};  // Bit_Extender bit_extender_5
  Shifter #(.width(32), .shift("ll")) shifter_1 (.in(bit_extender_1_out), .\dist (5'b01100), .out(shifter_1_out));
  // Probe on M_PC[11:0]
  D_Flip_Flop #(.trigger("high"), .Pre_Clr_Positions("LEGACY"), .NegatePresetClear("false"), .enable("true"), .NewFFLayout("false")) d_ff_1 (.Q(d_ff_1_q));  // open: clk, D, Qn, preset, en, reset
  // Probe on 13'hc
  not not_1 (not_1_out, CLK);
  Regifile regifile_1 (
    .Din(RDin), .Clk(not_1_out), .R1(regifile_1_r1), .R2(regifile_1_r2), .WE(RegWrite), .W_num(WB_rd),
    .R1_num(multiplexer_4_out), .R2_num(multiplexer_5_out));
  or or_3 (or_3_out, ~halt, Go);  // OR_Gate
  Adder #(.width(32)) adder_3 (.a(shifter_1_out), .b(ID_PC), .out(adder_3_out));  // open: cin, cout
  BHB bhb_1 (
    .IF_PC(IF_PC), .EX_PC(EX_PC), .EX_BranchAddr(multiplexer_6_out), .BranchTaken(BranchTaken),
    .EX_Branch(EX_Branch), .clk(CLK), .ID_PredictJump(IF_PredictJump), .PredictAddr(bhb_1_predictaddr));
  // Probe on WB_PC[11:0]
  Comparator #(.width(13), .mode("twosComplement")) comparator_1 (
    .a(CNT_num), .b(13'hc), .eq(comparator_1_eq), .lt(comparator_1_lt));  // open: gt
  Clock #(.highDuration(1), .lowDuration(1)) clock_2 (.out(clock_2_out));
  or or_4 (or_4_out, stall, PredictError);
  ID_EX id_ex_1 (
    .BEQ(\单周期硬布线控制器_1_beq ), .BNE(\单周期硬布线控制器_1_bne ), .MemToReg(\单周期硬布线控制器_1_memtoreg ),
    .MemWrite(\单周期硬布线控制器_1_memwrite ), .AluSrc(\单周期硬布线控制器_1_alu_src ), .RegWrite(\单周期硬布线控制器_1_regwrite ),
    .S_type(S_type), .ecall(ecall), .Jal(ID_JAL), .Jalr(\单周期硬布线控制器_1_jalr ), .LB(\单周期硬布线控制器_1_lb ),
    .BLTU(\单周期硬布线控制器_1_bltu ), .Uret(\单周期硬布线控制器_1_uret ), .AluOP(\单周期硬布线控制器_1_alu_op ), .rd(ID_IR[11:7]),
    .R1(regifile_1_r1), .R2(regifile_1_r2), .imm_1(multiplexer_7_out), .imm_2(multiplexer_8_out), .PC(ID_PC),
    .PC_4(if_id_1_pc_4_2), .IR(ID_IR), .RS1_Forward(\重定向处理逻辑_1_rs1_forward ),
    .RS2_Forward(\重定向处理逻辑_1_rs2_forward ), .BEQ_2(id_ex_1_beq_2), .BNE_2(id_ex_1_bne_2),
    .MemToReg_2(id_ex_1_memtoreg_2), .MemWrite_2(id_ex_1_memwrite_2), .AluSrc_2(id_ex_1_alusrc_2),
    .RegWrite_2(id_ex_1_regwrite_2), .ecall_2(EX_ecall), .Jal_2(EX_JAL), .Jalr_2(EX_JALR),
    .LB_2(id_ex_1_lb_2), .BLTU_2(id_ex_1_bltu_2), .AluOP_2(id_ex_1_aluop_2), .rd_2(id_ex_1_rd_2),
    .R1_2(id_ex_1_r1_2), .R2_2(id_ex_1_r2_2), .imm_1_2(id_ex_1_imm_1_2), .imm_2_2(id_ex_1_imm_2_2),
    .PC_2(EX_PC), .PC_4_2(id_ex_1_pc_4_2), .IR_2(EX_IR), .RS1_Forward_2(id_ex_1_rs1_forward_2),
    .RS2_Forward_2(id_ex_1_rs2_forward_2), .reset(RST), .flush(or_4_out), .en(or_3_out), .clk(CLK),
    .ID_PredictJump(if_id_1_id_predictjump), .EX_PredictJump(EX_PredictJump), .U_Type(\单周期硬布线控制器_1_u_type ),
    .U_Type_2(id_ex_1_u_type_2), .AUIPC_result(adder_3_out), .AUIPC_result_2(id_ex_1_auipc_result_2),
    .SLTIU(\单周期硬布线控制器_1_sltiu ), .SLTIU_2(id_ex_1_sltiu_2));  // open: S_type_2, Uret_2
  Multiplexer #(.select(1), .width(32), .disabled("Z"), .enable("false")) multiplexer_9 (
    .in0(IF_PC_4), .in1(bhb_1_predictaddr), .out(PredictAddr), .sel(IF_PredictJump));
  nand nand_1 (nand_1_out, d_ff_1_q, comparator_1_eq);
  Counter #(.width(13), .max('h1fff), .ongoal("stay"), .trigger("rising"), .behavior("old")) counter_1 (
    .count(comparator_1_lt), .Q(CNT_num), .clk(clock_2_out));  // open: load, D, carry, clr, preset
  assign CLK = nand_1_out ? clock_2_out : 1'bz;  // Controlled_Buffer controlled_buffer_1
  Multiplexer #(.select(2), .width(32), .disabled("Z"), .enable("false")) multiplexer_10 (
    .in0(id_ex_1_r1_2), .in1(RDin), .in2(MEM_ALURes), .out(EX_RS1), .sel(id_ex_1_rs1_forward_2));  // open: in3
  Pull_Resistor #(.pull(1)) pull_resistor_1 (.node(CLK));
  and and_3 (and_3_out, id_ex_1_bne_2, ~Equ);  // AND_Gate
  Multiplexer #(.select(2), .width(32), .disabled("Z"), .enable("false")) multiplexer_11 (
    .in0(id_ex_1_r2_2), .in1(RDin), .in2(MEM_ALURes), .out(EX_RS2), .sel(id_ex_1_rs2_forward_2));  // open: in3
  or or_5 (or_5_out[1], EX_JAL, BranchSuc);
  or or_6 (BranchSuc, and_3_out, and_4_out, and_5_out);
  and and_4 (and_4_out, Equ, id_ex_1_beq_2);
  Multiplexer #(.select(1), .width(32), .disabled("Z"), .enable("false")) multiplexer_12 (
    .in0(EX_RS2), .in1(id_ex_1_imm_1_2), .out(multiplexer_12_out), .sel(id_ex_1_alusrc_2));
  Comparator #(.width(32), .mode("twosComplement")) comparator_2 (
    .a(EX_RS1), .b(32'ha), .eq(comparator_2_eq));  // open: gt, lt
  or or_7 (BranchTaken, or_5_out[1], EX_JALR);
  and and_5 (and_5_out, id_ex_1_bltu_2, Less);
  or or_8 (\无条件跳转 , EX_JALR, EX_JAL);
  or or_9 (Branch, id_ex_1_bltu_2, id_ex_1_beq_2, id_ex_1_bne_2);
  Shifter #(.width(32), .shift("ll")) shifter_2 (.in(id_ex_1_imm_2_2), .\dist (5'b00001), .out(shifter_2_out));
  not not_2 (not_2_out, comparator_2_eq);
  or or_10 (EX_Branch, EX_JALR, EX_JAL, Branch);
  ALU alu_1 (
    .X(EX_RS1), .Y(multiplexer_12_out), .AluOP(id_ex_1_aluop_2), .Equal(Equ), .Result(ALU_addr), .out_6(Less));  // open: Result_2, out_4
  Adder #(.width(32)) adder_4 (.a(shifter_2_out), .b(EX_PC), .out(jumpAddr));  // open: cin, cout
  and and_6 (EX_halt, comparator_2_eq, EX_ecall);
  Register #(.width(32), .trigger("rising"), .Select("low")) register_1 (
    .D(EX_RS2), .en(and_7_out), .Q(LedData), .clk(CLK), .clr(RST));
  and and_7 (and_7_out, not_2_out, EX_ecall);
  xor xor_1 (PredictError, BranchTaken, EX_PredictJump);
  EX_MEM ex_mem_1 (
    .Jal(EX_JAL), .Jalr(EX_JALR), .MemToReg(id_ex_1_memtoreg_2), .MemWrite(id_ex_1_memwrite_2),
    .LB(id_ex_1_lb_2), .RegWrite(id_ex_1_regwrite_2), .halt(EX_halt), .rd(id_ex_1_rd_2), .Result(ALU_addr),
    .WriteData(EX_RS2), .IR(EX_IR), .PC(EX_PC), .PC_4(id_ex_1_pc_4_2), .Jal_2(ex_mem_1_jal_2),
    .Jalr_2(ex_mem_1_jalr_2), .MemToReg_2(ex_mem_1_memtoreg_2), .MemWrite_2(MemWrite), .LB_2(LB),
    .RegWrite_2(ex_mem_1_regwrite_2), .halt_2(ex_mem_1_halt_2), .rd_2(ex_mem_1_rd_2),
    .Result_2(ex_mem_1_result_2), .WriteData_2(MDin), .IR_2(MEM_IR), .PC_2(M_PC), .PC_4_2(ex_mem_1_pc_4_2),
    .reset(RST), .en(or_11_out), .clk(CLK), .U_Type(id_ex_1_u_type_2), .U_Type_2(ex_mem_1_u_type_2),
    .AUIPC_result(id_ex_1_auipc_result_2), .AUIPC_result_2(AUIPC_Res), .SLTIU(id_ex_1_sltiu_2),
    .SLTIU_2(ex_mem_1_sltiu_2), .LESS(Less), .LESS_2(ex_mem_1_less_2));
  or or_11 (or_11_out, ~halt, Go);  // OR_Gate
  Multiplexer #(.select(1), .width(32), .disabled("Z"), .enable("false")) multiplexer_13 (
    .in0(ex_mem_1_result_2), .in1(AUIPC_Res), .out(multiplexer_13_out), .sel(ex_mem_1_u_type_2));
  assign bit_extender_6_out = {{31{1'b0}}, ex_mem_1_less_2};  // Bit_Extender bit_extender_6
  RAM #(.addrWidth(10), .dataWidth(32), .bus("separate"), .Select("high")) ram_1 (
    .addr(ex_mem_1_result_2[11:2]), .din(MDin), .data(MemData), .str(MemWrite), .sel(1'b1), .clk(CLK),
    .ld(1'b1), .clr(RST));
  Multiplexer #(.select(1), .width(16), .disabled("Z"), .enable("false")) multiplexer_14 (
    .in0(MemData[15:0]), .in1(MemData[31:16]), .out(multiplexer_14_out), .sel(ex_mem_1_result_2[1]));
  Multiplexer #(.select(1), .width(32), .disabled("Z"), .enable("false")) multiplexer_15 (
    .in0(multiplexer_13_out), .in1(bit_extender_6_out), .out(MEM_ALURes), .sel(ex_mem_1_sltiu_2));
  assign bit_extender_7_out = {{16{multiplexer_14_out[15]}}, multiplexer_14_out};  // Bit_Extender bit_extender_7
  Multiplexer #(.select(1), .width(32), .disabled("Z"), .enable("false")) multiplexer_16 (
    .in0(MemData), .in1(bit_extender_7_out), .out(multiplexer_16_out), .sel(LB));
  or or_12 (or_12_out, ~halt, Go);  // OR_Gate
  MEM_WB mem_wb_1 (
    .Jal(ex_mem_1_jal_2), .Jalr(ex_mem_1_jalr_2), .MemToReg(ex_mem_1_memtoreg_2),
    .RegWrite(ex_mem_1_regwrite_2), .halt(ex_mem_1_halt_2), .rd(ex_mem_1_rd_2),
    .ALUResult(ex_mem_1_result_2), .ReadData(multiplexer_16_out), .IR(MEM_IR), .PC(M_PC),
    .PC_4(ex_mem_1_pc_4_2), .Jal_2(mem_wb_1_jal_2), .Jalr_2(mem_wb_1_jalr_2),
    .MemToReg_2(mem_wb_1_memtoreg_2), .RegWrite_2(RegWrite), .halt_2(mem_wb_1_halt_2), .rd_2(WB_rd),
    .ALUResult_2(mem_wb_1_aluresult_2), .ReadData_2(mem_wb_1_readdata_2), .IR_2(WB_IR), .PC_2(WB_PC),
    .PC_4_2(mem_wb_1_pc_4_2), .reset(RST), .en(or_12_out), .clk(CLK), .U_Type(ex_mem_1_u_type_2),
    .U_Type_2(mem_wb_1_u_type_2), .AUIPC_result(AUIPC_Res), .AUIPC_result_2(mem_wb_1_auipc_result_2),
    .SLTIU(ex_mem_1_sltiu_2), .SLTIU_2(mem_wb_1_sltiu_2), .LESS(ex_mem_1_less_2), .LESS_2(mem_wb_1_less_2));
  or or_13 (or_14_out[1], mem_wb_1_jalr_2, mem_wb_1_jal_2, mem_wb_1_u_type_2);
  or or_14 (or_14_out[0], mem_wb_1_u_type_2, mem_wb_1_memtoreg_2);
  D_Flip_Flop #(.trigger("rising"), .Pre_Clr_Positions("ABOVE_BELOW"), .NegatePresetClear("false"), .enable("true"), .NewFFLayout("true")) d_ff_2 (
    .clk(mem_wb_1_halt_2), .D(1'b1), .Q(halt), .en(1'b1), .reset(Go));  // open: Qn, preset
  Multiplexer #(.select(2), .width(32), .disabled("Z"), .enable("false")) multiplexer_17 (
    .in0(mem_wb_1_aluresult_2), .in1(mem_wb_1_readdata_2), .in2(mem_wb_1_pc_4_2),
    .in3(mem_wb_1_auipc_result_2), .out(multiplexer_17_out), .sel(or_14_out));
  assign bit_extender_8_out = {{31{1'b0}}, mem_wb_1_less_2};  // Bit_Extender bit_extender_8
  Counter #(.width(16), .max('hffff), .ongoal("wrap"), .trigger("rising"), .behavior("new")) counter_2 (
    .count(BranchSuc), .Q(\条件分支成功数 ), .clk(and_8_out), .clr(RST));  // open: load, D, carry, preset, down
  and and_8 (and_8_out, ~halt, CLK);  // AND_Gate
  Counter #(.width(16), .max('hffff), .ongoal("wrap"), .trigger("rising"), .behavior("new")) counter_3 (
    .count(Flush), .Q(\插入气泡数 ), .clk(and_9_out), .clr(RST));  // open: load, D, carry, preset, down
  and and_9 (and_9_out, ~halt, CLK);  // AND_Gate
  Multiplexer #(.select(1), .width(32), .disabled("Z"), .enable("false")) multiplexer_18 (
    .in0(multiplexer_17_out), .in1(bit_extender_8_out), .out(RDin), .sel(mem_wb_1_sltiu_2));
  and and_10 (and_10_out, ~halt, CLK);  // AND_Gate
  Counter #(.width(16), .max('hffff), .ongoal("wrap"), .trigger("rising"), .behavior("new")) counter_4 (
    .count(\无条件跳转 ), .Q(\无条件分支数 ), .clk(and_11_out), .clr(RST));  // open: load, D, carry, preset, down
  and and_11 (and_11_out, ~halt, CLK);  // AND_Gate
  Counter #(.width(16), .max('hffff), .ongoal("wrap"), .trigger("rising"), .behavior("new")) counter_5 (
    .count(CLK), .Q(\总周期数 ), .clk(and_10_out), .clr(RST));  // open: load, D, carry, preset, down
  Counter #(.width(16), .max('hffff), .ongoal("wrap"), .trigger("rising"), .behavior("new")) counter_6 (
    .count(stall), .Q(\LoadUse次数 ), .clk(and_12_out), .clr(RST));  // open: load, D, carry, preset, down
  and and_12 (and_12_out, ~halt, CLK);  // AND_Gate

  // Other names for the same wires on the sheet: IR[31:0] = ID_IR; MEM_PC[31:0] = M_PC; WB_RegWrite = RegWrite

  // Notes on the sheet:
  //   中断源
  //   时空图监测，可删除
  //   中断等待指示
  //   数码管输出
  //   指令存储器
  //   contents of rom_1 (hex, n*v repeats v):
  //   100493 100006f 100493 200913 300993 100006f 100493 200913 300993 100006f 100493 200913 300993
  //   100006f 100493 200913 300993 408000ef 100413 100493 1f49493 900533 2200893 73 24d493 48463 fedff06f
  //   900533 2200893 73 100493 249493 900533 2200893 73 48463 fedff06f 100493 1f49493 900533 2200893 73
  //   4034d493 900533 2200893 73 4044d493 900533 2200893 73 4044d493 900533 2200893 73 4044d493 900533
  //   2200893 73 4044d493 900533 2200893 73 4044d493 900533 2200893 73 4044d493 900533 2200893 73 4044d493
  //   900533 2200893 73 100413 1f41993 41f9d993 433 c00913 300b13 140413 f47413 800293 100313 499993
  //   89e9b3 1300533 2200893 73 406282b3 fe0294e3 140413 f00f93 1f47433 1c41413 800293 100313 49d993
  //   89e9b3 1300533 2200893 73 406282b3 fe0294e3 1c45413 406b0b33 b0463 f95ff06f 2b3 fff2c293 829293
  //   ff2e293 500533 2200893 73 fff00413 493 84a023 140413 448493 84a023 140413 448493 84a023 140413
  //   448493 84a023 140413 448493 84a023 140413 448493 84a023 140413 448493 84a023 140413 448493 84a023
  //   140413 448493 84a023 140413 448493 84a023 140413 448493 84a023 140413 448493 84a023 140413 448493
  //   84a023 140413 448493 84a023 140413 448493 84a023 140413 448493 84a023 140413 448493 140413 433
  //   3c00493 42983 4aa03 149a2b3 28663 134a023 1442023 ffc48493 fe9412e3 800533 2200893 73 440413 3c00493
  //   fc9416e3 a00893 73 13 430497 900533 2200893 73 430497 900533 2200893 73 430497 900533 2200893 73
  //   430497 900533 2200893 73 430497 900533 2200893 73 430497 900533 2200893 73 430497 900533 2200893 73
  //   430497 900533 2200893 73 a00893 73 fff00293 313 1900413 841413 9700493 940533 2200893 73 5484b3
  //   494b313 fe0306e3 a00893 73 313 1000e13 8400493 849493 8348493 400913 891913 490913 849493 8248493
  //   849493 8148493 891913 490913 891913 490913 932023 12484b3 430313 fffe0e13 fe0e18e3 2000e13 313 31483
  //   900533 2200893 73 230313 fffe0e13 fe0e14e3 a00893 73 ff100493 900533 2200893 73 148493 fe9068e3
  //   900533 2200893 73 a00893 73 413 140413 800533 2200893 73 240413 800533 2200893 73 340413 800533
  //   2200893 73 440413 800533 2200893 73 540413 800533 2200893 73 640413 800533 2200893 73 740413 800533
  //   2200893 73 840413 800533 2200893 2200893 73 8067
  //   指令探针
  //   RS1_used
  //   指令字
  //   S
  //   J
  //   RS2_used
  //   Beq
  //   Bne
  //   MemToReg
  //   MemWrite
  //   AluOP
  //   AluSrcB
  //   RegWrite
  //   S_type
  //   I
  //   B
  //   控制位
  //   Uret
  //   LBU
  //   JALR
  //   BLTU
  //   JAL
  //   流水调试日志用
  //   暂停节拍，不能为0
  //   ecall
  //   imm_1
  //   imm_2
  //   PredictJump
  //   戳工具置1进入计数暂停模式，ctrl+k时钟自动运行到对应节拍暂停
  //   ctrl+k关闭时钟连续运行，将控制位置零，进入单步调试模式调试
  //   rd
  //   IR
  //   PC
  //   PC+4
  //   可计数暂停的时钟源
  //   BranchTaken
  //   为方便自动评测，需要输出流水线各段保存的PC值，注意是PC不是PC+4，另外ID段寄存器写入信息，Mem段内存写入信息也要输出
  //   EX.MemToReg
  //   EX.RegWrite
  //   LB
  //   JALR
  //   JAL
  //   MemToReg
  //   MemWrite
  //   RegWrite
  //   rd
  //   IR
  //   PC
  //   PC+4
  //   数据存储器
  //   MEM.RegWrite
  //   Mem.rd
  //   JALR
  //   JAL
  //   MemToReg
  //   RegWrite
  //   halt
  //   ALUResult
  //   ReadData
endmodule

module MAX (
  input  [15:0] X,
  input  [15:0] Y,
  input  [2:0] Xid,
  input  [2:0] Yid,
  output [15:0] MAX,
  output [2:0] MAXID
);

  wire comparator_1_eq, comparator_1_lt, or_1_out;

  Comparator #(.width(16), .mode("unsigned")) comparator_1 (
    .a(X), .b(Y), .eq(comparator_1_eq), .lt(comparator_1_lt));  // open: gt
  or or_1 (or_1_out, comparator_1_eq, comparator_1_lt);
  Multiplexer #(.select(1), .width(16), .disabled("Z"), .enable("false")) multiplexer_1 (
    .in0(X), .in1(Y), .out(MAX), .sel(or_1_out));
  Multiplexer #(.select(1), .width(3), .disabled("Z"), .enable("false")) multiplexer_2 (
    .in0(Xid), .in1(Yid), .out(MAXID), .sel(or_1_out));
endmodule

module FSM (
  input  High,
  input  Low,
  input  Jump,
  output NextHigh,
  output NextLow
);

  wire and_1_out, and_2_out, and_3_out, and_4_out, not_1_out, not_2_out, not_3_out, not_4_out, not_5_out;

  not not_1 (not_1_out, Low);
  not not_2 (not_2_out, High);
  not not_3 (not_3_out, Low);
  not not_4 (not_4_out, Low);
  not not_5 (not_5_out, Jump);
  and and_1 (and_1_out, Low, Jump);
  and and_2 (and_2_out, High, not_1_out);
  and and_3 (and_3_out, not_2_out, not_3_out, Jump);
  and and_4 (and_4_out, High, not_4_out, not_5_out);
  or or_1 (NextHigh, and_1_out, and_2_out);
  or or_2 (NextLow, and_3_out, and_4_out);
endmodule
module \重定向流水终端旧  (
  output RegWrite,
  output MemWrite,
  output [31:0] IF_PC,
  output [31:0] ID_PC,
  output [31:0] EX_PC,
  output [31:0] M_PC,
  output [31:0] WB_PC,
  output [31:0] RDin,
  output [31:0] MDin,
  output [31:0] LedData
);

  wire and_1_out, and_2_out, and_3_out, and_4_out, and_5_out, and_7_out, and_8_out, and_9_out, and_11_out,
       and_12_out, and_13_out, and_14_out, and_15_out, and_16_out, and_17_out, BranchSuc, BranchTaken, CLK,
       clock_1_out, clock_2_out, comparator_2_eq, comparator_3_eq, comparator_4_eq, comparator_5_eq,
       comparator_6_eq, comparator_6_lt, comparator_7_eq, d_ff_1_q, d_ff_2_q, d_ff_3_q, d_ff_4_q, ecall, Equ,
       EX_ecall, EX_halt, ex_mem_1_halt_2, ex_mem_1_jal_2, ex_mem_1_jalr_2, ex_mem_1_memtoreg_2,
       ex_mem_1_regwrite_2, EX_URET, Flush, Go, halt, id_ex_1_alusrc_2, id_ex_1_beq_2, id_ex_1_bltu_2,
       id_ex_1_bne_2, id_ex_1_jal_2, id_ex_1_lb_2, id_ex_1_memtoreg_2, id_ex_1_memwrite_2,
       id_ex_1_regwrite_2, IE, if_id_1_id_predictjump, IF_URET, INT, Interrupt, IR1, IR1_q, IR1_Reset, IR2,
       IR2_q, IR2_Reset, IR3, IR3_q, IR3_Reset, IRA, IRB, IRC, JAL, LBU, Less, mem_wb_1_halt_2,
       mem_wb_1_jal_2, mem_wb_1_jalr_2, nand_1_out, not_1_out, not_2_out, or_1_out, or_5_out, or_6_out,
       or_7_out, or_8_out, or_9_out, or_10_out, or_11_out, or_12_out, or_17_out, or_18_out, or_19_out, RST,
       S_type, stall, W1, W2, W3, \单周期硬布线控制器_1_alu_src , \单周期硬布线控制器_1_beq , \单周期硬布线控制器_1_bltu ,
       \单周期硬布线控制器_1_bne , \单周期硬布线控制器_1_jalr , \单周期硬布线控制器_1_lb , \单周期硬布线控制器_1_memtoreg ,
       \单周期硬布线控制器_1_memwrite , \单周期硬布线控制器_1_regwrite , \单周期硬布线控制器_1_rs1_used , \单周期硬布线控制器_1_rs2_used ,
       \单周期硬布线控制器_1_uret , \无条件跳转 ;
  wire [1:0] id_ex_1_jalr_2, id_ex_1_rs1_forward_2, id_ex_1_rs2_forward_2, IR_id, mem_wb_1_memtoreg_2,
       register_1_q, \重定向处理逻辑_1_rs1_forward , \重定向处理逻辑_1_rs2_forward ;
  wire [2:0] register_2_q;
  wire [3:0] id_ex_1_aluop_2, \单周期硬布线控制器_1_alu_op ;
  wire [4:0] ex_mem_1_rd_2, id_ex_1_rd_2, multiplexer_2_out, multiplexer_3_out, WB_rd;
  wire [7:0] multiplexer_13_out;
  wire [12:0] CNT_num;
  wire [15:0] \LoadUse次数 , \总周期数 , \插入气泡数 , \无条件分支数 , \条件分支成功数 ;
  wire [31:0] ALU_addr, bit_extender_1_out, bit_extender_2_out, bit_extender_3_out, bit_extender_4_out,
       bit_extender_5_out, EPC, EX_IR, ex_mem_1_pc_4_2, id_ex_1_imm_1_2, id_ex_1_imm_2_2, id_ex_1_pc_4_2,
       id_ex_1_r1_2, id_ex_1_r2_2, ID_IR, if_id_1_pc_4_2, IF_IR, jumpAddr, MEM_ALURes, MEM_IR,
       mem_wb_1_aluresult_2, mem_wb_1_pc_4_2, mem_wb_1_readdata_2, MemData, multiplexer_4_out,
       multiplexer_5_out, multiplexer_6_out, multiplexer_7_out, multiplexer_8_out, multiplexer_9_out,
       multiplexer_11_out, multiplexer_12_out, multiplexer_14_out, PC_4, PC_Next, PC_Ori, regifile_1_r1,
       regifile_1_r2, shifter_1_out, WB_IR;

  Button \u_总复位  (.out(RST));
  Button _1 (.out(IR1));
  Button _2 (.out(IR2));
  Button _3 (.out(IR3));
  // Probe on \总周期数 
  // Probe on \总周期数 
  \重定向处理逻辑  \u_重定向处理逻辑_1  (
    .RS1_used(\单周期硬布线控制器_1_rs1_used ), .EX_RegWrite(id_ex_1_regwrite_2), .EX_MemToReg(id_ex_1_memtoreg_2),
    .IR(ID_IR), .RS2_used(\单周期硬布线控制器_1_rs2_used ), .MEM_RegWrite(ex_mem_1_regwrite_2), .EX_rd(id_ex_1_rd_2),
    .Ecall(ecall), .BranchTaken(BranchTaken), .MEM_rd(ex_mem_1_rd_2), .Stall(stall), .Flush(Flush),
    .RS1_Forward(\重定向处理逻辑_1_rs1_forward ), .RS2_Forward(\重定向处理逻辑_1_rs2_forward ));
  and and_1 (and_1_out, ~halt, ~stall);  // AND_Gate
  or or_1 (or_1_out, and_1_out, Go);
  Button \u_继续运行  (.out(Go));
  LED #(.active("true")) led_1 (.in(W1));
  LED #(.active("true")) led_2 (.in(W2));
  LED #(.active("true")) led_3 (.in(W3));
  Hex_Digit_Display hex_digit_display_1 (.value(LedData[31:28]));  // open: dp
  // Probe on IF_PC[19:0]
  // RiscV_Probe riscv_probe_1: pin names not known; wires that end beside it: IF_IR
  Multiplexer #(.select(2), .width(32), .disabled("Z"), .enable("false")) multiplexer_1 (
    .in0(PC_4), .in1(ALU_addr), .in2(jumpAddr), .out(PC_Ori), .sel(id_ex_1_jalr_2));  // open: in3
  Comparator #(.width(32), .mode("twosComplement")) comparator_1 (
    .a(IF_IR), .b(32'h200073), .eq(IF_URET));  // open: gt, lt
  Hex_Digit_Display hex_digit_display_2 (.value(LedData[27:24]));  // open: dp
  Hex_Digit_Display hex_digit_display_3 (.value(LedData[23:20]));  // open: dp
  // Probe on ID_PC[19:0]
  // RiscV_Probe riscv_probe_2: pin names not known; wires that end beside it: ID_IR
  Register #(.width(32), .trigger("rising"), .Select("low")) PC (
    .D(PC_Next), .en(or_1_out), .Q(IF_PC), .clk(CLK), .clr(RST));
  LED #(.active("true")) \_1号中断等待指示灯  (.in(W1));
  LED #(.active("true")) \_2号中断等待指示灯  (.in(W2));
  LED #(.active("true")) \_3号中断等待指示灯  (.in(W3));
  Hex_Digit_Display hex_digit_display_4 (.value(LedData[15:12]));  // open: dp
  Hex_Digit_Display hex_digit_display_5 (.value(LedData[19:16]));  // open: dp
  Adder #(.width(32)) adder_1 (.a(IF_PC), .b(32'h4), .out(PC_4));  // open: cin, cout
  // RiscV_Probe riscv_probe_3: pin names not known; wires that end beside it: IF_IR
  D_Flip_Flop #(.trigger("rising"), .Pre_Clr_Positions("LEGACY"), .NegatePresetClear("false"), .enable("true"), .NewFFLayout("false")) d_ff_1 (
    .clk(IR1), .D(1'b1), .Q(d_ff_1_q), .reset(IR1_q));  // open: Qn, preset, en
  or or_2 (W1, IR1_q, d_ff_1_q);
  D_Flip_Flop #(.trigger("rising"), .Pre_Clr_Positions("LEGACY"), .NegatePresetClear("false"), .enable("true"), .NewFFLayout("false")) d_ff_2 (
    .clk(IR2), .D(1'b1), .Q(d_ff_2_q), .reset(IR2_q));  // open: Qn, preset, en
  or or_3 (W2, IR2_q, d_ff_2_q);
  D_Flip_Flop #(.trigger("rising"), .Pre_Clr_Positions("LEGACY"), .NegatePresetClear("false"), .enable("true"), .NewFFLayout("false")) d_ff_3 (
    .clk(IR3), .D(1'b1), .Q(d_ff_3_q), .reset(IR3_q));  // open: Qn, preset, en
  or or_4 (W3, IR3_q, d_ff_3_q);
  Comparator #(.width(16), .mode("twosComplement")) comparator_2 (
    .a(16'h23b), .b(\总周期数 ), .eq(comparator_2_eq));  // open: gt, lt
  Comparator #(.width(16), .mode("twosComplement")) comparator_3 (
    .a(\总周期数 ), .b(16'h1), .eq(comparator_3_eq));  // open: gt, lt
  Comparator #(.width(16), .mode("twosComplement")) comparator_4 (
    .a(\总周期数 ), .b(16'h4), .eq(comparator_4_eq));  // open: gt, lt
  Comparator #(.width(16), .mode("twosComplement")) comparator_5 (
    .a(\总周期数 ), .b(16'h7), .eq(comparator_5_eq));  // open: gt, lt
  Hex_Digit_Display hex_digit_display_6 (.value(LedData[7:4]));  // open: dp
  Hex_Digit_Display hex_digit_display_7 (.value(LedData[11:8]));  // open: dp
  Clock #(.highDuration(1), .lowDuration(1)) clock_1 (.out(clock_1_out));
  // Probe on EX_PC[19:0]
  // RiscV_Probe riscv_probe_4: pin names not known; wires that end beside it: clock_1_out, EX_IR, CLK
  ROM #(.addrWidth(10), .dataWidth(32), .Select("high")) rom_1 (.addr(IF_PC[11:2]), .data(IF_IR));
  and and_2 (and_2_out, ~stall, or_5_out);  // AND_Gate
  or or_5 (or_5_out, ~halt, Go);  // OR_Gate
  or or_6 (or_6_out, d_ff_1_q, IR1_q);
  or or_7 (or_7_out, d_ff_2_q, IR2_q);
  or or_8 (or_8_out, d_ff_3_q, IR3_q);
  or or_9 (or_9_out, comparator_2_eq, comparator_3_eq);
  Pull_Resistor #(.pull(0)) pull_resistor_1 (.node(IRA));
  assign IRA = or_9_out ? ~CLK : 1'bz;  // Controlled_Inverter controlled_inverter_1
  Pull_Resistor #(.pull(0)) pull_resistor_2 (.node(IRB));
  assign IRB = comparator_4_eq ? ~CLK : 1'bz;  // Controlled_Inverter controlled_inverter_2
  Pull_Resistor #(.pull(0)) pull_resistor_3 (.node(IRC));
  assign IRC = comparator_5_eq ? ~CLK : 1'bz;  // Controlled_Inverter controlled_inverter_3
  Hex_Digit_Display hex_digit_display_8 (.value(LedData[3:0]));  // open: dp
  or or_10 (or_10_out, id_ex_1_jalr_2[1], id_ex_1_jalr_2[0]);
  IF_ID if_id_1 (
    .IR(IF_IR), .PC(IF_PC), .PC_4(PC_4), .IR_2(ID_IR), .PC_2(ID_PC), .PC_4_2(if_id_1_pc_4_2),
    .branch(or_10_out), .reset(RST), .en(and_2_out), .clk(CLK), .ID_PredictJump(if_id_1_id_predictjump),
    .IF_PredictJump(IF_URET));
  and and_3 (and_3_out, or_6_out, ~IR1_Reset);  // AND_Gate
  and and_4 (and_4_out, or_7_out, ~IR2_Reset);  // AND_Gate
  and and_5 (and_5_out, or_8_out, ~IR3_Reset);  // AND_Gate
  // Probe on \总周期数 
  // Probe on M_PC[19:0]
  // RiscV_Probe riscv_probe_5: pin names not known; wires that end beside it: MEM_IR
  \单周期硬布线控制器  \u_单周期硬布线控制器_1  (
    .Funct({ID_IR[30], ID_IR[25], ID_IR[14:12]}), .OP(ID_IR[6:2]), .ALU_OP(\单周期硬布线控制器_1_alu_op ),
    .MemToReg(\单周期硬布线控制器_1_memtoreg ), .MemWrite(\单周期硬布线控制器_1_memwrite ), .ALU_SRC(\单周期硬布线控制器_1_alu_src ),
    .RegWrite(\单周期硬布线控制器_1_regwrite ), .ecall(ecall), .S_type(S_type), .JALR(\单周期硬布线控制器_1_jalr ),
    .BEQ(\单周期硬布线控制器_1_beq ), .JAL(JAL), .BNE(\单周期硬布线控制器_1_bne ), .in_3(ID_IR[21]), .uret(\单周期硬布线控制器_1_uret ),
    .BLTU(\单周期硬布线控制器_1_bltu ), .LB(\单周期硬布线控制器_1_lb ), .rs1_used(\单周期硬布线控制器_1_rs1_used ),
    .rs2_used(\单周期硬布线控制器_1_rs2_used ));  // open: U_Type, CSR, SLTIU
  Multiplexer #(.select(1), .width(5), .disabled("Z"), .enable("false")) multiplexer_2 (
    .in0(ID_IR[19:15]), .in1(5'b10001), .out(multiplexer_2_out), .sel(ecall));
  Multiplexer #(.select(1), .width(5), .disabled("Z"), .enable("false")) multiplexer_3 (
    .in0(ID_IR[24:20]), .in1(5'b01010), .out(multiplexer_3_out), .sel(ecall));
  D_Flip_Flop #(.trigger("rising"), .Pre_Clr_Positions("LEGACY"), .NegatePresetClear("false"), .enable("true"), .NewFFLayout("false")) u_IR1 (
    .clk(CLK), .D(and_3_out), .Q(IR1_q), .reset(RST));  // open: Qn, preset, en
  D_Flip_Flop #(.trigger("rising"), .Pre_Clr_Positions("LEGACY"), .NegatePresetClear("false"), .enable("true"), .NewFFLayout("false")) u_IR2 (
    .clk(CLK), .D(and_4_out), .Q(IR2_q), .reset(RST));  // open: Qn, preset, en
  D_Flip_Flop #(.trigger("rising"), .Pre_Clr_Positions("LEGACY"), .NegatePresetClear("false"), .enable("true"), .NewFFLayout("false")) u_IR3 (
    .clk(CLK), .D(and_5_out), .Q(IR3_q), .reset(RST));  // open: Qn, preset, en
  // Probe on \总周期数 
  // Probe on \无条件分支数 
  // Probe on \条件分支成功数 
  // Probe on \插入气泡数 
  // Probe on \LoadUse次数 
  // Probe on multiplexer_2_out
  // Probe on multiplexer_3_out
  assign bit_extender_1_out = {{20{ID_IR[31]}}, ID_IR[31:20]};  // Bit_Extender bit_extender_1
  assign bit_extender_2_out = {{20{ID_IR[31]}}, {ID_IR[31:25], ID_IR[11:7]}};  // Bit_Extender bit_extender_2
  assign bit_extender_3_out = {{20{ID_IR[31]}}, {ID_IR[31], ID_IR[7], ID_IR[30:25], ID_IR[11:8]}};  // Bit_Extender bit_extender_3
  assign bit_extender_4_out = {{12{ID_IR[31]}}, {ID_IR[31], ID_IR[19:12], ID_IR[20], ID_IR[30:21]}};  // Bit_Extender bit_extender_4
  // Probe on IF_PC[11:0]
  // Probe on WB_PC[19:0]
  // RiscV_Probe riscv_probe_6: pin names not known; wires that end beside it: WB_IR
  not not_1 (not_1_out, CLK);
  Multiplexer #(.select(1), .width(32), .disabled("Z"), .enable("false")) multiplexer_4 (
    .in0(bit_extender_1_out), .in1(bit_extender_2_out), .out(multiplexer_4_out), .sel(S_type));
  Multiplexer #(.select(1), .width(32), .disabled("Z"), .enable("false")) multiplexer_5 (
    .in0(bit_extender_3_out), .in1(bit_extender_4_out), .out(multiplexer_5_out), .sel(JAL));
  Priority_Encoder #(.select(2), .disabled("Z")) priority_encoder_1 (
    .in1(IR1_q), .in2(IR2_q), .in3(IR3_q), .out(IR_id), .gs(INT));  // open: in0, en_out, en_in
  // Probe on ID_PC[11:0]
  // Probe on EX_PC[11:0]
  Regifile regifile_1 (
    .Din(RDin), .Clk(not_1_out), .R1(regifile_1_r1), .R2(regifile_1_r2), .WE(RegWrite), .W_num(WB_rd),
    .R1_num(multiplexer_2_out), .R2_num(multiplexer_3_out));
  or or_11 (or_11_out, ~halt, Go);  // OR_Gate
  Multiplexer #(.select(2), .width(32), .disabled("Z"), .enable("false")) multiplexer_6 (
    .in1(32'h30ac), .in2(32'h3150), .in3(32'h31f4), .out(multiplexer_6_out), .sel(IR_id));  // open: in0
  and and_6 (Interrupt, INT, IE);
  Register #(.width(2), .trigger("rising"), .Select("low")) register_1 (
    .D(IR_id), .en(Interrupt), .Q(register_1_q), .clk(CLK), .clr(RST));
  Demultiplexer #(.select(2), .width(1), .tristate("false"), .disabled("Z"), .enable("false")) demultiplexer_1 (
    .out1(IR1_Reset), .out2(IR2_Reset), .out3(IR3_Reset), .in(IF_URET), .sel(register_1_q));  // open: out0
  // Probe on M_PC[11:0]
  D_Flip_Flop #(.trigger("high"), .Pre_Clr_Positions("LEGACY"), .NegatePresetClear("false"), .enable("true"), .NewFFLayout("false")) d_ff_4 (.Q(d_ff_4_q));  // open: clk, D, Qn, preset, en, reset
  // Probe on 13'hc
  ID_EX id_ex_1 (
    .BEQ(\单周期硬布线控制器_1_beq ), .BNE(\单周期硬布线控制器_1_bne ), .MemToReg(\单周期硬布线控制器_1_memtoreg ),
    .MemWrite(\单周期硬布线控制器_1_memwrite ), .AluSrc(\单周期硬布线控制器_1_alu_src ), .RegWrite(\单周期硬布线控制器_1_regwrite ),
    .S_type(S_type), .ecall(ecall), .Jal(JAL), .Jalr(\单周期硬布线控制器_1_jalr ), .LB(\单周期硬布线控制器_1_lb ),
    .BLTU(\单周期硬布线控制器_1_bltu ), .Uret(\单周期硬布线控制器_1_uret ), .AluOP(\单周期硬布线控制器_1_alu_op ), .rd(ID_IR[11:7]),
    .R1(regifile_1_r1), .R2(regifile_1_r2), .imm_1(multiplexer_4_out), .imm_2(multiplexer_5_out), .PC(ID_PC),
    .PC_4(if_id_1_pc_4_2), .IR(ID_IR), .RS1_Forward(\重定向处理逻辑_1_rs1_forward ),
    .RS2_Forward(\重定向处理逻辑_1_rs2_forward ), .BEQ_2(id_ex_1_beq_2), .BNE_2(id_ex_1_bne_2),
    .MemToReg_2(id_ex_1_memtoreg_2), .MemWrite_2(id_ex_1_memwrite_2), .AluSrc_2(id_ex_1_alusrc_2),
    .RegWrite_2(id_ex_1_regwrite_2), .ecall_2(EX_ecall), .Jal_2(id_ex_1_jal_2), .Jalr_2(id_ex_1_jalr_2[0]),
    .LB_2(id_ex_1_lb_2), .BLTU_2(id_ex_1_bltu_2), .AluOP_2(id_ex_1_aluop_2), .rd_2(id_ex_1_rd_2),
    .R1_2(id_ex_1_r1_2), .R2_2(id_ex_1_r2_2), .imm_1_2(id_ex_1_imm_1_2), .imm_2_2(id_ex_1_imm_2_2),
    .PC_2(EX_PC), .PC_4_2(id_ex_1_pc_4_2), .IR_2(EX_IR), .RS1_Forward_2(id_ex_1_rs1_forward_2),
    .RS2_Forward_2(id_ex_1_rs2_forward_2), .reset(or_12_out), .flush(Flush), .en(or_11_out), .clk(CLK),
    .ID_PredictJump(if_id_1_id_predictjump), .EX_PredictJump(EX_URET));  // open: S_type_2, Uret_2, U_Type, U_Type_2, AUIPC_result, AUIPC_result_2, SLTIU, SLTIU_2
  or or_12 (or_12_out, RST, Interrupt);
  // Probe on WB_PC[11:0]
  Comparator #(.width(13), .mode("twosComplement")) comparator_6 (
    .a(CNT_num), .b(13'hc), .eq(comparator_6_eq), .lt(comparator_6_lt));  // open: gt
  Clock #(.highDuration(1), .lowDuration(1)) clock_2 (.out(clock_2_out));
  Multiplexer #(.select(2), .width(32), .disabled("Z"), .enable("false")) multiplexer_7 (
    .in0(id_ex_1_r1_2), .in1(RDin), .in2(MEM_ALURes), .out(multiplexer_7_out), .sel(id_ex_1_rs1_forward_2));  // open: in3
  Multiplexer #(.select(1), .width(32), .disabled("Z"), .enable("false")) multiplexer_8 (
    .in0(PC_Ori), .in1(multiplexer_6_out), .out(multiplexer_8_out), .sel(Interrupt));
  nand nand_1 (nand_1_out, d_ff_4_q, comparator_6_eq);
  Counter #(.width(13), .max('h1fff), .ongoal("stay"), .trigger("rising"), .behavior("old")) counter_1 (
    .count(comparator_6_lt), .Q(CNT_num), .clk(clock_2_out));  // open: load, D, carry, clr, preset
  Multiplexer #(.select(2), .width(32), .disabled("Z"), .enable("false")) multiplexer_9 (
    .in0(id_ex_1_r2_2), .in1(RDin), .in2(MEM_ALURes), .out(multiplexer_9_out), .sel(id_ex_1_rs2_forward_2));  // open: in3
  Multiplexer #(.select(1), .width(32), .disabled("Z"), .enable("false")) multiplexer_10 (
    .in0(multiplexer_8_out), .in1(EPC), .out(PC_Next), .sel(IF_URET));
  assign CLK = nand_1_out ? clock_2_out : 1'bz;  // Controlled_Buffer controlled_buffer_1
  or or_13 (id_ex_1_jalr_2[1], id_ex_1_jal_2, BranchSuc);
  and and_7 (and_7_out, id_ex_1_bne_2, ~Equ);  // AND_Gate
  Register #(.width(1), .trigger("rising"), .Select("low")) register_2 (
    .D(BranchTaken), .Q(register_2_q[0]), .clk(CLK), .clr(RST));  // open: en
  Pull_Resistor #(.pull(1)) pull_resistor_4 (.node(CLK));
  or or_14 (BranchSuc, and_7_out, and_8_out, and_9_out);
  and and_8 (and_8_out, Equ, id_ex_1_beq_2);
  and and_9 (and_9_out, id_ex_1_bltu_2, Less);
  Multiplexer #(.select(1), .width(32), .disabled("Z"), .enable("false")) multiplexer_11 (
    .in0(multiplexer_9_out), .in1(id_ex_1_imm_1_2), .out(multiplexer_11_out), .sel(id_ex_1_alusrc_2));
  Shifter #(.width(32), .shift("ll")) shifter_1 (.in(id_ex_1_imm_2_2), .\dist (5'b00001), .out(shifter_1_out));
  Comparator #(.width(32), .mode("twosComplement")) comparator_7 (
    .a(multiplexer_7_out), .b(32'ha), .eq(comparator_7_eq));  // open: gt, lt
  not not_2 (not_2_out, comparator_7_eq);
  Register #(.width(1), .trigger("rising"), .Select("low")) register_3 (
    .D(stall), .Q(register_2_q[2]), .clk(CLK), .clr(RST));  // open: en
  or or_15 (BranchTaken, id_ex_1_jalr_2[1], id_ex_1_jalr_2[0]);
  or or_16 (\无条件跳转 , id_ex_1_jalr_2[0], id_ex_1_jal_2);
  ALU alu_1 (
    .X(multiplexer_7_out), .Y(multiplexer_11_out), .AluOP(id_ex_1_aluop_2), .Equal(Equ), .Result(ALU_addr),
    .out_6(Less));  // open: Result_2, out_4
  and and_10 (EX_halt, comparator_7_eq, EX_ecall);
  and and_11 (and_11_out, not_2_out, EX_ecall);
  Register #(.width(1), .trigger("rising"), .Select("low")) register_4 (
    .D(register_2_q[0]), .Q(register_2_q[1]), .clk(CLK), .clr(RST));  // open: en
  Adder #(.width(32)) adder_2 (.a(shifter_1_out), .b(EX_PC), .out(jumpAddr));  // open: cin, cout
  Register #(.width(32), .trigger("rising"), .Select("low")) register_5 (
    .D(multiplexer_9_out), .en(and_11_out), .Q(LedData), .clk(CLK), .clr(RST));
  and and_12 (and_12_out, INT, ~EX_URET);  // AND_Gate
  EX_MEM ex_mem_1 (
    .Jal(id_ex_1_jal_2), .Jalr(id_ex_1_jalr_2[0]), .MemToReg(id_ex_1_memtoreg_2),
    .MemWrite(id_ex_1_memwrite_2), .LB(id_ex_1_lb_2), .RegWrite(id_ex_1_regwrite_2), .halt(EX_halt),
    .rd(id_ex_1_rd_2), .Result(ALU_addr), .WriteData(multiplexer_9_out), .IR(EX_IR), .PC(EX_PC),
    .PC_4(id_ex_1_pc_4_2), .Jal_2(ex_mem_1_jal_2), .Jalr_2(ex_mem_1_jalr_2),
    .MemToReg_2(ex_mem_1_memtoreg_2), .MemWrite_2(MemWrite), .LB_2(LBU), .RegWrite_2(ex_mem_1_regwrite_2),
    .halt_2(ex_mem_1_halt_2), .rd_2(ex_mem_1_rd_2), .Result_2(MEM_ALURes), .WriteData_2(MDin), .IR_2(MEM_IR),
    .PC_2(M_PC), .PC_4_2(ex_mem_1_pc_4_2), .reset(or_18_out), .en(or_17_out), .clk(CLK));  // open: U_Type, U_Type_2, AUIPC_result, AUIPC_result_2, SLTIU, SLTIU_2, LESS, LESS_2
  or or_17 (or_17_out, ~halt, Go);  // OR_Gate
  D_Flip_Flop #(.trigger("rising"), .Pre_Clr_Positions("LEGACY"), .NegatePresetClear("false"), .enable("true"), .NewFFLayout("false")) d_ff_5 (
    .clk(CLK), .D(and_12_out), .Qn(IE));  // open: Q, preset, en, reset
  Multiplexer #(.select(3), .width(32), .disabled("Z"), .enable("false")) multiplexer_12 (
    .in0(EX_PC), .in1(IF_PC), .in2(ID_PC), .in4(ID_PC), .out(multiplexer_12_out), .sel(register_2_q));  // open: in3, in5, in6, in7
  or or_18 (or_18_out, RST, Interrupt);
  Register #(.width(32), .trigger("rising"), .Select("low")) u_EPC (
    .D(multiplexer_12_out), .en(Interrupt), .Q(EPC), .clk(CLK), .clr(RST));
  RAM #(.addrWidth(10), .dataWidth(32), .bus("separate"), .Select("high")) ram_1 (
    .addr(MEM_ALURes[11:2]), .din(MDin), .data(MemData), .str(MemWrite), .sel(1'b1), .clk(CLK), .ld(1'b1),
    .clr(RST));
  Multiplexer #(.select(2), .width(8), .disabled("Z"), .enable("false")) multiplexer_13 (
    .in0(MemData[7:0]), .in1(MemData[15:8]), .in2(MemData[23:16]), .in3(MemData[31:24]),
    .out(multiplexer_13_out), .sel(MEM_ALURes[1:0]));
  Multiplexer #(.select(1), .width(32), .disabled("Z"), .enable("false")) multiplexer_14 (
    .in0(MemData), .in1(bit_extender_5_out), .out(multiplexer_14_out), .sel(LBU));
  assign bit_extender_5_out = {{24{1'b0}}, multiplexer_13_out};  // Bit_Extender bit_extender_5
  MEM_WB mem_wb_1 (
    .Jal(ex_mem_1_jal_2), .Jalr(ex_mem_1_jalr_2), .MemToReg(ex_mem_1_memtoreg_2),
    .RegWrite(ex_mem_1_regwrite_2), .halt(ex_mem_1_halt_2), .rd(ex_mem_1_rd_2), .ALUResult(MEM_ALURes),
    .ReadData(multiplexer_14_out), .IR(MEM_IR), .PC(M_PC), .PC_4(ex_mem_1_pc_4_2), .Jal_2(mem_wb_1_jal_2),
    .Jalr_2(mem_wb_1_jalr_2), .MemToReg_2(mem_wb_1_memtoreg_2[0]), .RegWrite_2(RegWrite),
    .halt_2(mem_wb_1_halt_2), .rd_2(WB_rd), .ALUResult_2(mem_wb_1_aluresult_2),
    .ReadData_2(mem_wb_1_readdata_2), .IR_2(WB_IR), .PC_2(WB_PC), .PC_4_2(mem_wb_1_pc_4_2), .reset(RST),
    .en(or_19_out), .clk(CLK));  // open: U_Type, U_Type_2, AUIPC_result, AUIPC_result_2, SLTIU, SLTIU_2, LESS, LESS_2
  or or_19 (or_19_out, ~halt, Go);  // OR_Gate
  D_Flip_Flop #(.trigger("rising"), .Pre_Clr_Positions("ABOVE_BELOW"), .NegatePresetClear("false"), .enable("true"), .NewFFLayout("true")) d_ff_6 (
    .clk(mem_wb_1_halt_2), .D(1'b1), .Q(halt), .en(1'b1), .reset(Go));  // open: Qn, preset
  or or_20 (mem_wb_1_memtoreg_2[1], mem_wb_1_jalr_2, mem_wb_1_jal_2);
  Multiplexer #(.select(2), .width(32), .disabled("Z"), .enable("false")) multiplexer_15 (
    .in0(mem_wb_1_aluresult_2), .in1(mem_wb_1_readdata_2), .in2(mem_wb_1_pc_4_2), .out(RDin),
    .sel(mem_wb_1_memtoreg_2));  // open: in3
  Counter #(.width(16), .max('hffff), .ongoal("wrap"), .trigger("rising"), .behavior("new")) counter_2 (
    .count(BranchSuc), .Q(\条件分支成功数 ), .clk(and_13_out), .clr(RST));  // open: load, D, carry, preset, down
  and and_13 (and_13_out, ~halt, CLK);  // AND_Gate
  Counter #(.width(16), .max('hffff), .ongoal("wrap"), .trigger("rising"), .behavior("new")) counter_3 (
    .count(Flush), .Q(\插入气泡数 ), .clk(and_14_out), .clr(RST));  // open: load, D, carry, preset, down
  and and_14 (and_14_out, ~halt, CLK);  // AND_Gate
  Counter #(.width(16), .max('hffff), .ongoal("wrap"), .trigger("rising"), .behavior("new")) counter_4 (
    .count(\无条件跳转 ), .Q(\无条件分支数 ), .clk(and_15_out), .clr(RST));  // open: load, D, carry, preset, down
  and and_15 (and_15_out, ~halt, CLK);  // AND_Gate
  Counter #(.width(16), .max('hffff), .ongoal("wrap"), .trigger("rising"), .behavior("new")) counter_5 (
    .count(CLK), .Q(\总周期数 ), .clk(and_16_out), .clr(RST));  // open: load, D, carry, preset, down
  and and_16 (and_16_out, ~halt, CLK);  // AND_Gate
  Counter #(.width(16), .max('hffff), .ongoal("wrap"), .trigger("rising"), .behavior("new")) counter_6 (
    .count(stall), .Q(\LoadUse次数 ), .clk(and_17_out), .clr(RST));  // open: load, D, carry, preset, down
  and and_17 (and_17_out, ~halt, CLK);  // AND_Gate

  // Other names for the same wires on the sheet: IR[31:0] = ID_IR; MEM_PC[31:0] = M_PC; WB_RegWrite = RegWrite

  // Notes on the sheet:
  //   中断源
  //   时空图监测，可删除
  //   中断等待指示
  //   单级中断测试信号模拟器
  //   数码管输出
  //   指令存储器
  //   指令探针
  //   contents of rom_1 (hex, n*v repeats v):
  //   7d000113 100413 1f41993 41f9d993 433 c00913 800b13 140413 f47413 800293 100313 499993 89e9b3 1300533
  //   2200893 73 406282b3 fe0294e3 140413 f00f93 1f47433 1c41413 800293 100313 49d993 89e9b3 1300533
  //   2200893 73 406282b3 fe0294e3 1c45413 406b0b33 b0463 f95ff06f 2b3 fff2c293 1029293 fff2e293 500533
  //   2200893 73 f5dff06f 1112023 410113 a12023 410113 812023 410113 1312023 410113 1412023 410113 1512023
  //   410113 1612023 410113 100b13 300a13 100a93 1600433 441413 14469b3 1300533 2200893 73 fe0416e3
  //   415a0a33 fe0a10e3 ffc10113 12b03 ffc10113 12a83 ffc10113 12a03 ffc10113 12983 ffc10113 12403
  //   ffc10113 12503 ffc10113 12883 200073 1112023 410113 a12023 410113 812023 410113 1312023 410113
  //   1412023 410113 1512023 410113 1612023 410113 200b13 300a13 100a93 1600433 441413 14469b3 1300533
  //   2200893 73 fe0416e3 415a0a33 fe0a10e3 ffc10113 12b03 ffc10113 12a83 ffc10113 12a03 ffc10113 12983
  //   ffc10113 12403 ffc10113 12503 ffc10113 12883 200073 1112023 410113 a12023 410113 812023 410113
  //   1312023 410113 1412023 410113 1512023 410113 1612023 410113 300b13 300a13 100a93 1600433 441413
  //   14469b3 1300533 2200893 73 fe0416e3 415a0a33 fe0a10e3 ffc10113 12b03 ffc10113 12a83 ffc10113 12a03
  //   ffc10113 12983 ffc10113 12403 ffc10113 12503 ffc10113 12883 200073
  //   指令字
  //   J
  //   RS1_used
  //   I
  //   S
  //   B
  //   Reset 
  //   Reset 
  //   Reset 
  //   RS2_used
  //   JALR
  //   Beq
  //   Bne
  //   MemToReg
  //   MemWrite
  //   AluOP
  //   AluSrcB
  //   RegWrite
  //   S_type
  //   Uret
  //   LBU
  //   BLT
  //   JAL
  //   控制位
  //   ecall
  //   imm_1
  //   imm_2
  //   rd
  //   IR
  //   PC
  //   PC+4
  //   流水调试日志用
  //   暂停节拍，不能为0
  //   戳工具置1进入计数暂停模式，ctrl+k时钟自动运行到对应节拍暂停
  //   ctrl+k关闭时钟连续运行，将控制位置零，进入单步调试模式调试
  //   可计数暂停的时钟源
  //   BranchTaken
  //   EX.MemToReg
  //   为方便自动评测，需要输出流水线各段保存的PC值，注意是PC不是PC+4，另外ID段寄存器写入信息，Mem段内存写入信息也要输出
  //   EX.RegWrite
  //   LBU
  //   JALR
  //   JAL
  //   MemToReg
  //   MemWrite
  //   RegWrite
  //   rd
  //   IR
  //   PC
  //   PC+4
  //   数据存储器
  //   MEM.RegWrite
  //   JALR
  //   JAL
  //   MemToReg
  //   RegWrite
  //   halt
  //   ALUResult
  //   ReadData
  //   Mem.rd
endmodule
